// Digital circuit 74HC138.dig as structural Verilog
module _74HC138 (
  input  A0,
  input  A1,
  input  A2,
  input  nE1,
  input  nE2,
  input  E3,
  output nY0,
  output nY1,
  output nY2,
  output nY3,
  output nY4,
  output nY5,
  output nY6,
  output nY7
);

  wire and_1_out, demultiplexer_1_out_0, demultiplexer_1_out_1, demultiplexer_1_out_2, demultiplexer_1_out_3,
       demultiplexer_1_out_4, demultiplexer_1_out_5, demultiplexer_1_out_6, demultiplexer_1_out_7;

  and and_1 (and_1_out, ~nE1, ~nE2, E3);  // And
  Demultiplexer #(.Selector_Bits(3)) demultiplexer_1 (
    .sel({A2, A1, A0}), .in(and_1_out), .out_0(demultiplexer_1_out_0), .out_1(demultiplexer_1_out_1),
    .out_2(demultiplexer_1_out_2), .out_3(demultiplexer_1_out_3), .out_4(demultiplexer_1_out_4),
    .out_5(demultiplexer_1_out_5), .out_6(demultiplexer_1_out_6), .out_7(demultiplexer_1_out_7));
  not not_1 (nY0, demultiplexer_1_out_0);
  not not_2 (nY1, demultiplexer_1_out_1);
  not not_3 (nY2, demultiplexer_1_out_2);
  not not_4 (nY3, demultiplexer_1_out_3);
  not not_5 (nY4, demultiplexer_1_out_4);
  not not_6 (nY5, demultiplexer_1_out_5);
  not not_7 (nY6, demultiplexer_1_out_6);
  not not_8 (nY7, demultiplexer_1_out_7);
endmodule
