// Digital circuit 74HC4017.dig as structural Verilog
module _74HC4017 (
  input  CLK,
  input  nEN,
  input  MR,
  output Q0,
  output Q1,
  output Q2,
  output Q3,
  output Q4,
  output Q5,
  output Q6,
  output Q7,
  output Q8,
  output Q9,
  output nQ59
);

  wire and_2_out, CLK_t, d_ff_as_1_nq, d_ff_as_1_q, d_ff_as_2_nq, d_ff_as_2_q, d_ff_as_3_nq, d_ff_as_3_q,
       d_ff_as_4_nq, d_ff_as_4_q, d_ff_as_5_q, or_1_out;

  and and_1 (CLK_t, CLK, ~nEN);  // And
  nor nor_1 (Q0, d_ff_as_1_q, d_ff_as_5_q);
  nor nor_2 (Q1, d_ff_as_1_nq, d_ff_as_2_q);
  D_FF_AS d_ff_as_1 (.Set(1'b0), .D(nQ59), .C(CLK_t), .Clr(MR), .Q(d_ff_as_1_q), .nQ(d_ff_as_1_nq));
  nor nor_3 (Q2, d_ff_as_3_q, d_ff_as_2_nq);
  or or_1 (or_1_out, d_ff_as_3_q, d_ff_as_1_q);
  D_FF_AS d_ff_as_2 (.Set(1'b0), .D(d_ff_as_1_q), .C(CLK_t), .Clr(MR), .Q(d_ff_as_2_q), .nQ(d_ff_as_2_nq));
  nor nor_4 (Q3, d_ff_as_3_nq, d_ff_as_4_q);
  and and_2 (and_2_out, or_1_out, d_ff_as_2_q);
  nor nor_5 (Q4, d_ff_as_4_nq, d_ff_as_5_q);
  D_FF_AS d_ff_as_3 (.Set(1'b0), .D(and_2_out), .C(CLK_t), .Clr(MR), .Q(d_ff_as_3_q), .nQ(d_ff_as_3_nq));
  nor nor_6 (Q5, nQ59, d_ff_as_1_nq);
  D_FF_AS d_ff_as_4 (.Set(1'b0), .D(d_ff_as_3_q), .C(CLK_t), .Clr(MR), .Q(d_ff_as_4_q), .nQ(d_ff_as_4_nq));
  nor nor_7 (Q6, d_ff_as_2_nq, d_ff_as_1_q);
  D_FF_AS d_ff_as_5 (.Set(1'b0), .D(d_ff_as_4_q), .C(CLK_t), .Clr(MR), .Q(d_ff_as_5_q), .nQ(nQ59));
  nor nor_8 (Q7, d_ff_as_3_nq, d_ff_as_2_q);
  nor nor_9 (Q8, d_ff_as_3_q, d_ff_as_4_nq);
  nor nor_10 (Q9, nQ59, d_ff_as_4_q);

  // Notes on the sheet:
  //   CLK: Hz: 4
endmodule

/* Test case:
CLK ~EN MR  Q0 Q1 Q2 Q3 Q4 Q5 Q6 Q7 Q8 Q9 ~Q59

0   0   1   1  0  0  0  0  0  0  0  0  0  1
0   0   0   1  0  0  0  0  0  0  0  0  0  1
1   0   0   0  1  0  0  0  0  0  0  0  0  1
0   0   0   0  1  0  0  0  0  0  0  0  0  1
1   0   0   0  0  1  0  0  0  0  0  0  0  1
0   0   0   0  0  1  0  0  0  0  0  0  0  1
1   0   0   0  0  0  1  0  0  0  0  0  0  1
0   0   0   0  0  0  1  0  0  0  0  0  0  1
1   0   0   0  0  0  0  1  0  0  0  0  0  1
0   0   0   0  0  0  0  1  0  0  0  0  0  1
1   0   0   0  0  0  0  0  1  0  0  0  0  0
0   0   0   0  0  0  0  0  1  0  0  0  0  0
1   0   0   0  0  0  0  0  0  1  0  0  0  0
0   0   0   0  0  0  0  0  0  1  0  0  0  0
1   0   0   0  0  0  0  0  0  0  1  0  0  0
0   0   0   0  0  0  0  0  0  0  1  0  0  0
1   0   0   0  0  0  0  0  0  0  0  1  0  0
0   0   0   0  0  0  0  0  0  0  0  1  0  0
1   0   0   0  0  0  0  0  0  0  0  0  1  0
0   0   0   0  0  0  0  0  0  0  0  0  1  0
1   0   0   1  0  0  0  0  0  0  0  0  0  1
0   0   0   1  0  0  0  0  0  0  0  0  0  1
1   0   0   0  1  0  0  0  0  0  0  0  0  1
0   0   0   0  1  0  0  0  0  0  0  0  0  1
1   0   0   0  0  1  0  0  0  0  0  0  0  1
0   0   0   0  0  1  0  0  0  0  0  0  0  1
1   1   0   0  0  1  0  0  0  0  0  0  0  1
0   1   0   0  0  1  0  0  0  0  0  0  0  1
1   1   0   0  0  1  0  0  0  0  0  0  0  1
0   1   0   0  0  1  0  0  0  0  0  0  0  1
*/
