// Digital circuit 74HC4024.dig as structural Verilog
module _74HC4024 (
  input  CP,
  input  MR,
  output Q0,
  output Q1,
  output Q2,
  output Q3,
  output Q4,
  output Q5,
  output Q6
);

  wire jk_ff_as_1_nq, jk_ff_as_2_nq, jk_ff_as_3_nq, jk_ff_as_4_nq, jk_ff_as_5_nq, jk_ff_as_6_nq, not_1_out;

  not not_1 (not_1_out, CP);
  JK_FF_AS jk_ff_as_1 (.Set(1'b0), .J(1'b1), .C(not_1_out), .K(1'b1), .Clr(MR), .Q(Q0), .nQ(jk_ff_as_1_nq));
  JK_FF_AS jk_ff_as_2 (.Set(1'b0), .J(1'b1), .C(jk_ff_as_1_nq), .K(1'b1), .Clr(MR), .Q(Q1), .nQ(jk_ff_as_2_nq));
  JK_FF_AS jk_ff_as_3 (.Set(1'b0), .J(1'b1), .C(jk_ff_as_2_nq), .K(1'b1), .Clr(MR), .Q(Q2), .nQ(jk_ff_as_3_nq));
  JK_FF_AS jk_ff_as_4 (.Set(1'b0), .J(1'b1), .C(jk_ff_as_3_nq), .K(1'b1), .Clr(MR), .Q(Q3), .nQ(jk_ff_as_4_nq));
  JK_FF_AS jk_ff_as_5 (.Set(1'b0), .J(1'b1), .C(jk_ff_as_4_nq), .K(1'b1), .Clr(MR), .Q(Q4), .nQ(jk_ff_as_5_nq));
  JK_FF_AS jk_ff_as_6 (.Set(1'b0), .J(1'b1), .C(jk_ff_as_5_nq), .K(1'b1), .Clr(MR), .Q(Q5), .nQ(jk_ff_as_6_nq));
  JK_FF_AS jk_ff_as_7 (.Set(1'b0), .J(1'b1), .C(jk_ff_as_6_nq), .K(1'b1), .Clr(MR), .Q(Q6));  // open: nQ

  // Notes on the sheet:
  //   CP: default 1
endmodule
