// Digital circuit 74HC573.dig as structural Verilog
module _74HC573 (
  input  D0,
  input  D1,
  input  D2,
  input  D3,
  input  D4,
  input  D5,
  input  D6,
  input  D7,
  input  LE,
  input  nOE,
  output Q0,
  output Q1,
  output Q2,
  output Q3,
  output Q4,
  output Q5,
  output Q6,
  output Q7
);

  wire [7:0] nand_1_out, nand_2_out, nand_3_out, nand_4_out;

  assign nand_1_out = ~({D7, D6, D5, D4, D3, D2, D1, D0} & {8{LE}});  // NAnd nand_1, 8 bits wide
  assign nand_2_out = ~({8{LE}} & ~{D7, D6, D5, D4, D3, D2, D1, D0});  // NAnd nand_2, 8 bits wide
  assign nand_3_out = ~(nand_1_out & nand_4_out);  // NAnd nand_3, 8 bits wide
  assign nand_4_out = ~(nand_3_out & nand_2_out);  // NAnd nand_4, 8 bits wide
  assign {Q7, Q6, Q5, Q4, Q3, Q2, Q1, Q0} = ~nOE ? nand_3_out : 8'bz;  // DriverInvSel driverinvsel_1
endmodule
