// Digital circuit 74HC574.dig as structural Verilog
module _74HC574 (
  input  D0,
  input  D1,
  input  D2,
  input  D3,
  input  D4,
  input  D5,
  input  D6,
  input  D7,
  input  CP,
  input  nOE,
  output Q0,
  output Q1,
  output Q2,
  output Q3,
  output Q4,
  output Q5,
  output Q6,
  output Q7
);

  wire [7:0] d_ff_1_q;

  D_FF #(.Bits(8)) d_ff_1 (.D({D7, D6, D5, D4, D3, D2, D1, D0}), .C(CP), .Q(d_ff_1_q));  // open: nQ
  assign {Q7, Q6, Q5, Q4, Q3, Q2, Q1, Q0} = ~nOE ? d_ff_1_q : 8'bz;  // DriverInvSel driverinvsel_1
endmodule
