// Digital circuit 74HC595.dig as structural Verilog
module _74HC595 (
  input  SER,
  input  SRCLK,
  input  nSRCLR,
  input  RCLK,
  input  nOE,
  input  VCC,
  input  GND,
  output QH,
  output QG,
  output QF,
  output QE,
  output QD,
  output QC,
  output QB,
  output QA,
  output QH_2
);

  wire d_ff_as_1_q, d_ff_as_2_q, d_ff_as_3_q, d_ff_as_4_q, d_ff_as_5_q, d_ff_as_6_q, d_ff_as_7_q,
       d_ff_as_8_q, d_ff_as_9_q, d_ff_as_10_q, d_ff_as_11_q, d_ff_as_12_q, d_ff_as_13_q, d_ff_as_14_q,
       d_ff_as_16_q, not_1_out;

  PowerSupply powersupply_1 (.VDD(VCC), .GND(GND));
  not not_1 (not_1_out, nSRCLR);
  D_FF_AS d_ff_as_1 (.Set(1'b0), .D(SER), .C(SRCLK), .Clr(not_1_out), .Q(d_ff_as_1_q));  // open: nQ
  D_FF_AS d_ff_as_2 (.Set(1'b0), .D(d_ff_as_1_q), .C(RCLK), .Clr(1'b0), .Q(d_ff_as_2_q));  // open: nQ
  D_FF_AS d_ff_as_3 (.Set(1'b0), .D(d_ff_as_1_q), .C(SRCLK), .Clr(not_1_out), .Q(d_ff_as_3_q));  // open: nQ
  assign QA = ~nOE ? d_ff_as_2_q : 1'bz;  // DriverInvSel driverinvsel_1
  D_FF_AS d_ff_as_4 (.Set(1'b0), .D(d_ff_as_3_q), .C(SRCLK), .Clr(not_1_out), .Q(d_ff_as_4_q));  // open: nQ
  D_FF_AS d_ff_as_5 (.Set(1'b0), .D(d_ff_as_3_q), .C(RCLK), .Clr(1'b0), .Q(d_ff_as_5_q));  // open: nQ
  assign QB = ~nOE ? d_ff_as_5_q : 1'bz;  // DriverInvSel driverinvsel_2
  D_FF_AS d_ff_as_6 (.Set(1'b0), .D(d_ff_as_4_q), .C(RCLK), .Clr(1'b0), .Q(d_ff_as_6_q));  // open: nQ
  D_FF_AS d_ff_as_7 (.Set(1'b0), .D(d_ff_as_4_q), .C(SRCLK), .Clr(not_1_out), .Q(d_ff_as_7_q));  // open: nQ
  assign QC = ~nOE ? d_ff_as_6_q : 1'bz;  // DriverInvSel driverinvsel_3
  D_FF_AS d_ff_as_8 (.Set(1'b0), .D(d_ff_as_7_q), .C(RCLK), .Clr(1'b0), .Q(d_ff_as_8_q));  // open: nQ
  D_FF_AS d_ff_as_9 (.Set(1'b0), .D(d_ff_as_7_q), .C(SRCLK), .Clr(not_1_out), .Q(d_ff_as_9_q));  // open: nQ
  assign QD = ~nOE ? d_ff_as_8_q : 1'bz;  // DriverInvSel driverinvsel_4
  D_FF_AS d_ff_as_10 (.Set(1'b0), .D(d_ff_as_9_q), .C(RCLK), .Clr(1'b0), .Q(d_ff_as_10_q));  // open: nQ
  D_FF_AS d_ff_as_11 (.Set(1'b0), .D(d_ff_as_9_q), .C(SRCLK), .Clr(not_1_out), .Q(d_ff_as_11_q));  // open: nQ
  assign QE = ~nOE ? d_ff_as_10_q : 1'bz;  // DriverInvSel driverinvsel_5
  D_FF_AS d_ff_as_12 (.Set(1'b0), .D(d_ff_as_11_q), .C(SRCLK), .Clr(not_1_out), .Q(d_ff_as_12_q));  // open: nQ
  D_FF_AS d_ff_as_13 (.Set(1'b0), .D(d_ff_as_11_q), .C(RCLK), .Clr(1'b0), .Q(d_ff_as_13_q));  // open: nQ
  assign QF = ~nOE ? d_ff_as_13_q : 1'bz;  // DriverInvSel driverinvsel_6
  D_FF_AS d_ff_as_14 (.Set(1'b0), .D(d_ff_as_12_q), .C(RCLK), .Clr(1'b0), .Q(d_ff_as_14_q));  // open: nQ
  D_FF_AS d_ff_as_15 (.Set(1'b0), .D(d_ff_as_12_q), .C(SRCLK), .Clr(not_1_out), .Q(QH_2));  // open: nQ
  assign QG = ~nOE ? d_ff_as_14_q : 1'bz;  // DriverInvSel driverinvsel_7
  D_FF_AS d_ff_as_16 (.Set(1'b0), .D(QH_2), .C(RCLK), .Clr(1'b0), .Q(d_ff_as_16_q));  // open: nQ
  assign QH = ~nOE ? d_ff_as_16_q : 1'bz;  // DriverInvSel driverinvsel_8

  // Notes on the sheet:
  //   QH: pin 7
  //   QG: pin 6
  //   QF: pin 5
  //   QE: pin 4
  //   QD: pin 3
  //   QC: pin 2
  //   QB: pin 1
  //   QA: pin 15
  //   SER: pin 14
  //   SRCLK: pin 11
  //   nSRCLR: pin 10
  //   RCLK: pin 12
  //   nOE: pin 13
  //   QH_2: pin 9
  //   VCC: pin 16, default 1
  //   GND: pin 8
endmodule
