// Digital circuit 74HC597.dig as structural Verilog
module _74HC597 (
  input  nMR,
  input  SHCP,
  input  DS,
  input  STCP,
  input  nPL,
  input  D7,
  input  D6,
  input  D5,
  input  D4,
  input  D3,
  input  D2,
  input  D1,
  input  D0,
  output Q7
);

  wire and_1_out, and_2_out, and_3_out, and_4_out, and_5_out, and_6_out, and_7_out, and_8_out, and_9_out,
       and_10_out, and_11_out, and_12_out, and_13_out, and_14_out, and_15_out, and_16_out, d_ff_1_nq,
       d_ff_1_q, d_ff_2_nq, d_ff_2_q, d_ff_3_nq, d_ff_3_q, d_ff_4_nq, d_ff_4_q, d_ff_5_nq, d_ff_5_q,
       d_ff_6_nq, d_ff_6_q, d_ff_7_nq, d_ff_7_q, d_ff_8_nq, d_ff_8_q, d_ff_as_1_q, d_ff_as_2_q, d_ff_as_3_q,
       d_ff_as_4_q, d_ff_as_5_q, d_ff_as_6_q, d_ff_as_7_q, not_1_out, not_2_out, or_1_out, or_2_out,
       or_3_out, or_4_out, or_5_out, or_6_out, or_7_out, or_8_out;

  D_FF d_ff_1 (.D(D0), .C(STCP), .Q(d_ff_1_q), .nQ(d_ff_1_nq));
  D_FF d_ff_2 (.D(D1), .C(STCP), .Q(d_ff_2_q), .nQ(d_ff_2_nq));
  D_FF d_ff_3 (.D(D2), .C(STCP), .Q(d_ff_3_q), .nQ(d_ff_3_nq));
  D_FF d_ff_4 (.D(D3), .C(STCP), .Q(d_ff_4_q), .nQ(d_ff_4_nq));
  D_FF d_ff_5 (.D(D4), .C(STCP), .Q(d_ff_5_q), .nQ(d_ff_5_nq));
  D_FF d_ff_6 (.D(D5), .C(STCP), .Q(d_ff_6_q), .nQ(d_ff_6_nq));
  D_FF d_ff_7 (.D(D6), .C(STCP), .Q(d_ff_7_q), .nQ(d_ff_7_nq));
  D_FF d_ff_8 (.D(D7), .C(STCP), .Q(d_ff_8_q), .nQ(d_ff_8_nq));
  not not_1 (not_1_out, nPL);
  and and_1 (and_1_out, not_1_out, d_ff_1_q);
  and and_2 (and_2_out, d_ff_1_nq, not_1_out);
  and and_3 (and_3_out, not_1_out, d_ff_2_q);
  and and_4 (and_4_out, d_ff_2_nq, not_1_out);
  and and_5 (and_5_out, not_1_out, d_ff_3_q);
  and and_6 (and_6_out, d_ff_3_nq, not_1_out);
  and and_7 (and_7_out, not_1_out, d_ff_4_q);
  and and_8 (and_8_out, d_ff_4_nq, not_1_out);
  and and_9 (and_9_out, not_1_out, d_ff_5_q);
  and and_10 (and_10_out, d_ff_5_nq, not_1_out);
  and and_11 (and_11_out, not_1_out, d_ff_6_q);
  and and_12 (and_12_out, d_ff_6_nq, not_1_out);
  and and_13 (and_13_out, not_1_out, d_ff_7_q);
  and and_14 (and_14_out, d_ff_7_nq, not_1_out);
  and and_15 (and_15_out, not_1_out, d_ff_8_q);
  and and_16 (and_16_out, d_ff_8_nq, not_1_out);
  not not_2 (not_2_out, nMR);
  or or_1 (or_1_out, and_2_out, not_2_out);
  or or_2 (or_2_out, and_4_out, not_2_out);
  or or_3 (or_3_out, and_6_out, not_2_out);
  or or_4 (or_4_out, and_8_out, not_2_out);
  or or_5 (or_5_out, and_10_out, not_2_out);
  or or_6 (or_6_out, and_12_out, not_2_out);
  or or_7 (or_7_out, and_14_out, not_2_out);
  or or_8 (or_8_out, and_16_out, not_2_out);
  D_FF_AS d_ff_as_1 (.Set(and_1_out), .D(DS), .C(SHCP), .Clr(or_1_out), .Q(d_ff_as_1_q));  // open: nQ
  D_FF_AS d_ff_as_2 (.Set(and_3_out), .D(d_ff_as_1_q), .C(SHCP), .Clr(or_2_out), .Q(d_ff_as_2_q));  // open: nQ
  D_FF_AS d_ff_as_3 (.Set(and_5_out), .D(d_ff_as_2_q), .C(SHCP), .Clr(or_3_out), .Q(d_ff_as_3_q));  // open: nQ
  D_FF_AS d_ff_as_4 (.Set(and_7_out), .D(d_ff_as_3_q), .C(SHCP), .Clr(or_4_out), .Q(d_ff_as_4_q));  // open: nQ
  D_FF_AS d_ff_as_5 (.Set(and_9_out), .D(d_ff_as_4_q), .C(SHCP), .Clr(or_5_out), .Q(d_ff_as_5_q));  // open: nQ
  D_FF_AS d_ff_as_6 (.Set(and_11_out), .D(d_ff_as_5_q), .C(SHCP), .Clr(or_6_out), .Q(d_ff_as_6_q));  // open: nQ
  D_FF_AS d_ff_as_7 (.Set(and_13_out), .D(d_ff_as_6_q), .C(SHCP), .Clr(or_7_out), .Q(d_ff_as_7_q));  // open: nQ
  D_FF_AS d_ff_as_8 (.Set(and_15_out), .D(d_ff_as_7_q), .C(SHCP), .Clr(or_8_out), .Q(Q7));  // open: nQ
endmodule
