// Digital circuit 74HC85.dig as structural Verilog
module _74HC85 (
  input  A0,
  input  A1,
  input  A2,
  input  A3,
  input  B0,
  input  B1,
  input  B2,
  input  B3,
  input  I__gt,
  input  I__eq,
  input  I__lt,
  output gt,
  output eq,
  output lt
);

  wire and_1_out, and_2_out, comparator_1_eq, comparator_1_gt, comparator_1_lt;

  Comparator #(.Bits(4)) comparator_1 (
    .a({A3, A2, A1, A0}), .b({B3, B2, B1, B0}), .gt(comparator_1_gt), .eq(comparator_1_eq),
    .lt(comparator_1_lt));
  and and_1 (and_1_out, comparator_1_eq, I__gt);
  and and_2 (and_2_out, comparator_1_eq, I__lt);
  and and_3 (eq, comparator_1_eq, I__eq);
  or or_1 (gt, comparator_1_gt, and_1_out);
  or or_2 (lt, comparator_1_lt, and_2_out);
endmodule
