// Digital circuit ALU-comb.dig as structural Verilog
module ALU_comb (
  input  A,
  input  B,
  input  C,
  input  N,
  output XOR,
  output OR,
  output AND,
  output SUM,
  output nC,
  output nNEG
);

  wire and_2_out, and_3_out, nor_1_out, nor_3_out, nor_4_out, xor_1_out, xor_3_out;

  xor xor_1 (xor_1_out, B, N);
  xor xor_2 (XOR, A, B);
  nor nor_1 (nor_1_out, A, B);
  and and_1 (AND, A, B);
  nor nor_2 (OR, nor_1_out, nor_1_out);
  xor xor_3 (xor_3_out, A, xor_1_out);
  and and_2 (and_2_out, A, xor_1_out);
  nor nor_3 (nor_3_out, A, xor_1_out);
  and and_3 (and_3_out, xor_3_out, C);
  nor nor_4 (nor_4_out, nor_3_out, C);
  xor xor_4 (SUM, xor_3_out, C);
  nor nor_5 (nC, and_3_out, and_2_out);
  nor nor_6 (nNEG, and_2_out, nor_4_out);

  // Notes on the sheet:
  //   Explanation of ~{NEG}:
  //   Consider a and b to be the most significant bits of the signed numbers A and B
  //   ~{NEG} is 0 if A < B otherwise ~{NEG} is 1
  //   If a & ~b is true, A is negative and B is positive, so A is always smaller than B and ~{NEG} is forced low
  //   If ~a & b is true, A is positive and B is negative, so A is always larger than B and ~{NEG} is forced high
  //   If a = b , A and B have the same sign, and the result of the comparison depends on he sign of A-B.
  //   The MSB of the result is given by a + ~b + C, and since a + ~b = 1 we find ~{NEG} = C
endmodule

/* Test case Test Boolean:
A    B    C    N       XOR OR AND
0    0    X    X       0   0  0
0    1    X    X       1   1  0
1    0    X    X       1   1  0
1    1    X    X       0   1  1
*/

/* Test case Test Add:
A    B    C    N     SUM ~C ~NEG
0    0    0    0     0    1  X	
0    1    0    0     1    1  X	
1    0    0    0     1    1  X	
1    1    0    0     0    0  X	
0    0    1    0     1    1  X	
0    1    1    0     0    0  X	
1    0    1    0     0    0  X	
1    1    1    0     1    0  X
*/

/* Test case Test Sub:
A    B    C    N     SUM ~C ~NEG
0    0    1    1     0    0  1
1    0    1    1     1    0  0
0    1    1    1     1    1  1
1    1    1    1     0    0  1
0    0    0    1     1    1  0
1    0    0    1     0    0  0
0    1    0    1     0    1  1
1    1    0    1     1    1  0
*/
