// Digital circuit ALU-shift-step.dig as structural Verilog
module ALU_shift_step (
  input  nCLK,
  input  nRESET,
  input  nEN,
  output SH_LOADLEN,
  output nSH_OUTPUT,
  output SH_RESET
);

  wire _74hc4017_1_q0, _74hc4017_1_q1, _74hc4017_1_q2, _74hc4017_1_q3, _74hc4017_1_q4, _74hc4017_1_q9,
       d_ff_as_1_q, diodeforward_6_out, not_1_out, or_1_out;

  D_FF_AS d_ff_as_1 (.Set(1'b0), .D(1'b1), .C(diodeforward_6_out), .Clr(~nRESET), .Q(d_ff_as_1_q));  // open: nQ
  not not_1 (not_1_out, nRESET);
  or or_1 (or_1_out, d_ff_as_1_q, nEN);
  _74HC4017 _74hc4017_1 (
    .CLK(nCLK), .nEN(or_1_out), .MR(not_1_out), .Q0(_74hc4017_1_q0), .Q1(_74hc4017_1_q1),
    .Q2(_74hc4017_1_q2), .Q3(_74hc4017_1_q3), .Q4(_74hc4017_1_q4), .Q9(_74hc4017_1_q9));  // open: Q5, Q6, Q7, Q8, nQ59
  DiodeForward diodeforward_1 (.in(_74hc4017_1_q0), .out(SH_LOADLEN));
  DiodeForward diodeforward_2 (.in(_74hc4017_1_q1), .out(SH_LOADLEN));
  DiodeForward diodeforward_3 (.in(_74hc4017_1_q2), .out(SH_LOADLEN));
  DiodeForward diodeforward_4 (.in(_74hc4017_1_q3), .out(SH_LOADLEN));
  DiodeForward diodeforward_5 (.in(_74hc4017_1_q4), .out(SH_RESET));
  DiodeForward diodeforward_6 (.in(_74hc4017_1_q9), .out(diodeforward_6_out));
  PullDown pulldown_1 (.out(SH_LOADLEN));
  PullDown pulldown_2 (.out(SH_RESET));
  not not_2 (nSH_OUTPUT, diodeforward_6_out);
  PullDown pulldown_3 (.out(diodeforward_6_out));
endmodule

/* Test case:
CLK  ~CLK  ~EN  ~RESET    SH-LOADLEN  SH-RESET  ~{SH-OUTPUT}

#0
0    1     0    0         1           0         1
1    0     0    0         1           0         1

#1
0    1     0    1         1           0         1
1    0     0    1         1           0         1

#2
0    1     0    1         1           0         1
1    0     0    1         1           0         1

#3
0    1     0    1         1           0         1
1    0     0    1         1           0         1

#4
0    1     0    1         0           1         1
1    0     0    1         0           1         1

#5
0    1     0    1         0           0         1
1    0     0    1         0           0         1

#6
0    1     0    1         0           0         1
1    0     0    1         0           0         1

#7
0    1     0    1         0           0         1
1    0     0    1         0           0         1

#8
0    1     0    1         0           0         1
1    0     0    1         0           0         1

#9
0    1     0    1         0           0         0
1    0     0    1         0           0         0

#10
0    1     0    1         0           0         0
1    0     0    1         0           0         0

#11
0    1     0    1         0           0         0
1    0     0    1         0           0         0

#12
0    1     0    1         0           0         0
1    0     0    1         0           0         0
*/
