// Digital circuit ALU.dig as structural Verilog
module ALU (
  input  CLK,
  input  A,
  input  B,
  input  N,
  input  nRESET_ALU,
  input  CLK_F,
  input  [2:0] S,
  input  LOADLEN_SH,
  input  nOUTPUT_SH,
  input  RESET_SH,
  output FLAG,
  output OUT,
  output [5:0] DLEN,
  output DSUM
);

  wire AND, C, d_ff_as_2_nq, demultiplexer_1_out_0, demultiplexer_1_out_1, EQUAL, LT, LTU, multiplexer_1_out,
       multiplexer_2_out, multiplexer_3_out, nC_O, nNEG_O, nor_1_out, OR, SHIFT, XOR;

  ALU_shifter alu_shifter_1 (
    .CLK(CLK), .IN_SH(A), .LENIN_SH(DSUM), .nLA(S[0]), .LOADLEN_SH(LOADLEN_SH), .nOUTPUT_SH(nOUTPUT_SH),
    .RESET_SH(RESET_SH), .OUT_SH(SHIFT), .DLEN(DLEN));
  nor nor_1 (nor_1_out, XOR, d_ff_as_2_nq);
  ALU_comb alu_comb_1 (.A(A), .B(B), .C(C), .N(N), .XOR(XOR), .OR(OR), .AND(AND), .SUM(DSUM), .nC(nC_O), .nNEG(nNEG_O));
  Demultiplexer #(.Default(1)) demultiplexer_1 (
    .sel(N), .in(nRESET_ALU), .out_0(demultiplexer_1_out_0), .out_1(demultiplexer_1_out_1));
  D_FF_AS d_ff_as_1 (.Set(~demultiplexer_1_out_0), .D(nC_O), .C(CLK), .Clr(~demultiplexer_1_out_1), .Q(LTU), .nQ(C));
  D_FF_AS d_ff_as_2 (.Set(~nRESET_ALU), .D(nor_1_out), .C(CLK), .Clr(1'b0), .Q(EQUAL), .nQ(d_ff_as_2_nq));
  D_FF_AS d_ff_as_3 (.Set(1'b0), .D(nNEG_O), .C(CLK), .Clr(~nRESET_ALU), .nQ(LT));  // open: Q
  Multiplexer #(.Selector_Bits(2)) multiplexer_1 (
    .sel(S[1:0]), .in_0(DSUM), .in_1(OR), .in_2(XOR), .in_3(AND), .out(multiplexer_1_out));
  Multiplexer #(.Selector_Bits(2)) multiplexer_2 (
    .sel(S[1:0]), .in_0(LTU), .in_1(LT), .in_2(EQUAL), .in_3(1'b0), .out(multiplexer_2_out));
  D_FF_AS d_ff_as_4 (.Set(1'b0), .D(multiplexer_2_out), .C(CLK_F), .Clr(1'b0), .Q(FLAG));  // open: nQ
  Multiplexer multiplexer_3 (.sel(S[1]), .in_0(FLAG), .in_1(SHIFT), .out(multiplexer_3_out));
  Multiplexer multiplexer_4 (.sel(S[2]), .in_0(multiplexer_1_out), .in_1(multiplexer_3_out), .out(OUT));

  // Other names for the same wires on the sheet: nRESET = nRESET_ALU; SUM = DSUM
endmodule

/* Test case Binary Operators:
CLK S          A        B        N ~RESET_ALU CLK_F LOADLEN_SH ~OUTPUT_SH RESET_SH   OUT           FLAG DLEN DSUM

loop (rep,32)

let A = random(256);
let B = random(256);

let ADD = 0;
let OR  = 1;
let XOR = 2;
let AND = 3;

# A+B

# Reset ALU
0    (ADD)     0        0        0 1          0     0          1          0          X             X    X    X
1    (ADD)     0        0        0 0          0     0          1          0          X             X    X    X

# Perform computation
loop (i,8)
0    (ADD)     (A>>i&1) (B>>i&1) 0 1          0     0          1          0          ((A+B)>>i&1)  X    X    X
1    (ADD)     (A>>i&1) (B>>i&1) 0 1          0     0          1          0          X             X    X    X
end loop

#A-B

0    (ADD)     0        0        1 1          0     0          1          0          X             X    X    X
1    (ADD)     0        0        1 0          0     0          1          0          X             X    X    X

loop (i,8)
0    (ADD)     (A>>i&1) (B>>i&1) 1 1          0     0          1          0          ((A-B)>>i&1)  X    X    X
1    (ADD)     (A>>i&1) (B>>i&1) 1 1          0     0          1          0          X             X    X    X
end loop

#A|B

0    (OR)      0        0        1 1          0     0          1          0          X             X    X    X
1    (OR)      0        0        1 0          0     0          1          0          X             X    X    X

loop (i,8)
0    (OR)      (A>>i&1) (B>>i&1) 1 1          0     0          1          0          ((A|B)>>i&1)  X    X    X
1    (OR)      (A>>i&1) (B>>i&1) 1 1          0     0          1          0          X             X    X    X
end loop


#A^B

0    (XOR)     0        0        1 1          0     0          1          0          X             X    X    X
1    (XOR)     0        0        1 0          0     0          1          0          X             X    X    X

loop (i,8)
0    (XOR)     (A>>i&1) (B>>i&1) 1 1          0     0          1          0          ((A^B)>>i&1)  X    X    X
1    (XOR)     (A>>i&1) (B>>i&1) 1 1          0     0          1          0          X             X    X    X
end loop


#A&B

0    (AND)     0        0        1 1          0     0          1          0          X             X    X    X
1    (AND)     0        0        1 0          0     0          1          0          X             X    X    X

loop (i,8)
0    (AND)     (A>>i&1) (B>>i&1) 1 1          0     0          1          0          ((A&B)>>i&1)  X    X    X
1    (AND)     (A>>i&1) (B>>i&1) 1 1          0     0          1          0          X             X    X    X
end loop

end loop
*/

/* Test case Flags:
CLK S          A        B        N ~RESET_ALU CLK_F LOADLEN_SH ~OUTPUT_SH RESET_SH   OUT           FLAG DLEN DSUM

loop (rep,32)

##############################################################################################################
#
# 0 <= A < B < 128

let A = random(127);
let B = A + 1 + random(126-A);
let U = 1;
let S = 1;
let E = 0;

let LTU   = 0;
let LT    = 1;
let EQUAL = 2;

# LTU

# Reset ALU
0    (LTU)     0        0        1 1          0     0          1          0          X             X    X    X
1    (LTU)     0        0        1 0          0     0          1          0          X             X    X    X

# Perform calculation
loop (i,8)
0    (LTU)     (A>>i&1) (B>>i&1) 1 1          0     0          1          0          X             X    X    X
1    (LTU)     (A>>i&1) (B>>i&1) 1 1          0     0          1          0          X             X    X    X
end loop

# Clock in flag
0    (LTU)     0        0        1 1          1     0          1          0          X             X    X    X
1    (LTU)     0        0        1 1          1     0          1          0          X             X    X    X

# Check
0    (LTU)     0        0        1 1          0     0          1          0          X             (U)  X    X
1    (LTU)     0        0        1 1          0     0          1          0          X             (U)  X    X
0    (LTU)     0        0        1 1          0     0          1          0          X             (U)  X    X

# LT

0    (LT)      0        0        1 1          0     0          1          0          X             X    X    X
1    (LT)      0        0        1 0          0     0          1          0          X             X    X    X

loop (i,8)
0    (LT)      (A>>i&1) (B>>i&1) 1 1          0     0          1          0          X             X    X    X
1    (LT)      (A>>i&1) (B>>i&1) 1 1          0     0          1          0          X             X    X    X
end loop

0    (LT)      0        0        1 1          1     0          1          0          X             X    X    X
1    (LT)      0        0        1 1          1     0          1          0          X             X    X    X
0    (LT)      0        0        1 1          0     0          1          0          X             (S)  X    X
1    (LT)      0        0        1 1          0     0          1          0          X             (S)  X    X
0    (LT)      0        0        1 1          0     0          1          0          X             (S)  X    X

# Equal

0    (EQUAL)   0        0        1 1          0     0          1          0          X             X    X    X
1    (EQUAL)   0        0        1 0          0     0          1          0          X             X    X    X

loop (i,8)
0    (EQUAL)   (A>>i&1) (B>>i&1) 1 1          0     0          1          0          X             X    X    X
1    (EQUAL)   (A>>i&1) (B>>i&1) 1 1          0     0          1          0          X             X    X    X
end loop

0    (EQUAL)   0        0        1 1          1     0          1          0          X             X    X    X
1    (EQUAL)   0        0        1 1          1     0          1          0          X             X    X    X
0    (EQUAL)   0        0        1 1          0     0          1          0          X             (E)  X    X
1    (EQUAL)   0        0        1 1          0     0          1          0          X             (E)  X    X
0    (EQUAL)   0        0        1 1          0     0          1          0          X             (E)  X    X


##############################################################################################################
#
# 0 <= B < A < 128

let A = 1 + random(127);
let B = random(A);
let U = 0;
let S = 0;
let E = 0;

# LTU

0    (LTU)     0        0        1 1          0     0          1          0          X             X    X    X
1    (LTU)     0        0        1 0          0     0          1          0          X             X    X    X

loop (i,8)
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*/

/* Test case SLT/SLTU:
CLK S          A        B        N ~RESET_ALU CLK_F LOADLEN_SH ~OUTPUT_SH RESET_SH   OUT           FLAG DLEN DSUM

loop (rep,32)

##############################################################################################################
#
# 0 <= A < B < 128

let A = random(127);
let B = A + 1 + random(126-A);
let U = 1;
let S = 1;

let SLTU = 4;
let SLT  = 5;
let ADD  = 0;

# SLTU

# Reset ALU
0    (SLTU)    0        0        1 1          0     0          1          0          X             X    X    X
1    (SLTU)    0        0        1 0          0     0          1          0          X             X    X    X

# Perform computation
loop (i,8)
0    (SLTU)    (A>>i&1) (B>>i&1) 1 1          0     0          1          0          X             X    X    X
1    (SLTU)    (A>>i&1) (B>>i&1) 1 1          0     0          1          0          X             X    X    X
end loop

# Set flag
0    (SLTU)    0        0        1 1          1     0          1          0          X             X    X    X
1    (SLTU)    0        0        1 1          1     0          1          0          X             X    X    X

# Output flag
0    (SLTU)    0        0        1 1          0     0          1          0          (U)           X    X    X
1    (SLTU)    0        0        1 1          0     0          1          0          X             X    X    X

# Output zeros
loop (i,7)
0    (ADD)     0        0        1 0          0     0          1          0          0             X    X    X
1    (ADD)     0        0        1 0          0     0          1          0          X             X    X    X
end loop


# SLT

0    (SLT)     0        0        1 1          0     0          1          0          X             X    X    X
1    (SLT)     0        0        1 0          0     0          1          0          X             X    X    X

loop (i,8)
0    (SLT)     (A>>i&1) (B>>i&1) 1 1          0     0          1          0          X             X    X    X
1    (SLT)     (A>>i&1) (B>>i&1) 1 1          0     0          1          0          X             X    X    X
end loop

0    (SLT)     0        0        1 1          1     0          1          0          X             X    X    X
1    (SLT)     0        0        1 1          1     0          1          0          X             X    X    X

0    (SLT)     0        0        1 1          0     0          1          0          (S)           X    X    X
1    (SLT)     0        0        1 1          0     0          1          0          X             X    X    X

loop (i,7)
0    (ADD)     0        0        1 0          0     0          1          0          0             X    X    X
1    (ADD)     0        0        1 0          0     0          1          0          X             X    X    X
end loop



##############################################################################################################
#
# 0 <= B < A < 128

let A = 1 + random(127);
let B = random(A);
let U = 0;
let S = 0;


# SLTU

0    (SLTU)    0        0        1 1          0     0          1          0          X             X    X    X
1    (SLTU)    0        0        1 0          0     0          1          0          X             X    X    X

loop (i,8)
0    (SLTU)    (A>>i&1) (B>>i&1) 1 1          0     0          1          0          X             X    X    X
1    (SLTU)    (A>>i&1) (B>>i&1) 1 1          0     0          1          0          X             X    X    X
end loop

0    (SLTU)    0        0        1 1          1     0          1          0          X             X    X    X
1    (SLTU)    0        0        1 1          1     0          1          0          X             X    X    X

0    (SLTU)    0        0        1 1          0     0          1          0          (U)           X    X    X
1    (SLTU)    0        0        1 1          0     0          1          0          X             X    X    X

loop (i,7)
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*/

/* Test case SLL/SRL:
CLK S          A        B        N ~RESET_ALU CLK_F LOADLEN_SH ~OUTPUT_SH RESET_SH   OUT           FLAG DLEN DSUM

loop (rep,32)

let A = random(256);
let B = random(8);

let SLL = 6;

# SLL

let R = (A << B) & 0xFF;

# Reset ALU

0   (SLL)      0        0        0 1          0     0          1          0          X             X    X    X
1   (SLL)      0        0        0 0          0     0          1          0          X             X    X    X

# Load length

loop (i,16)
0   (SLL)      (7>>i&1) (B>>i&1) 0 1          0     1          1          0          X             X    X    X
1   (SLL)      (7>>i&1) (B>>i&1) 0 1          0     1          1          0          X             X    X    X
end loop

# Latch in length

0   (SLL)      0        0        0 1          0     0          1          1          X             X    X    X
1   (SLL)      0        0        0 1          0     0          1          0          X             X    X    X

# Load in argument

loop (i,8)
0   (SLL)      (A>>i&1) 0        0 1          0     0          1          0          X             X    X    X
1   (SLL)      (A>>i&1) 0        0 1          0     0          1          0          X             X    X    X
end loop

# Output result

loop (i,8)
0   (SLL)      0        0        0 1          0     0          0          0          (R>>i&1)      X    X    X
1   (SLL)      0        0        0 1          0     0          0          0          X             X    X    X
end loop

# SRL

let R = (A >> B) & 0xFF;

0   (SLL)      0        0        1 1          0     0          1          0          X             X    X    X
1   (SLL)      0        0        1 0          0     0          1          0          X             X    X    X

loop (i,16)
0   (SLL)      (7>>i&1) (B>>i&1) 1 1          0     1          1          0          X             X    X    X
1   (SLL)      (7>>i&1) (B>>i&1) 1 1          0     1          1          0          X             X    X    X
end loop

0   (SLL)      0        0        0 1          0     0          1          1          X             X    X    X
1   (SLL)      0        0        0 1          0     0          1          0          X             X    X    X

loop (i,8)
0   (SLL)      (A>>i&1) 0        0 1          0     0          1          0          X             X    X    X
1   (SLL)      (A>>i&1) 0        0 1          0     0          1          0          X             X    X    X
end loop

loop (i,8)
0   (SLL)      0        0        0 1          0     0          0          0          (R>>i&1)      X    X    X
1   (SLL)      0        0        0 1          0     0          0          0          X             X    X    X
end loop

end loop
*/

/* Test case SRA:
CLK S          A        B        N ~RESET_ALU CLK_F LOADLEN_SH ~OUTPUT_SH RESET_SH   OUT           FLAG DLEN DSUM

loop (rep,32)

let SRA = 7;

# SRA

let A = random(256);
let S = (A >> 7) & 1;

let B = 0;
let R = (A >> B) & 0xFF;

# Reset ALU

0   (SRA)      0        0        1 1          0     0          1          0          X             X    X    X
1   (SRA)      0        0        1 0          0     0          1          0          X             X    X    X

# Load shift length

loop (i,16)
0   (SRA)      (7>>i&1) (B>>i&1) 1 1          0     1          1          0          X             X    X    X
1   (SRA)      (7>>i&1) (B>>i&1) 1 1          0     1          1          0          X             X    X    X
end loop

# Latch length

0   (SRA)      0        0        1 1          0     0          1          1          X             X    X    X
1   (SRA)      0        0        1 1          0     0          1          0          X             X    X    X

# Load argument

loop (i,8)
0   (SRA)      (A>>i&1) 0        1 1          0     0          1          0          X             X    X    X
1   (SRA)      (A>>i&1) 0        1 1          0     0          1          0          X             X    X    X
end loop

# Output result

loop (i,8-0)
0   (SRA)      0        0        1 1          0     0          0          0          (R>>i&1)      X    X    X
1   (SRA)      0        0        1 1          0     0          0          0          X             X    X    X
end loop

loop (i,0)
0   (SRA)      0        0        1 1          0     0          0          0          (S)           X    X    X
1   (SRA)      0        0        1 1          0     0          0          0          X             X    X    X
end loop




let B = 1;
let R = (A >> B) & 0xFF;

0   (SRA)      0        0        1 1          0     0          1          0          X             X    X    X
1   (SRA)      0        0        1 0          0     0          1          0          X             X    X    X

loop (i,16)
0   (SRA)      (7>>i&1) (B>>i&1) 1 1          0     1          1          0          X             X    X    X
1   (SRA)      (7>>i&1) (B>>i&1) 1 1          0     1          1          0          X             X    X    X
end loop

0   (SRA)      0        0        1 1          0     0          1          1          X             X    X    X
1   (SRA)      0        0        1 1          0     0          1          0          X             X    X    X

loop (i,8)
0   (SRA)      (A>>i&1) 0        1 1          0     0          1          0          X             X    X    X
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*/
