// Digital circuit CPU.dig as structural Verilog
module CPU (
  input  CLK_RAW,
  input  [31:0] Breakpoint,
  output [31:0] x8_s0,
  output [31:0] x9_s1,
  output [31:0] x10_a0,
  output [31:0] PC,
  output [31:0] Address,
  output [31:0] Instr,
  output [7:0] Data_Read,
  output [5:0] Step,
  output [7:0] Substep,
  output [31:0] A,
  output [31:0] B,
  output [31:0] Result,
  output [11:0] CSR_Address,
  output [31:0] x11_a1,
  output [31:0] x4_tp,
  output [31:0] x5_t0,
  output [31:0] x6_t1,
  output [31:0] x7_t2,
  output [31:0] x1_ra,
  output [31:0] x2_sp,
  output [31:0] x3_gp,
  output [31:0] x12_a2,
  output [31:0] x13_a3,
  output [31:0] x14_a4,
  output [31:0] x15_a5,
  output [31:0] mepc,
  output [31:0] mscratch,
  output [31:0] mstatus,
  output [31:0] mie,
  output [31:0] mip,
  output [31:0] mcause,
  output [31:0] mtvec,
  output [7:0] Data_Write,
  output [31:0] Instr_2,
  output [31:0] Cycles,
  output [15:0] Instr16,
  output [4:0] Val,
  output out_40,
  output Compr,
  output [7:0] Data,
  output en,
  output rs
);

  wire ADDR_CLK_GATED, ADDR_IN, ADDR_LATCH, ALU_A, ALU_AUX, ALU_B, ALU_B_MUX, ALU_N, ALU_OUT, and_1_out,
       and_2_out, and_7_out, and_8_out, B_INSTR, B_RESET, B_RUN, B_STEP, B_STOP, B_SUBSTEP, BUS_CLK, BUS_EN,
       BUT_INSTR, BUT_STOP, button_1_out, button_2_out, CLK, CLK_t, CNT_2, comparator_1_eq, comparator_1_gt,
       comparator_1_lt, comparator_2_eq, comparator_3_eq, CS_0x4000000, CS_IO, CS_RAM, CS_ROM,
       CSR_ADDR_LATCH, CSR_IN, CSR_IN_LATCH, CSR_IN_t, CSR_OUT, CSR_OUT_LATCH, CSR_PC_OUT, d_ff_7_q,
       d_ff_8_q, d_ff_9_q, d_ff_12_q, d_ff_13_q, d_ff_15_q, d_ff_as_1_q, d_ff_as_4_q, d_ff_as_5_q, FLAG, Imm,
       Imm_t, INT1P, INT2P, INT3P, LASTSTEP, LED_G, LED_R, LEN8, Mem_Dval, MEM_IN, MEM_OUT, MEM_OUT_t,
       MEPC_OUT, mie_1_mei1e, mie_1_mei2e, mie_1_mei3e, MIE_t, mip_1_mei1p, mip_1_mei2p, mip_1_mei3p, MRET,
       MTVEC_OUT, multiplexer_4_out, multiplexer_7_out, nALU_RESET, nand_1_out, nCLK, nCLK_t, nILL_OP, nIRQ,
       nKB_INT, nMEM_OE, nMEM_OE_GATED, nMEM_OE_OUT, nMEM_WE, nMEM_WE_OUT, not_1_out, not_2_out, not_4_out,
       nREG_IN_EN, nRESET, nS_EXT, nSLEEP, nWAIT, OP_FETCH, OP_IMM_LATCH, OP_IN_MUX, OP_LATCH, OP_LATCH_LSB,
       OPDONE, or_3_out, or_5_out, PC_IN, PC_IN_LATCH, PC_IN_MUX, PC_OUT, PC_OUT_LATCH, PC_OUT_t, REG_IN,
       regviewer_1_p5, regviewer_1_p6, regviewer_1_p7, regviewer_1_p8, regviewer_1_p9, regviewer_1_p10,
       regviewer_1_p11, regviewer_1_p12, regviewer_1_p13, regviewer_1_p14, regviewer_1_p15, regviewer_1_p16,
       regviewer_1_p17, regviewer_1_p18, regviewer_1_p19, regviewer_1_p20, regviewer_1_p21, regviewer_1_p22,
       regviewer_1_p23, regviewer_1_p24, regviewer_1_p25, regviewer_1_p26, regviewer_1_p27,
       regviewermonitor_1_p24, regviewermonitor_1_p25, regviewermonitor_1_p26, regviewermonitor_1_p27,
       regviewermonitor_1_p28, regviewermonitor_1_p29, regviewermonitor_1_p30, regviewermonitor_1_p31, RESET,
       reset_2_out, RS1, RS1_t, RS2, RSA, RSB, SA, sd_spi_1_cs, sd_spi_1_mosi, sd_spi_1_nwait, sd_spi_1_sclk,
       sdcard_1_p5, STEPDONE, switch_1_a, switchdt_1_p4, SYS, TRAP_OP, WAKEUP;
  wire [0:0] LEN;
  wire [1:0] ALU_A_MUX, REG_IN_MUX, TRAP2;
  wire [2:0] ALU_OP, FUNC3, IMM_MUX;
  wire [3:0] RSD;
  wire [4:0] OPCODE;
  wire [15:0] d_ff_14_q;
  wire [20:8] d_ff_17_q;
  wire [31:0] MicroCode_d;
  wire [31:1] DATA_ADDR;

  // RegViewer regviewer_1: pin names not known; wires that end beside it: BUS_CLK, nREG_IN_EN, REG_IN, RSD, regviewer_1_p5, regviewer_1_p6, regviewer_1_p7, regviewer_1_p8, regviewer_1_p9, regviewer_1_p10, regviewer_1_p11, regviewer_1_p12, regviewer_1_p13, regviewer_1_p14, regviewer_1_p15, regviewer_1_p16, regviewer_1_p17, regviewer_1_p18, regviewer_1_p19, regviewer_1_p20, regviewer_1_p21, regviewer_1_p22, regviewer_1_p23, regviewer_1_p24, regviewer_1_p25, regviewer_1_p26, regviewer_1_p27
  not not_1 (not_1_out, nCLK);
  // RegViewerMonitor regviewermonitor_1: pin names not known; wires that end beside it: regviewer_1_p5, regviewer_1_p6, regviewer_1_p7, regviewer_1_p8, regviewer_1_p9, regviewer_1_p10, regviewer_1_p11, regviewer_1_p12, regviewer_1_p13, regviewer_1_p14, regviewer_1_p15, regviewer_1_p16, regviewer_1_p17, regviewer_1_p18, regviewer_1_p19, regviewer_1_p20, regviewer_1_p21, regviewer_1_p22, regviewer_1_p23, regviewer_1_p24, regviewer_1_p25, regviewer_1_p26, regviewer_1_p27, regviewermonitor_1_p24, regviewermonitor_1_p25, regviewermonitor_1_p26, regviewermonitor_1_p27, regviewermonitor_1_p28, regviewermonitor_1_p29, regviewermonitor_1_p30, regviewermonitor_1_p31
  D_FF d_ff_1 (.D(RS1), .C(not_1_out), .Q(RS1_t));  // open: nQ
  D_FF d_ff_2 (.D(RS2), .C(not_1_out), .Q(MEM_IN));  // open: nQ
  D_FF d_ff_3 (.D(MEM_OUT), .C(not_1_out), .Q(MEM_OUT_t));  // open: nQ
  D_FF d_ff_4 (.D(Imm), .C(not_1_out), .Q(Imm_t));  // open: nQ
  D_FF d_ff_5 (.D(PC_OUT), .C(not_1_out), .Q(PC_OUT_t));  // open: nQ
  D_FF d_ff_6 (.D(CSR_IN), .C(not_1_out), .Q(CSR_IN_t));  // open: nQ
  D_FF d_ff_7 (.D(ALU_OUT), .C(not_1_out), .Q(d_ff_7_q));  // open: nQ
  Multiplexer multiplexer_1 (.sel(ALU_OP[2]), .in_0(ALU_OUT), .in_1(d_ff_7_q), .out(ADDR_IN));
  // RGBLED rgbled_1: pin names not known; wires that end beside it: LED_R, LED_G, 1'b0
  Comparator #(.Bits(32)) comparator_1 (
    .a(x3_gp), .b(32'h1), .gt(comparator_1_gt), .eq(comparator_1_eq), .lt(comparator_1_lt));
  and and_1 (and_1_out, nIRQ, nILL_OP);
  // RGBLED rgbled_2: pin names not known; wires that end beside it: comparator_1_gt, comparator_1_eq, comparator_1_lt
  Comparator #(.Bits(32)) comparator_2 (.a(Breakpoint), .b(PC), .eq(comparator_2_eq));  // open: gt, lt
  Button #(.activeLow("true")) Stop (.out(BUT_STOP));
  Button #(.activeLow("true")) Run (.out(B_RUN));
  Button #(.activeLow("true")) u_Reset (.out(B_RESET));
  Switch switch_1 (.A(switch_1_a), .B(comparator_1_lt));
  D_FF d_ff_8 (.D(comparator_2_eq), .C(~OPDONE), .Q(d_ff_8_q));  // open: nQ
  Interrupt_Controller interrupt_controller_1 (
    .BUS_CLK(BUS_CLK), .OP_FETCH(OP_LATCH), .nTRAP(and_1_out), .nRESET(nRESET), .TRAP_OP(TRAP_OP),
    .TRAP_OP_FETCH(OP_IN_MUX));
  PullUp pullup_1 (.out(switch_1_a));
  D_FF_AS #(.Default(1)) d_ff_as_1 (.Set(nCLK), .D(1'b0), .C(d_ff_8_q), .Clr(1'b0), .Q(d_ff_as_1_q));  // open: nQ
  Button #(.activeLow("true")) One_Instruction (.out(BUT_INSTR));
  Button #(.activeLow("true")) One_Step (.out(B_STEP));
  Button #(.activeLow("true")) One_Substep (.out(B_SUBSTEP));
  D_FF #(.Default(1)) d_ff_9 (.D(switch_1_a), .C(OPDONE), .Q(d_ff_9_q));  // open: nQ
  DiodeBackward diodebackward_1 (.in(d_ff_9_q), .out(B_STOP));
  DiodeBackward diodebackward_2 (.in(BUT_STOP), .out(B_STOP));
  DiodeBackward diodebackward_3 (.in(d_ff_as_1_q), .out(B_INSTR));
  DiodeBackward diodebackward_4 (.in(BUT_INSTR), .out(B_INSTR));
  PullUp pullup_2 (.out(B_STOP));
  PullUp pullup_3 (.out(B_INSTR));
  not not_2 (not_2_out, BUS_CLK);
  ALU alu_1 (
    .BUS_CLK(BUS_CLK), .A(ALU_A), .B(ALU_B), .N(ALU_N), .ALU_nRESET(nALU_RESET), .ALU_AUX(ALU_AUX),
    .S(ALU_OP), .FLAG(FLAG), .OUT(ALU_OUT));  // open: DLEN, DSUM, C
  and and_2 (and_2_out, CNT_2, OP_LATCH_LSB);
  nand nand_1 (nand_1_out, nMEM_OE_GATED, nMEM_WE);
  // _744024 _744024_1: pin names not known; wires that end beside it: not_2_out, RESET, Val[0], Val[1], Val[2], Val[3], Val[4], CLK, CLK_t, nCLK
  and and_3 (LEN8, LEN[0], BUS_EN);
  // Mem mem_1: pin names not known; wires that end beside it: CLK, BUS_CLK, MEM_IN, ADDR_IN, ADDR_LATCH, ADDR_CLK_GATED, nMEM_OE_GATED, nMEM_WE, nS_EXT, nRESET, MEM_OUT, Data, {DATA_ADDR, rs}, Address, Mem_Dval, nMEM_OE_OUT
  D_FF #(.Bits(8)) d_ff_10 (.D(Data), .C(nMEM_OE_OUT), .Q(Data_Read));  // open: nQ
  D_FF #(.Bits(8)) d_ff_11 (.D(Data), .C(nMEM_WE_OUT), .Q(Data_Write));  // open: nQ
  Clock_driver clock_driver_1 (
    .CLK_RAW(CLK_RAW), .Stop(B_STOP), .Run(B_RUN), .One_Instruction(B_INSTR), .One_Step(B_STEP),
    .One_Substep(B_SUBSTEP), .nSTEPDONE(STEPDONE), .OP_LATCH(OPDONE), .nRESET(RESET), .nWAKEUP(WAKEUP),
    .SLEEP(nSLEEP), .nWAIT_DONE(nWAIT));  // open: nWAIT, CLK, nCLK, Running
  Reset reset_2 (.out(reset_2_out));
  and and_4 (nRESET, reset_2_out, B_RESET);
  or or_1 (nMEM_OE_GATED, nMEM_OE, and_2_out);
  D_FF d_ff_12 (.D(nand_1_out), .C(CLK), .Q(d_ff_12_q));  // open: nQ
  or or_2 (out_40, BUS_EN, Val[3], Val[4]);
  Comparator #(.Bits(8)) comparator_3 (.a({8{1'b0}}), .b(DATA_ADDR[15:8]), .eq(comparator_3_eq));  // open: gt, lt
  not not_3 (RESET, nRESET);
  D_FF d_ff_13 (.D(d_ff_12_q), .C(nCLK), .Q(d_ff_13_q));  // open: nQ
  D_FF #(.Bits(16)) d_ff_14 (.D({DATA_ADDR[15:1], rs}), .C(~CS_0x4000000), .Q(d_ff_14_q));  // open: nQ
  SD_SPI sd_spi_1 (
    .A({DATA_ADDR[15:1], rs}), .nCS(CS_0x4000000), .nWE(nMEM_WE_OUT), .nOE(nMEM_OE_OUT),
    .SPI_CLK_RAW(CLK_RAW), .MISO(sdcard_1_p5), .D(Data), .nWAIT(sd_spi_1_nwait), .SCLK(sd_spi_1_sclk),
    .MOSI(sd_spi_1_mosi), .CS(sd_spi_1_cs));
  and and_5 (OP_LATCH_LSB, Val[4], OP_FETCH);
  nor nor_1 (LASTSTEP, LEN[0], BUS_EN);
  or or_3 (or_3_out, d_ff_13_q, ADDR_LATCH);
  // Probe on d_ff_14_q
  nor nor_2 (en, nMEM_WE_OUT, ~comparator_3_eq, CS_0x4000000);  // NOr
  D_FF_AS d_ff_as_2 (.Set(~1'b1), .D(LASTSTEP), .C(CLK_t), .Clr(~nRESET), .Q(OP_LATCH));  // open: nQ
  PullUp pullup_4 (.out(nWAIT));
  D_FF d_ff_15 (.D(or_3_out), .C(CLK), .Q(d_ff_15_q));  // open: nQ
  // Probe on sd_spi_1_cs
  Clock clock_1 (
    .CLK(nCLK_t), .nCLK(CLK_t), .nLEN8(LEN8), .LASTSTEP(LASTSTEP), .nRESET(nRESET), .STEP(Step),
    .STEPDONE(STEPDONE), .SUBSTEP(Substep), .OPDONE(OPDONE));
  // SwitchDT switchdt_1: pin names not known; wires that end beside it: nMEM_WE_OUT, nMEM_WE_OUT, 1'b1, switchdt_1_p4
  Terminal terminal_1 (
    .A({DATA_ADDR[15:1], rs}), .nCS(CS_IO), .nWE(nMEM_WE_OUT), .nOE(nMEM_OE_OUT), .D(Data), .nINT(nKB_INT));
  D_FF d_ff_16 (.D(d_ff_15_q), .C(nCLK), .Q(ADDR_CLK_GATED));  // open: nQ
  // Probe on sd_spi_1_sclk
  // SdCard #(.AddrBits(16), .Bits(8)) sdcard_1: pin names not known; wires that end beside it: sd_spi_1_nwait, sd_spi_1_sclk, sd_spi_1_mosi, sd_spi_1_cs, sdcard_1_p5
  D_FF_AS d_ff_as_3 (.Set(~1'b1), .D(OP_LATCH), .C(nCLK), .Clr(~nRESET), .Q(OP_IMM_LATCH));  // open: nQ
  and and_6 (BUS_CLK, CLK, BUS_EN);
  EEPROM #(.AddrBits(16), .Bits(8)) Firmware (
    .A({DATA_ADDR[15:1], rs}), .CS(~CS_ROM), .WE(~switchdt_1_p4), .OE(~nMEM_OE_OUT), .D(Data));
  RAMSinglePortSel #(.AddrBits(16), .Bits(8)) RAM (
    .A({DATA_ADDR[15:1], rs}), .CS(~CS_RAM), .WE(~nMEM_WE_OUT), .OE(~nMEM_OE_OUT), .D(Data));
  Demultiplexer #(.Selector_Bits(2), .Default(1)) demultiplexer_1 (
    .sel(DATA_ADDR[31:30]), .in(1'b0), .out_0(CS_ROM), .out_1(CS_0x4000000), .out_2(CS_RAM), .out_3(CS_IO));
  // HD44780LCD #(.colorScheme(1)) hd44780lcd_1: pin names not known; wires that end beside it: rs, 1'b0, en, Data
  DebugShift32 debugshift32_1 (.CLK(BUS_CLK), .D(ALU_A), .nEN(1'b0), .Val(A));
  DebugShift32 debugshift32_2 (.CLK(BUS_CLK), .D(ALU_B), .nEN(1'b0), .Val(B));
  DebugShift32 debugshift32_3 (.CLK(BUS_CLK), .D(ADDR_IN), .nEN(1'b0), .Val(Result));
  // OpCode opcode_1: pin names not known; wires that end beside it: BUS_CLK, MEM_OUT_t, OP_LATCH, OP_LATCH_LSB, OP_IMM_LATCH, out_40, IMM_MUX, nRESET, OP_FETCH, OP_IN_MUX, Imm, RSA, RSB, RSD, OPCODE, FUNC3, SA, nS_EXT, SYS, TRAP2, CNT_2, Instr, Instr16, Compr, MRET
  // Probe on {FLAG, SA, SYS, FUNC3, OPCODE}
  ROM #(.AddrBits(17), .isProgramMemory("true"), .Bits(32)) MicroCode (
    .A({FLAG, SA, SYS, FUNC3, OPCODE, 1'b0, Step[4:0]}), .sel(1'b1), .D(MicroCode_d));
  // Probe on {FLAG, SA, SYS, FUNC3, OPCODE, 1'b0, Step[4:0]}
  and and_7 (and_7_out, nRESET, nCLK);
  Multiplexer multiplexer_2 (.sel(PC_IN_MUX), .in_0(ADDR_IN), .in_1(CSR_PC_OUT), .out(PC_IN));
  Multiplexer #(.Selector_Bits(2)) multiplexer_3 (
    .sel(REG_IN_MUX), .in_0(ALU_OUT), .in_1(MEM_OUT_t), .in_2(CSR_IN_t), .in_3(PC_OUT_t), .out(REG_IN));
  D_FF #(.Bits(32), .Default(4294967295)) d_ff_17 (
    .D(MicroCode_d), .C(and_7_out),
    .Q({REG_IN_MUX, IMM_MUX, ALU_A_MUX, PC_IN_MUX, CSR_IN_LATCH, CSR_OUT_LATCH, CSR_ADDR_LATCH, d_ff_17_q[20:18], nALU_RESET, ALU_AUX, ALU_OP, ALU_N, nREG_IN_EN, nMEM_WE, nMEM_OE, d_ff_17_q[8], ADDR_LATCH, nILL_OP, PC_OUT_LATCH, PC_IN_LATCH, OP_FETCH, nSLEEP, BUS_EN, LEN[0]}));  // open: nQ
  // Probe on {REG_IN_MUX, IMM_MUX, ALU_A_MUX, PC_IN_MUX, CSR_IN_LATCH, CSR_OUT_LATCH, CSR_ADDR_LATCH, d_ff_17_q[20:18], nALU_RESET, ALU_AUX, ALU_OP, ALU_N, nREG_IN_EN, nMEM_WE, nMEM_OE, d_ff_17_q[8], ADDR_LATCH, nILL_OP, PC_OUT_LATCH, PC_IN_LATCH, OP_FETCH, nSLEEP, BUS_EN, LEN[0]}
  Multiplexer multiplexer_4 (.sel(ALU_A_MUX[0]), .in_0(RS1_t), .in_1(PC_OUT_t), .out(multiplexer_4_out));
  Multiplexer multiplexer_5 (.sel(ALU_B_MUX), .in_0(MEM_IN), .in_1(Imm_t), .out(ALU_B));
  or or_4 (ALU_B_MUX, IMM_MUX[0], IMM_MUX[1], IMM_MUX[2]);
  Multiplexer multiplexer_6 (.sel(ALU_A_MUX[1]), .in_0(multiplexer_4_out), .in_1(ALU_A_MUX[0]), .out(ALU_A));
  PC pc_1 (
    .CLK(CLK), .BUS_CLK(BUS_CLK), .IN(PC_IN), .IN_LATCH(PC_IN_LATCH), .OUT_LATCH(PC_OUT_LATCH),
    .OUT_SnP(out_40), .CNT_EN(OP_IMM_LATCH), .CNT_2(CNT_2), .nRESET(nRESET), .OUT(PC_OUT), .PC(PC));
  // Register_bank register_bank_1: pin names not known; wires that end beside it: BUS_CLK, REG_IN, nREG_IN_EN, RSA, RSB, RSD, RESET, RS1, RS2
  Register_view register_view_1 (
    .BUS_CLK(BUS_CLK), .nREG_IN_EN(nREG_IN_EN), .REG_IN(REG_IN), .RSD(RSD), .x1_ra(x1_ra), .x2_sp(x2_sp),
    .x3_gp(x3_gp), .x4_tp(x4_tp), .x5_t0(x5_t0), .x6_t1(x6_t1), .x7_t2(x7_t2), .x8_s0_fp(x8_s0),
    .x9_s1(x9_s1), .x10_a0(x10_a0), .x11_a1(x11_a1), .x12_a2(x12_a2), .x13_a3(x13_a3), .x14_a4(x14_a4),
    .x15_a5(x15_a5));
  Button #(.activeLow("true")) button_1 (.out(button_1_out));
  Button #(.activeLow("true")) button_2 (.out(button_2_out));
  not not_4 (not_4_out, MRET);
  Multiplexer multiplexer_7 (.sel(FUNC3[2]), .in_0(RS1_t), .in_1(Imm), .out(multiplexer_7_out));
  PullDown pulldown_1 (.out(CSR_IN));
  and and_8 (and_8_out, not_4_out, PC_IN_MUX);
  D_FF_AS #(.Default(1)) d_ff_as_4 (.Set(CLK), .D(1'b0), .C(PC_IN_MUX), .Clr(1'b0), .Q(d_ff_as_4_q));  // open: nQ
  Counter #(.Bits(32)) counter_1 (.en(1'b1), .C(CLK), .clr(1'b0), .out(Cycles));  // open: ovf
  MIE mie_1 (
    .CLK(CLK), .BUS_CLK(BUS_CLK), .CSR_IN(CSR_OUT), .CSR_IN_LATCH(CSR_IN_LATCH),
    .CSR_OUT_LATCH(CSR_OUT_LATCH), .CSR_ADDR(CSR_Address), .nRESET(nRESET), .CSR_OUT(CSR_IN), .mie(mie),
    .MEI1E(mie_1_mei1e), .MEI2E(mie_1_mei2e), .MEI3E(mie_1_mei3e));
  MIP mip_1 (
    .CLK(CLK), .BUS_CLK(BUS_CLK), .CSR_IN(CSR_OUT), .CSR_IN_LATCH(CSR_IN_LATCH),
    .CSR_OUT_LATCH(CSR_OUT_LATCH), .CSR_ADDR(CSR_Address), .nINT1(nKB_INT), .nINT2(button_1_out),
    .nINT3(button_2_out), .nRESET(nRESET), .CSR_OUT(CSR_IN), .mip(mip), .MEI1P(mip_1_mei1p),
    .MEI2P(mip_1_mei2p), .MEI3P(mip_1_mei3p));
  CSR csr_1 (
    .CLK(BUS_CLK), .INA(multiplexer_7_out), .INB(CSR_IN), .CSR_FUNC(FUNC3[1:0]), .ADDR_IN(Imm),
    .ADDR_LATCH(CSR_ADDR_LATCH), .nRESET(nRESET), .NEW_VAL(CSR_OUT), .ADDR(CSR_Address));
  MEPC mepc_1 (
    .BUS_CLK(BUS_CLK), .PC_IN(PC_OUT_t), .IN_EN(and_8_out), .CSR_IN(CSR_OUT), .CSR_IN_LATCH(CSR_IN_LATCH),
    .CSR_ADDR(CSR_Address), .RESET(RESET), .OUT(MEPC_OUT), .CSR_OUT(CSR_IN), .mepc(mepc));
  MSTATUS mstatus_1 (
    .CLK(CLK), .BUS_CLK(BUS_CLK), .CSR_IN(CSR_OUT), .CSR_IN_LATCH(CSR_IN_LATCH),
    .CSR_OUT_LATCH(CSR_OUT_LATCH), .CSR_ADDR(CSR_Address), .IRQ(PC_IN_MUX), .MRET(MRET),
    .IRQ_LATCH(d_ff_as_4_q), .RESET(RESET), .nRESET(nRESET), .CSR_OUT(CSR_IN), .mstatus(mstatus), .MIE(MIE_t));  // open: MPIE
  Counter #(.Bits(32)) counter_2 (.en(1'b1), .C(OPDONE), .clr(1'b0), .out(Instr_2));  // open: ovf
  or or_5 (or_5_out, CLK, RESET);
  D_FF_AS #(.Default(1)) d_ff_as_5 (.Set(or_5_out), .D(MRET), .C(PC_IN_MUX), .Clr(1'b0), .Q(d_ff_as_5_q));  // open: nQ
  and and_9 (INT1P, mie_1_mei1e, mip_1_mei1p);
  and and_10 (INT2P, mie_1_mei2e, mip_1_mei2p);
  and and_11 (INT3P, mie_1_mei3e, mip_1_mei3p);
  MTVEC mtvec_1 (
    .BUS_CLK(BUS_CLK), .MTVEC_SnP(PC_IN_MUX), .CSR_IN(CSR_OUT), .CSR_IN_LATCH(CSR_IN_LATCH),
    .CSR_ADDR(CSR_Address), .RESET(RESET), .MTVEC_OUT(MTVEC_OUT), .CSR_OUT(CSR_IN), .mtvec(mtvec));
  MSCRATCH mscratch_1 (
    .BUS_CLK(BUS_CLK), .CSR_IN(CSR_OUT), .CSR_IN_LATCH(CSR_IN_LATCH), .CSR_ADDR(CSR_Address), .RESET(RESET),
    .CSR_OUT(CSR_IN), .mscratch(mscratch));
  MCAUSE mcause_1 (
    .BUS_CLK(BUS_CLK), .CSR_IN_LATCH(CSR_IN_LATCH), .CSR_OUT_LATCH(CSR_OUT_LATCH), .CSR_ADDR(CSR_Address),
    .TRAP2(TRAP2), .nIRQ(nIRQ), .INT1P(INT1P), .INT2P(INT2P), .INT3P(INT3P), .IRQ_LATCH(d_ff_as_5_q),
    .nRESET(nRESET), .CSR_OUT(CSR_IN), .mcause(mcause));
  DiodeForward diodeforward_1 (.in(INT1P), .out(WAKEUP));
  DiodeForward diodeforward_2 (.in(INT2P), .out(WAKEUP));
  DiodeForward diodeforward_3 (.in(INT3P), .out(WAKEUP));
  Multiplexer multiplexer_8 (.sel(MRET), .in_0(MTVEC_OUT), .in_1(MEPC_OUT), .out(CSR_PC_OUT));
  PullDown pulldown_2 (.out(WAKEUP));
  nand nand_2 (nIRQ, MIE_t, WAKEUP);

  // Other names for the same wires on the sheet: LEN[1] = BUS_EN; ALU_OUT_t = ADDR_IN; CntCycles[31:0] = Cycles;
  //   CntInstr[31:0] = Instr_2; CSR_ADDR[11:0] = CSR_Address; Da[31:0] = A; DATA_ADDR[0] = rs;
  //   DATA_ADDR_16[15:0] = {DATA_ADDR[15:1], rs}; Db[31:0] = B; Dres[31:0] = Result; Mem_Addr[31:0] = Address;
  //   Mem_Data_R[7:0] = Data_Read; Mem_Data_W[7:0] = Data_Write; OP_IN = MEM_OUT_t; PC_CNT_EN = OP_IMM_LATCH;
  //   IMM_PC_OUT_SnP = out_40; IMM_SnP = out_40; PC_OUT_SnP = out_40; RS2_t = MEM_IN; x1[31:0] = x1_ra;
  //   x2[31:0] = x2_sp; x3[31:0] = x3_gp; x4[31:0] = x4_tp; x5[31:0] = x5_t0; x6[31:0] = x6_t1; x7[31:0] = x7_t2;
  //   x8[31:0] = x8_s0; x9[31:0] = x9_s1; x10[31:0] = x10_a0; x11[31:0] = x11_a1; x12[31:0] = x12_a2;
  //   x13[31:0] = x13_a3; x14[31:0] = x14_a4; x15[31:0] = x15_a5

  // Notes on the sheet:
  //   CLK_RAW: Hz: 4000000
  //   Breakpoint: default 4294967295
  //   Debug
  //   Interrupts
  //   Clock
  //   ALU
  //   Memory
  //   Note: we assume that bus cycles 
  //   always come in groups of at least 8.
  //   Hence we only need to check the
  //   upper two bits of the counter.
  //   contents of sdcard_1 (hex, n*v repeats v):
  //   eb,3c,90,4d,54,4f,4f,34,30,32,33,0,2,1,1,0,2,0,2,c0,f,f0,c,0,3f
  //   ,0,10,11*0,29,c0,97,7d,20,4d,79,4c,61,62,65,6c,4*20,46,41,54,31
  //   ,32,20,20,20,fa,31,c0,8e,d8,8e,c0,fc,b9,0,1,be,0,7c,bf,0,80,f3
  //   ,a5,ea,56,0,0,8,b8,1,2,bb,0,7c,ba,80,0,b9,1,0,cd,13,72,5,ea,0
  //   ,7c,0,0,cd,19,337*0,80,0,1,0,1,f,3f,3,4*0,c0,f,50*0,55,aa,f0,ff,ff,ff
  //   ,4f,0,5,60,0,7,80,0,9,a0,0,b,c0,0,d,e0,0,f,0,1,11,20,1,13,40,1
  //   ,15,60,1,17,80,1,19,a0,1,1b,c0,1,1d,e0,1,1f,0,2,21,20,2,23,40
  //   ,2,25,60,2,27,80,2,29,a0,2,2b,c0,2,2d,e0,2,2f,0,3,31,20,3,33,40
  //   ,3,35,60,3,37,80,3,39,a0,3,3b,c0,3,3d,e0,3,3f,0,4,41,20,4,43,f0
  //   ,ff,6042*0,f0,ff,ff,ff,4f,0,5,60,0,7,80,0,9,a0,0,b,c0,0,d,e0,0
  //   ,f,0,1,11,20,1,13,40,1,15,60,1,17,80,1,19,a0,1,1b,c0,1,1d,e0,1
  //   ,1f,0,2,21,20,2,23,40,2,25,60,2,27,80,2,29,a0,2,2b,c0,2,2d,e0
  //   ,2,2f,0,3,31,20,3,33,40,3,35,60,3,37,80,3,39,a0,3,3b,c0,3,3d,e0
  //   ,3,3f,0,4,41,20,4,43,f0,ff,6042*0,54,45,53,54,4*20,54,58,54,20
  //   ,18,0,a7,ab,4b,55,4b,55,0,0,a7,ab,4b,55,2,0,d,0,0,0,41,4d,0,79
  //   ,0,4c,0,61,0,62,0,f,0,d9,65,0,6c,0,0,0,6*ff,0,0,4*ff,4d,59,4c
  //   ,41,42,45,4c,4*20,8,0,0,5b,b1,4b,55,4b,55,0,0,5b,b1,4b,55,6*0
  //   ,4c,4f,52,45,4d,20,20,20,54,58,54,20,18,0,87,6d,4d,55,4d,55,0,0
  //   ,87,6d,4d,55,3,0,6e,80,16258*0,48,65,6c,6c,6f,20,57,6f,72,6c,64
  //   ,21,a,499*0,4c,6f,72,65,6d,20,69,70,73,75,6d,20,64,6f,6c,6f,72
  //   ,20,73,69,74,20,61,6d,65,74,2c,20,63,6f,6e,73,65,63,74,65,74,75
  //   ,72,20,61,64,69,70,69,73,63,69,6e,67,20,65,6c,69,74,2e,20,4d,6f
  //   ,72,62,69,20,69,6e,20,66,65,75,67,69,61,74,20,6c,69,62,65,72,6f
  //   ,2e,20,4d,61,75,72,69,73,20,65,73,74,20,6a,75,73,74,6f,2c,20,73
  //   ,75,73,63,69,70,69,74,20,73,69,74,20,61,6d,65,74,20,6e,69,73,6c
  //   ,20,73,65,64,2c,20,67,72,61,76,69,64,61,20,63,6f,6e,73,65,71,75
  //   ,61,74,20,6e,69,73,69,2e,20,43,75,72,61,62,69,74,75,72,20,6e,6f
  //   ,6e,20,6d,61,75,72,69,73,20,6a,75,73,74,6f,2e,20,50,65,6c,6c,65
  //   ,6e,74,65,73,71,75,65,20,68,61,62,69,74,61,6e,74,20,6d,6f,72,62
  //   ,69,20,74,72,69,73,74,69,71,75,65,20,73,65,6e,65,63,74,75,73,20
  //   ,65,74,20,6e,65,74,75,73,20,65,74,20,6d,61,6c,65,73,75,61,64,61
  //   ,20,66,61,6d,65,73,20,61,63,20,74,75,72,70,69,73,20,65,67,65,73
  //   ,74,61,73,2e,20,50,65,6c,6c,65,6e,74,65,73,71,75,65,20,73,69,74
  //   ,20,61,6d,65,74,20,76,6f,6c,75,74,70,61,74,20,6a,75,73,74,6f,2e
  //   ,20,49,6e,74,65,67,65,72,20,6e,75,6e,63,20,6d,65,74,75,73,2c,20
  //   ,75,6c,74,72,69,63,69,65,73,20,74,72,69,73,74,69,71,75,65,20,66
  //   ,61,75,63,69,62,75,73,20,61,63,2c,20,66,61,75,63,69,62,75,73,20
  //   ,69,6e,20,6f,72,63,69,2e,20,4e,61,6d,20,68,65,6e,64,72,65,72,69
  //   ,74,20,72,75,74,72,75,6d,20,72,69,73,75,73,2c,20,61,20,66,65,75
  //   ,67,69,61,74,20,73,61,70,69,65,6e,20,61,6c,69,71,75,65,74,20,6e
  //   ,6f,6e,2e,20,50,65,6c,6c,65,6e,74,65,73,71,75,65,20,61,20,64,6f
  //   ,6c,6f,72,20,71,75,61,6d,2e,20,50,72,61,65,73,65,6e,74,20,70,75
  //   ,6c,76,69,6e,61,72,20,61,6e,74,65,20,76,69,76,65,72,72,61,20,74
  //   ,65,6c,6c,75,73,20,63,6f,6e,73,65,71,75,61,74,20,75,6c,74,72,69
  //   ,63,69,65,73,2e,20,50,72,61,65,73,65,6e,74,20,6d,69,20,65,6e,69
  //   ,6d,2c,20,70,6c,61,63,65,72,61,74,20,61,63,20,6c,69,67,75,6c,61
  //   ,20,61,74,2c,20,76,75,6c,70,75,74,61,74,65,20,61,63,63,75,6d,73
  //   ,61,6e,20,6e,69,73,69,2e,20,4d,6f,72,62,69,20,63,6f,6e,76,61,6c,6c
  //   ,69,73,20,75,72,6e,61,20,61,74,20,64,69,61,6d,20,6d,61,6c,65,73
  //   ,75,61,64,61,2c,20,6e,6f,6e,20,63,6f,6d,6d,6f,64,6f,20,61,6e,74
  //   ,65,20,66,65,75,67,69,61,74,2e,20,50,72,61,65,73,65,6e,74,20,65
  //   ,75,20,64,75,69,20,64,75,69,2e,20,4e,75,6e,63,20,64,69,61,6d,20
  //   ,6d,61,75,72,69,73,2c,20,66,65,72,6d,65,6e,74,75,6d,20,73,65,64
  //   ,20,62,6c,61,6e,64,69,74,20,65,75,2c,20,68,65,6e,64,72,65,72,69
  //   ,74,20,76,65,6c,20,64,69,61,6d,2e,20,4d,61,65,63,65,6e,61,73,20
  //   ,61,20,61,72,63,75,20,61,20,6c,6f,72,65,6d,20,66,61,75,63,69,62
  //   ,75,73,20,64,69,63,74,75,6d,20,75,74,20,6e,6f,6e,20,6e,65,71,75
  //   ,65,2e,20,53,75,73,70,65,6e,64,69,73,73,65,20,6d,61,75,72,69,73
  //   ,20,6e,75,6e,63,2c,20,6c,6f,62,6f,72,74,69,73,20,71,75,69,73,20
  //   ,73,6f,6c,6c,69,63,69,74,75,64,69,6e,20,65,74,2c,20,6d,6f,6c,6c
  //   ,69,73,20,73,69,74,20,61,6d,65,74,20,61,6e,74,65,2e,20,4d,61,75
  //   ,72,69,73,20,69,6e,20,6e,75,6c,6c,61,20,6d,61,73,73,61,2e,a,a
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  //   contents of Firmware (hex, n*v repeats v):
  //   b7,5,0,40,31,46,23,80,c5,0,5,46,23,80,c5,0,17,85,0,0,13,5,5,9c
  //   ,81,45,ef,70,b0,a,9,45,b5,45,ef,70,30,10,81,40,1,41,33,87,20,0
  //   ,81,43,b7,4,2,0,89,4,5,4,63,4,77,0,6f,70,10,5,85,40,5,41,33,87
  //   ,20,0,89,43,b7,4,2,0,8d,4,5,4,63,4,77,0,6f,70,70,3,8d,40,1d,41
  //   ,33,87,20,0,a9,43,b7,4,2,0,91,4,5,4,63,4,77,0,6f,70,d0,1,81,40
  //   ,37,81,ff,ff,33,87,20,0,e1,73,b7,4,2,0,95,4,5,4,63,4,77,0,6f,70
  //   ,10,0,b7,0,0,80,1,41,33,87,20,0,b7,3,0,80,b7,4,2,0,99,4,5,4,63
  //   ,4,77,0,6f,70,20,7e,b7,0,0,80,37,81,ff,ff,33,87,20,0,b7,83,ff
  //   ,7f,b7,4,2,0,9d,4,5,4,63,4,77,0,6f,70,20,7c,81,40,37,81,0,0,7d
  //   ,11,33,87,20,0,a1,63,fd,13,b7,4,2,0,a1,4,5,4,63,4,77,0,6f,70,20
  //   ,7a,b7,0,0,80,fd,10,1,41,33,87,20,0,b7,3,0,80,fd,13,b7,4,2,0,a5
  //   ,4,5,4,63,4,77,0,6f,70,0,78,b7,0,0,80,fd,10,37,81,0,0,7d,11,33
  //   ,87,20,0,b7,83,0,80,f9,13,b7,4,2,0,a9,4,5,4,63,4,77,0,6f,70,a0
  //   ,75,b7,0,0,80,37,81,0,0,7d,11,33,87,20,0,b7,83,0,80,fd,13,b7,4
  //   ,2,0,ad,4,5,4,63,4,77,0,6f,70,60,73,b7,0,0,80,fd,10,37,81,ff,ff
  //   ,33,87,20,0,b7,83,ff,7f,fd,13,b7,4,2,0,b1,4,5,4,63,4,77,0,6f,70
  //   ,20,71,81,40,13,1,f0,ff,33,87,20,0,93,3,f0,ff,b7,4,2,0,b5,4,5
  //   ,4,63,4,77,0,6f,70,40,6f,93,0,f0,ff,5,41,33,87,20,0,81,43,b7,4
  //   ,2,0,b9,4,5,4,63,4,77,0,6f,70,80,6d,93,0,f0,ff,13,1,f0,ff,33,87
  //   ,20,0,93,3,e0,ff,b7,4,2,0,bd,4,5,4,63,4,77,0,6f,70,80,6b,85,40
  //   ,37,1,0,80,7d,11,33,87,20,0,b7,3,0,80,b7,4,2,0,c1,4,5,4,63,4,77
  //   ,0,6f,70,80,69,b5,40,2d,41,8a,90,e1,43,b7,4,2,0,c5,4,5,4,63,84
  //   ,70,0,6f,70,0,68,b9,40,2d,41,6,91,e5,43,b7,4,2,0,c9,4,5,4,63,4
  //   ,71,0,6f,70,80,66,b5,40,86,90,e9,43,b7,4,2,0,cd,4,5,4,63,84,70
  //   ,0,6f,70,20,65,1,42,b5,40,2d,41,33,87,20,0,3a,83,5,2,89,42,e3
  //   ,19,52,fe,e1,43,b7,4,2,0,d1,4,5,4,63,4,73,0,6f,70,c0,62,1,42,b9
  //   ,40,2d,41,33,87,20,0,1,0,3a,83,5,2,89,42,e3,18,52,fe,e5,43,b7
  //   ,4,2,0,d5,4,5,4,63,4,73,0,6f,70,40,60,1,42,bd,40,2d,41,33,87,20
  //   ,0,1,0,1,0,3a,83,5,2,89,42,e3,17,52,fe,e9,43,b7,4,2,0,d9,4,5,4
  //   ,63,4,73,0,6f,70,a0,5d,1,42,b5,40,2d,41,33,87,20,0,5,2,89,42,e3
  //   ,1a,52,fe,e1,43,b7,4,2,0,dd,4,5,4,63,4,77,0,6f,70,60,5b,1,42,b9
  //   ,40,2d,41,1,0,33,87,20,0,5,2,89,42,e3,19,52,fe,e5,43,b7,4,2,0
  //   ,e1,4,5,4,63,4,77,0,6f,70,0,59,1,42,bd,40,2d,41,1,0,1,0,33,87
  //   ,20,0,5,2,89,42,e3,18,52,fe,e9,43,b7,4,2,0,e5,4,5,4,63,4,77,0
  //   ,6f,70,80,56,1,42,b5,40,1,0,2d,41,33,87,20,0,5,2,89,42,e3,19,52
  //   ,fe,e1,43,b7,4,2,0,e9,4,5,4,63,4,77,0,6f,70,20,54,1,42,b9,40,1
  //   ,0,2d,41,1,0,33,87,20,0,5,2,89,42,e3,18,52,fe,e5,43,b7,4,2,0,ed
  //   ,4,5,4,63,4,77,0,6f,70,a0,51,1,42,bd,40,1,0,1,0,2d,41,33,87,20
  //   ,0,5,2,89,42,e3,18,52,fe,e9,43,b7,4,2,0,f1,4,5,4,63,4,77,0,6f
  //   ,70,20,4f,1,42,2d,41,b5,40,33,87,20,0,5,2,89,42,e3,1a,52,fe,e1
  //   ,43,b7,4,2,0,f5,4,5,4,63,4,77,0,6f,70,e0,4c,1,42,2d,41,b9,40,1
  //   ,0,33,87,20,0,5,2,89,42,e3,19,52,fe,e5,43,b7,4,2,0,f9,4,5,4,63
  //   ,4,77,0,6f,70,80,4a,1,42,2d,41,bd,40,1,0,1,0,33,87,20,0,5,2,89
  //   ,42,e3,18,52,fe,e9,43,b7,4,2,0,fd,4,5,4,63,4,77,0,6f,70,0,48,1
  //   ,42,2d,41,1,0,b5,40,33,87,20,0,5,2,89,42,e3,19,52,fe,e1,43,b7
  //   ,4,2,0,93,84,4,2,5,4,63,4,77,0,6f,70,80,45,1,42,2d,41,1,0,b9,40
  //   ,1,0,33,87,20,0,5,2,89,42,e3,18,52,fe,e5,43,b7,4,2,0,93,84,14
  //   ,2,5,4,63,4,77,0,6f,70,e0,42,1,42,2d,41,1,0,1,0,bd,40,33,87,20
  //   ,0,5,2,89,42,e3,18,52,fe,e9,43,b7,4,2,0,93,84,24,2,5,4,63,4,77
  //   ,0,6f,70,40,40,bd,40,6,81,bd,43,b7,4,2,0,93,84,34,2,5,4,63,4,71
  //   ,0,6f,70,c0,3e,93,0,0,2,33,81,0,0,93,3,0,2,b7,4,2,0,93,84,44,2
  //   ,5,4,63,4,71,0,6f,70,e0,3c,b3,0,0,0,81,43,b7,4,2,0,93,84,54,2
  //   ,5,4,63,84,70,0,6f,70,60,3b,c1,40,79,41,33,80,20,0,81,43,b7,4
  //   ,2,0,93,84,64,2,5,4,63,4,70,0,6f,70,a0,39,d,45,b5,45,ef,70,a0
  //   ,42,81,40,1,41,33,87,20,40,81,43,b7,4,3,0,89,4,5,4,63,4,77,0,6f
  //   ,70,80,37,85,40,5,41,33,87,20,40,81,43,b7,4,3,0,8d,4,5,4,63,4
  //   ,77,0,6f,70,e0,35,8d,40,1d,41,33,87,20,40,93,3,c0,ff,b7,4,3,0
  //   ,91,4,5,4,63,4,77,0,6f,70,20,34,81,40,37,81,ff,ff,33,87,20,40
  //   ,a1,63,b7,4,3,0,95,4,5,4,63,4,77,0,6f,70,60,32,b7,0,0,80,1,41
  //   ,33,87,20,40,b7,3,0,80,b7,4,3,0,99,4,5,4,63,4,77,0,6f,70,80,30
  //   ,b7,0,0,80,37,81,ff,ff,33,87,20,40,b7,83,0,80,b7,4,3,0,9d,4,5
  //   ,4,63,4,77,0,6f,70,80,2e,81,40,37,81,0,0,7d,11,33,87,20,40,e1
  //   ,73,85,3,b7,4,3,0,a1,4,5,4,63,4,77,0,6f,70,80,2c,b7,0,0,80,fd
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  //   Microcode
  //   Opcode
  //   Muxes
  //   contents of MicroCode (hex, n*v repeats v):
  //   a10e45,4*8a30e47,a30ee5,a30e45,a30c45,4*72a32647,a306c5,a30645
  //   ,a30c6d,a30e4f,a30c4d,a30e4f,a30c4d,a30e4f,a30c4d,a30e4f,a30e44,a30e44
  //   ,40*0,a30e45,a30e05,4*32a32e07,a30e85,a30e05,a30c0d,a30e0f,a30c0d
  //   ,a30e0f,a30c0d,a30e0f,a30c0d,a30e0f,a30e04,a30e04,46*0,a30e45
  //   ,a30e05,4*32a32e07,a30e85,a30e05,a30c0d,a30e0f,a30c0d,a30e0f,a30c0d
  //   ,a30e0f,a30c0d,a30e0f,a30e04,a30e04,46*0,a30e4d,a30c6d,a30e4f
  //   ,a30c4d,a30e4f,a30c4d,a30e4f,a30c4d,a30e4f,a30e44,a30e44,53*0
  //   ,a10c4d,8a3064f,8a3046d,8a3064f,8a3044d,8a3064f,8a3044d,8a3064f
  //   ,a30e44,a30e44,54*0,a10c4d,22a3064f,22a3046d,22a3064f,22a3044d
  //   ,22a3064f,22a3044d,22a3064f,a30e44,a30e44,54*0,a30e45,a30e05,4*32a32e07
  //   ,a30e85,a30e05,a30c0d,a30e0f,a30c0d,a30e0f,a30c0d,a30e0f,a30c0d
  //   ,a30e0f,a30e04,a30e04,46*0,a30e45,a30e05,4*32a32e07,a30e85,a30e05
  //   ,a30c0d,a30e0f,a30c0d,a30e0f,a30c0d,a30e0f,a30c0d,a30e0f,a30e04,a30e04
  //   ,46*0,a10e45,4*10a30e47,a30ee5,32a32e47,32a32a45,32a32e47,32a32e47,32a32e47
  //   ,a30ec5,a30e45,a30c6d,a30e4f,a30c4d,a30e4f,a30c4d,a30e4f,a30c4d
  //   ,a30e4f,a30e44,a30e44,41*0,a30e45,a30e05,4*32a32e07,a30e85,a30e05
  //   ,a30c0d,a30e0f,a30c0d,a30e0f,a30c0d,a30e0f,a30c0d,a30e0f,a30e04,a30e04
  //   ,46*0,a30e45,a30e05,4*32a32e07,a30e85,a30e05,a30c0d,a30e0f,a30c0d
  //   ,a30e0f,a30c0d,a30e0f,a30c0d,a30e0f,a30e04,a30e04,46*0,a30e45
  //   ,a30e05,4*32a32e07,a30e85,a30e05,a30c0d,a30e0f,a30c0d,a30e0f,a30c0d
  //   ,a30e0f,a30c0d,a30e0f,a30e04,a30e04,46*0,a10c4d,a3064f,a3046d
  //   ,a3064f,a3044d,a3064f,a3044d,a3064f,a30e44,a30e44,54*0,a10c4d
  //   ,24a3064f,24a3046d,24a3064f,24a3044d,24a3064f,24a3044d,24a3064f
  //   ,a30e44,a30e44,54*0,a30e45,a30e05,4*32a32e07,a30e85,a30e05,a30c0d
  //   ,a30e0f,a30c0d,a30e0f,a30c0d,a30e0f,a30c0d,a30e0f,a30e04,a30e04
  //   ,46*0,a30e45,a30e05,4*32a32e07,a30e85,a30e05,a30c0d,a30e0f,a30c0d
  //   ,a30e0f,a30c0d,a30e0f,a30c0d,a30e0f,a30e04,a30e04,46*0,a30e45
  //   ,a30e05,4*32a32e07,a30e85,a30e05,a30c0d,a30e0f,a30c0d,a30e0f,a30c0d
  //   ,a30e0f,a30c0d,a30e0f,a30e04,a30e04,46*0,a30e45,a30e05,4*32a32e07
  //   ,a30e85,a30e05,a30c0d,a30e0f,a30c0d,a30e0f,a30c0d,a30e0f,a30c0d
  //   ,a30e0f,a30e04,a30e04,46*0,a30e45,a30e05,4*32a32e07,a30e85,a30e05
  //   ,a30c0d,a30e0f,a30c0d,a30e0f,a30c0d,a30e0f,a30c0d,a30e0f,a30e04,a30e04
  //   ,46*0,a30e45,a30e05,4*32a32e07,a30e85,a30e05,a30c0d,a30e0f,a30c0d
  //   ,a30e0f,a30c0d,a30e0f,a30c0d,a30e0f,a30e04,a30e04,46*0,a30e45
  //   ,a30e05,4*32a32e07,a30e85,a30e05,a30c0d,a30e0f,a30c0d,a30e0f,a30c0d
  //   ,a30e0f,a30c0d,a30e0f,a30e04,a30e04,46*0,a30e45,a30e05,4*32a32e07
  //   ,a30e85,a30e05,a30c0d,a30e0f,a30c0d,a30e0f,a30c0d,a30e0f,a30c0d
  //   ,a30e0f,a30e04,a30e04,46*0,a30e45,a30e05,4*32a32e07,a30e85,a30e05
  //   ,a30c0d,a30e0f,a30c0d,a30e0f,a30c0d,a30e0f,a30c0d,a30e0f,a30e04,a30e04
  //   ,46*0,a30e45,a30e05,4*32a32e07,a30e85,a30e05,a30c0d,a30e0f,a30c0d
  //   ,a30e0f,a30c0d,a30e0f,a30c0d,a30e0f,a30e04,a30e04,46*0,a11e45
  //   ,4*a25e47,a30e45,a30c6d,a30e4f,a30c4d,a30e4f,a30c4d,a30e4f,a30c4d
  //   ,a30e4f,a30e44,a30e44,48*0,a10e45,4*8a30e47,a10ee5,a10e55,a10c4d
  //   ,32a3264f,32a3244d,32a3264f,32a3244d,32a3264f,32a3244d,32a3264f
  //   ,a30e64,a30e64,47*0,a30e45,a30e05,4*32a32e07,a30e85,a30e05,a30c0d
  //   ,a30e0f,a30c0d,a30e0f,a30c0d,a30e0f,a30c0d,a30e0f,a30e04,a30e04
  //   ,46*0,a10e45,4*2aa30e47,a10ee5,a10e55,a10c4d,32a3264f,32a3244d
  //   ,32a3264f,32a3244d,32a3264f,32a3244d,32a3264f,a30e64,a30e64,47*0
  //   ,a30e45,4*1a30e47,a30e55,a30e65,4*32a32e47,a30ec5,a30e45,a30c4d
  //   ,a30e4f,a30c4d,a30e4f,a30c4d,a30e4f,a30c4d,a30e4f,a30e44,a30e44
  //   ,41*0,a30e45,a30e05,4*32a32e07,a30e85,a30e05,a30c0d,a30e0f,a30c0d
  //   ,a30e0f,a30c0d,a30e0f,a30c0d,a30e0f,a30e04,a30e04,46*0,a30e45
  //   ,a30e05,4*32a32e07,a30e85,a30e05,a30c0d,a30e0f,a30c0d,a30e0f,a30c0d
  //   ,a30e0f,a30c0d,a30e0f,a30e04,a30e04,46*0,a30e45,a30e05,4*32a32e07
  //   ,a30e85,a30e05,a30c0d,a30e0f,a30c0d,a30e0f,a30c0d,a30e0f,a30c0d
  //   ,a30e0f,a30e04,a30e04,46*0,a10e45,4*8a30e47,a30ee5,a30e45,a30c45
  //   ,72a32647,72a32445,72a32647,72a32647,72a32647,a306c5,a30645,a30c6d
  //   ,a30e4f,a30c4d,a30e4f,a30c4d,a30e4f,a30c4d,a30e4f,a30e44,a30e44
  //   ,39*0,a30e45,a30e05,4*32a32e07,a30e85,a30e05,a30c0d,a30e0f,a30c0d
  //   ,a30e0f,a30c0d,a30e0f,a30c0d,a30e0f,a30e04,a30e04,46*0,a30e45
  //   ,a30e05,4*32a32e07,a30e85,a30e05,a30c0d,a30e0f,a30c0d,a30e0f,a30c0d
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  //   PC
  //   Registers
  //   CSR
endmodule
