// Digital circuit CSR-address.dig as structural Verilog
module CSR_address (
  input  CLK,
  input  IN,
  input  LATCH,
  input  nRESET,
  output [11:0] OUT
);

  wire _74hc595_2_qh_2, hef4557b_1_q;

  _74HC595 _74hc595_1 (
    .SER(_74hc595_2_qh_2), .SRCLK(CLK), .nSRCLR(nRESET), .RCLK(LATCH), .nOE(1'b0), .VCC(1'b1), .GND(1'b0),
    .QH(OUT[0]), .QG(OUT[1]), .QF(OUT[2]), .QE(OUT[3]), .QD(OUT[4]), .QC(OUT[5]), .QB(OUT[6]), .QA(OUT[7]));  // open: QH_2
  _74HC595 _74hc595_2 (
    .SER(hef4557b_1_q), .SRCLK(CLK), .nSRCLR(nRESET), .RCLK(LATCH), .nOE(1'b0), .VCC(1'b1), .GND(1'b0),
    .QH(OUT[8]), .QG(OUT[9]), .QF(OUT[10]), .QE(OUT[11]), .QH_2(_74hc595_2_qh_2));  // open: QD, QC, QB, QA
  HEF4557B hef4557b_1 (
    .DA(IN), .DB(1'b0), .A_nB(1'b1), .nCP1(1'b0), .CP0(CLK), .MR(1'b0), .L32(1'b0), .L16(1'b0), .L8(1'b1),
    .L4(1'b1), .L2(1'b1), .L1(1'b1), .VCC(1'b1), .GND(1'b0), .Q(hef4557b_1_q));  // open: nQ
endmodule
