// Digital circuit CSR-counter.dig as structural Verilog
module CSR_counter (
  input  CLK,
  input  CNT_CLK,
  input  LATCH,
  input  SnP,
  input  nRESET,
  output OUT_LOW,
  output OUT_HI,
  output [63:0] VAL
);

  wire _74hc597_2_q7, _74hc597_3_q7, _74hc597_4_q7, _74hc597_6_q7, _74hc597_7_q7, _74hc597_8_q7,
       _74161_1_p12, _74161_1_p13, _74161_1_p14, _74161_1_p15, _74161_1_p16, _74161_2_p12, _74161_2_p13,
       _74161_2_p14, _74161_2_p15, _74161_2_p16, _74161_3_p12, _74161_3_p13, _74161_3_p14, _74161_3_p15,
       _74161_3_p16, _74161_4_p12, _74161_4_p13, _74161_4_p14, _74161_4_p15, _74161_4_p16, _74161_5_p12,
       _74161_5_p13, _74161_5_p14, _74161_5_p15, _74161_5_p16, _74161_6_p12, _74161_6_p13, _74161_6_p14,
       _74161_6_p15, _74161_6_p16, _74161_7_p12, _74161_7_p13, _74161_7_p14, _74161_7_p15, _74161_7_p16,
       _74161_8_p12, _74161_8_p13, _74161_8_p14, _74161_8_p15, _74161_8_p16, _74161_9_p12, _74161_9_p13,
       _74161_9_p14, _74161_9_p15, _74161_9_p16, _74161_10_p12, _74161_10_p13, _74161_10_p14, _74161_10_p15,
       _74161_10_p16, _74161_11_p12, _74161_11_p13, _74161_11_p14, _74161_11_p15, _74161_11_p16,
       _74161_12_p12, _74161_12_p13, _74161_12_p14, _74161_12_p15, _74161_12_p16, _74161_13_p12,
       _74161_13_p13, _74161_13_p14, _74161_13_p15, _74161_13_p16, _74161_14_p12, _74161_14_p13,
       _74161_14_p14, _74161_14_p15, _74161_14_p16, _74161_15_p12, _74161_15_p13, _74161_15_p14,
       _74161_15_p15, _74161_15_p16, _74161_16_p12, _74161_16_p13, _74161_16_p14, _74161_16_p15;

  // _74161 _74161_1: pin names not known; wires that end beside it: 1'b1, nRESET, CNT_CLK, 1'b1, 1'b1, 1'b0, 1'b0, 1'b0, 1'b0, 1'b1, 1'b0, _74161_1_p12, _74161_1_p13, _74161_1_p14, _74161_1_p15, _74161_1_p16
  // _74161 _74161_2: pin names not known; wires that end beside it: 1'b1, nRESET, CNT_CLK, _74161_1_p12, 1'b1, 1'b0, 1'b0, 1'b0, 1'b0, 1'b1, 1'b0, _74161_2_p12, _74161_2_p13, _74161_2_p14, _74161_2_p15, _74161_2_p16
  // _74161 _74161_3: pin names not known; wires that end beside it: 1'b1, nRESET, CNT_CLK, _74161_2_p12, 1'b1, 1'b0, 1'b0, 1'b0, 1'b0, 1'b1, 1'b0, _74161_3_p12, _74161_3_p13, _74161_3_p14, _74161_3_p15, _74161_3_p16
  // _74161 _74161_4: pin names not known; wires that end beside it: 1'b1, nRESET, CNT_CLK, _74161_3_p12, 1'b1, 1'b0, 1'b0, 1'b0, 1'b0, 1'b1, 1'b0, _74161_4_p12, _74161_4_p13, _74161_4_p14, _74161_4_p15, _74161_4_p16
  // _74161 _74161_5: pin names not known; wires that end beside it: 1'b1, nRESET, CNT_CLK, _74161_4_p12, 1'b1, 1'b0, 1'b0, 1'b0, 1'b0, 1'b1, 1'b0, _74161_5_p12, _74161_5_p13, _74161_5_p14, _74161_5_p15, _74161_5_p16
  // _74161 _74161_6: pin names not known; wires that end beside it: 1'b1, nRESET, CNT_CLK, _74161_5_p12, 1'b1, 1'b0, 1'b0, 1'b0, 1'b0, 1'b1, 1'b0, _74161_6_p12, _74161_6_p13, _74161_6_p14, _74161_6_p15, _74161_6_p16
  // _74161 _74161_7: pin names not known; wires that end beside it: 1'b1, nRESET, CNT_CLK, _74161_6_p12, 1'b1, 1'b0, 1'b0, 1'b0, 1'b0, 1'b1, 1'b0, _74161_7_p12, _74161_7_p13, _74161_7_p14, _74161_7_p15, _74161_7_p16
  // _74161 _74161_8: pin names not known; wires that end beside it: 1'b1, nRESET, CNT_CLK, _74161_7_p12, 1'b1, 1'b0, 1'b0, 1'b0, 1'b0, 1'b1, 1'b0, _74161_8_p12, _74161_8_p13, _74161_8_p14, _74161_8_p15, _74161_8_p16
  _74HC597 _74hc597_1 (
    .nMR(nRESET), .SHCP(CLK), .DS(_74hc597_2_q7), .STCP(LATCH), .nPL(SnP), .D7(_74161_1_p13),
    .D6(_74161_1_p14), .D5(_74161_1_p15), .D4(_74161_1_p16), .D3(_74161_2_p13), .D2(_74161_2_p14),
    .D1(_74161_2_p15), .D0(_74161_2_p16), .Q7(OUT_LOW), .Val(VAL[7:0]));
  _74HC597 _74hc597_2 (
    .nMR(nRESET), .SHCP(CLK), .DS(_74hc597_3_q7), .STCP(LATCH), .nPL(SnP), .D7(_74161_3_p13),
    .D6(_74161_3_p14), .D5(_74161_3_p15), .D4(_74161_3_p16), .D3(_74161_4_p13), .D2(_74161_4_p14),
    .D1(_74161_4_p15), .D0(_74161_4_p16), .Q7(_74hc597_2_q7), .Val(VAL[15:8]));
  _74HC597 _74hc597_3 (
    .nMR(nRESET), .SHCP(CLK), .DS(_74hc597_4_q7), .STCP(LATCH), .nPL(SnP), .D7(_74161_5_p13),
    .D6(_74161_5_p14), .D5(_74161_5_p15), .D4(_74161_5_p16), .D3(_74161_6_p13), .D2(_74161_6_p14),
    .D1(_74161_6_p15), .D0(_74161_6_p16), .Q7(_74hc597_3_q7), .Val(VAL[23:16]));
  _74HC597 _74hc597_4 (
    .nMR(nRESET), .SHCP(CLK), .DS(1'b0), .STCP(LATCH), .nPL(SnP), .D7(_74161_7_p13), .D6(_74161_7_p14),
    .D5(_74161_7_p15), .D4(_74161_7_p16), .D3(_74161_8_p13), .D2(_74161_8_p14), .D1(_74161_8_p15),
    .D0(_74161_8_p16), .Q7(_74hc597_4_q7), .Val(VAL[31:24]));
  // _74161 _74161_9: pin names not known; wires that end beside it: 1'b1, nRESET, CNT_CLK, _74161_8_p12, 1'b1, 1'b0, 1'b0, 1'b0, 1'b0, 1'b1, 1'b0, _74161_9_p12, _74161_9_p13, _74161_9_p14, _74161_9_p15, _74161_9_p16
  // _74161 _74161_10: pin names not known; wires that end beside it: 1'b1, nRESET, CNT_CLK, _74161_9_p12, 1'b1, 1'b0, 1'b0, 1'b0, 1'b0, 1'b1, 1'b0, _74161_10_p12, _74161_10_p13, _74161_10_p14, _74161_10_p15, _74161_10_p16
  // _74161 _74161_11: pin names not known; wires that end beside it: 1'b1, nRESET, CNT_CLK, _74161_10_p12, 1'b1, 1'b0, 1'b0, 1'b0, 1'b0, 1'b1, 1'b0, _74161_11_p12, _74161_11_p13, _74161_11_p14, _74161_11_p15, _74161_11_p16
  // _74161 _74161_12: pin names not known; wires that end beside it: 1'b1, nRESET, CNT_CLK, _74161_11_p12, 1'b1, 1'b0, 1'b0, 1'b0, 1'b0, 1'b1, 1'b0, _74161_12_p12, _74161_12_p13, _74161_12_p14, _74161_12_p15, _74161_12_p16
  // _74161 _74161_13: pin names not known; wires that end beside it: 1'b1, nRESET, CNT_CLK, _74161_12_p12, 1'b1, 1'b0, 1'b0, 1'b0, 1'b0, 1'b1, 1'b0, _74161_13_p12, _74161_13_p13, _74161_13_p14, _74161_13_p15, _74161_13_p16
  // _74161 _74161_14: pin names not known; wires that end beside it: 1'b1, nRESET, CNT_CLK, _74161_13_p12, 1'b1, 1'b0, 1'b0, 1'b0, 1'b0, 1'b1, 1'b0, _74161_14_p12, _74161_14_p13, _74161_14_p14, _74161_14_p15, _74161_14_p16
  // _74161 _74161_15: pin names not known; wires that end beside it: 1'b1, nRESET, CNT_CLK, _74161_14_p12, 1'b1, 1'b0, 1'b0, 1'b0, 1'b0, 1'b1, 1'b0, _74161_15_p12, _74161_15_p13, _74161_15_p14, _74161_15_p15, _74161_15_p16
  // _74161 _74161_16: pin names not known; wires that end beside it: 1'b1, nRESET, CNT_CLK, _74161_15_p12, 1'b1, 1'b0, 1'b0, 1'b0, 1'b0, 1'b1, 1'b0, _74161_16_p12, _74161_16_p13, _74161_16_p14, _74161_16_p15
  _74HC597 _74hc597_5 (
    .nMR(nRESET), .SHCP(CLK), .DS(_74hc597_6_q7), .STCP(LATCH), .nPL(SnP), .D7(_74161_9_p13),
    .D6(_74161_9_p14), .D5(_74161_9_p15), .D4(_74161_9_p16), .D3(_74161_10_p13), .D2(_74161_10_p14),
    .D1(_74161_10_p15), .D0(_74161_10_p16), .Q7(OUT_HI), .Val(VAL[39:32]));
  _74HC597 _74hc597_6 (
    .nMR(nRESET), .SHCP(CLK), .DS(_74hc597_7_q7), .STCP(LATCH), .nPL(SnP), .D7(_74161_11_p13),
    .D6(_74161_11_p14), .D5(_74161_11_p15), .D4(_74161_11_p16), .D3(_74161_12_p13), .D2(_74161_12_p14),
    .D1(_74161_12_p15), .D0(_74161_12_p16), .Q7(_74hc597_6_q7), .Val(VAL[47:40]));
  _74HC597 _74hc597_7 (
    .nMR(nRESET), .SHCP(CLK), .DS(_74hc597_8_q7), .STCP(LATCH), .nPL(SnP), .D7(_74161_13_p13),
    .D6(_74161_13_p14), .D5(_74161_13_p15), .D4(_74161_13_p16), .D3(_74161_14_p13), .D2(_74161_14_p14),
    .D1(_74161_14_p15), .D0(_74161_14_p16), .Q7(_74hc597_7_q7), .Val(VAL[55:48]));
  _74HC597 _74hc597_8 (
    .nMR(nRESET), .SHCP(CLK), .DS(1'b0), .STCP(LATCH), .nPL(SnP), .D7(_74161_15_p13), .D6(_74161_15_p14),
    .D5(_74161_15_p15), .D4(_74161_15_p16), .D3(_74161_16_p12), .D2(_74161_16_p13), .D1(_74161_16_p14),
    .D0(_74161_16_p15), .Q7(_74hc597_8_q7), .Val(VAL[63:56]));

  // Other names for the same wires on the sheet: VAL00[7:0] = VAL[7:0]; VAL08[7:0] = VAL[15:8];
  //   VAL10[7:0] = VAL[23:16]; VAL18[7:0] = VAL[31:24]; VAL20[7:0] = VAL[39:32]; VAL28[7:0] = VAL[47:40];
  //   VAL30[7:0] = VAL[55:48]; VAL38[7:0] = VAL[63:56]

  // Notes on the sheet:
  //   CLK: Hz: 2147483647
endmodule
