// Digital circuit CSR.dig as structural Verilog
module CSR (
  input  CLK,
  input  INA,
  input  INB,
  input  [1:0] CSR_FUNC,
  input  ADDR_IN,
  input  ADDR_LATCH,
  input  nRESET,
  output NEW_VAL,
  output [11:0] ADDR
);

  wire and_1_out, multiplexer_2_out, not_1_out, or_1_out;

  CSR_address csr_address_1 (.CLK(CLK), .IN(ADDR_IN), .LATCH(ADDR_LATCH), .nRESET(nRESET), .OUT(ADDR));
  not not_1 (not_1_out, INA);
  or or_1 (or_1_out, INA, INB);
  and and_1 (and_1_out, not_1_out, INB);
  Multiplexer multiplexer_1 (.sel(CSR_FUNC[1]), .in_0(INA), .in_1(multiplexer_2_out), .out(NEW_VAL));
  Multiplexer multiplexer_2 (.sel(CSR_FUNC[0]), .in_0(or_1_out), .in_1(and_1_out), .out(multiplexer_2_out));

  // Other names for the same wires on the sheet: CSR_ADDR[11:0] = ADDR
endmodule
