// Digital circuit Clock.dig as structural Verilog
module Clock (
  input  CLK,
  input  nCLK,
  input  nLEN4,
  input  LASTSTEP,
  input  SUBSTEP_EN,
  input  nRESET,
  output [5:0] STEP,
  output LASTSUBSTEP,
  output nSTEPDONE,
  output [7:0] SUBSTEP,
  output nOPDONE
);

  wire and_1_out, not_1_out, substep_counter_1_step_done, switchdt_1_p3;

  not not_1 (not_1_out, CLK);
  // SwitchDT switchdt_1: pin names not known; wires that end beside it: nCLK, not_1_out, switchdt_1_p3
  Substep_Counter substep_counter_1 (
    .nCLK(switchdt_1_p3), .CLK(CLK), .LEN4(nLEN4), .EN(SUBSTEP_EN), .nRESET(nRESET),
    .LAST_SUBSTEP(LASTSUBSTEP), .nSTEP_DONE(nSTEPDONE), .DVAL(SUBSTEP),
    .STEP_DONE(substep_counter_1_step_done));
  Step_Counter step_counter_1 (
    .nCLK(switchdt_1_p3), .nRESET(nRESET), .EN(substep_counter_1_step_done), .nOPDONE(nOPDONE), .COUNT(STEP));
  and and_1 (and_1_out, LASTSUBSTEP, LASTSTEP);
  D_FF d_ff_1 (.D(and_1_out), .C(CLK), .nQ(nOPDONE));  // open: Q

  // Notes on the sheet:
  //   LASTSTEP: default 1
endmodule

/* Test case:
CLK ~CLK SUBSTEP-EN ~RESET ~LEN4 LASTSTEP STEP SUBSTEP LASTSUBSTEP ~STEPDONE ~OPDONE

1 0 1 0 1 0 X X X X X
1 0 1 1 1 0 X X X X X
0 1 1 1 0 0 0 1 0 X 1
1 0 1 1 0 0 0 1 0 1 1
0 1 1 1 0 0 0 2 0 1 1
1 0 1 1 0 0 0 2 0 1 1
0 1 1 1 0 0 0 3 0 1 1
1 0 1 1 0 0 0 3 0 1 1
0 1 1 1 0 0 0 4 1 1 1
1 0 1 1 0 0 0 4 1 0 1
0 1 1 1 0 0 1 1 0 0 1
1 0 1 1 0 0 1 1 0 1 1
0 1 1 1 0 0 1 2 0 1 1
1 0 1 1 0 0 1 2 0 1 1
0 1 1 1 0 0 1 3 0 1 1
1 0 1 1 0 0 1 3 0 1 1
0 1 1 1 0 0 1 4 1 1 1
1 0 1 1 0 0 1 4 1 0 1
0 1 1 1 0 0 2 1 0 0 1
1 0 1 1 0 0 2 1 0 1 1
0 1 1 1 0 0 2 2 0 1 1
1 0 1 1 0 0 2 2 0 1 1
0 1 1 1 0 0 2 3 0 1 1
1 0 1 1 0 0 2 3 0 1 1
0 1 1 1 0 0 2 4 1 1 1
1 0 1 1 0 0 2 4 1 0 1
0 1 1 1 0 0 3 1 0 0 1
1 0 1 1 0 0 3 1 0 1 1
0 1 1 1 0 0 3 2 0 1 1
1 0 1 1 0 0 3 2 0 1 1
0 1 1 1 0 0 3 3 0 1 1
1 0 1 1 0 0 3 3 0 1 1
0 1 1 1 0 0 3 4 1 1 1
1 0 1 1 0 0 3 4 1 0 1
0 1 1 1 0 0 4 1 0 0 1
1 0 1 1 0 0 4 1 0 1 1
0 1 1 1 0 0 4 2 0 1 1
1 0 1 1 0 0 4 2 0 1 1
0 1 1 1 0 0 4 3 0 1 1
1 0 1 1 0 0 4 3 0 1 1
0 1 1 1 0 0 4 4 1 1 1
1 0 1 1 0 0 4 4 1 0 1
0 1 1 1 0 0 5 1 0 0 1
1 0 1 1 0 0 5 1 0 1 1
0 1 1 1 0 0 5 2 0 1 1
1 0 1 1 0 0 5 2 0 1 1
0 1 1 1 0 0 5 3 0 1 1
1 0 1 1 0 0 5 3 0 1 1
0 1 1 1 0 0 5 4 1 1 1
1 0 1 1 0 0 5 4 1 0 1
0 1 1 1 0 0 6 1 0 0 1
1 0 1 1 0 0 6 1 0 1 1
0 1 1 1 0 0 6 2 0 1 1
1 0 1 1 0 0 6 2 0 1 1
0 1 1 1 0 0 6 3 0 1 1
1 0 1 1 0 0 6 3 0 1 1
0 1 1 1 0 0 6 4 1 1 1
1 0 1 1 0 0 6 4 1 0 1
0 1 1 1 0 0 7 1 0 0 1
1 0 1 1 0 0 7 1 0 1 1
0 1 1 1 0 0 7 2 0 1 1
1 0 1 1 0 0 7 2 0 1 1
0 1 1 1 0 0 7 3 0 1 1
1 0 1 1 0 0 7 3 0 1 1
0 1 1 1 0 0 7 4 1 1 1
1 0 1 1 0 0 7 4 1 0 1
0 1 1 1 1 0 8 1 1 0 1
1 0 1 1 1 0 8 1 1 0 1
0 1 1 1 1 0 9 1 1 0 1
1 0 1 1 1 0 9 1 1 0 1
0 1 1 1 1 0 10 1 1 0 1
1 0 1 1 1 0 10 1 1 0 1
0 1 1 1 0 0 11 1 0 0 1
1 0 1 1 0 0 11 1 0 1 1
0 1 1 1 0 0 11 2 0 1 1
1 0 1 1 0 0 11 2 0 1 1
0 1 1 1 0 0 11 3 0 1 1
1 0 1 1 0 0 11 3 0 1 1
0 1 1 1 0 0 11 4 1 1 1
1 0 1 1 0 0 11 4 1 0 1
0 1 1 1 0 0 12 1 0 0 1
1 0 1 1 0 0 12 1 0 1 1
0 1 1 1 0 0 12 2 0 1 1
1 0 1 1 0 0 12 2 0 1 1
0 1 1 1 0 0 12 3 0 1 1
1 0 1 1 0 0 12 3 0 1 1
0 1 1 1 0 0 12 4 1 1 1
1 0 1 1 0 0 12 4 1 0 1
0 1 1 1 1 0 13 1 1 0 1
1 0 1 1 1 0 13 1 1 0 1
0 1 1 1 0 0 14 1 0 0 1
1 0 1 1 0 0 14 1 0 1 1
0 1 1 1 0 0 14 2 0 1 1
1 0 1 1 0 0 14 2 0 1 1
0 1 1 1 0 0 14 3 0 1 1
1 0 1 1 0 0 14 3 0 1 1
0 1 1 1 0 0 14 4 1 1 1
1 0 1 1 0 0 14 4 1 0 1
0 1 1 1 0 0 15 1 0 0 1
1 0 1 1 0 0 15 1 0 1 1
0 1 1 1 0 0 15 2 0 1 1
1 0 1 1 0 0 15 2 0 1 1
0 1 1 1 0 0 15 3 0 1 1
1 0 1 1 0 0 15 3 0 1 1
0 1 1 1 0 0 15 4 1 1 1
1 0 1 1 0 0 15 4 1 0 1
0 1 1 1 1 0 16 1 1 0 1
1 0 1 1 1 0 16 1 1 0 1
0 1 1 1 0 0 17 1 0 0 1
1 0 1 1 0 0 17 1 0 1 1
0 1 1 1 0 0 17 2 0 1 1
1 0 1 1 0 0 17 2 0 1 1
0 1 1 1 0 0 17 3 0 1 1
1 0 1 1 0 0 17 3 0 1 1
0 1 1 1 0 0 17 4 1 1 1
1 0 1 1 0 0 17 4 1 0 1
0 1 1 1 0 0 18 1 0 0 1
1 0 1 1 0 0 18 1 0 1 1
0 1 1 1 0 0 18 2 0 1 1
1 0 1 1 0 0 18 2 0 1 1
0 1 1 1 0 0 18 3 0 1 1
1 0 1 1 0 0 18 3 0 1 1
0 1 1 1 0 0 18 4 1 1 1
1 0 1 1 0 0 18 4 1 0 1
0 1 1 1 1 0 19 1 1 0 1
1 0 1 1 1 0 19 1 1 0 1
0 1 1 1 0 0 20 1 0 0 1
1 0 1 1 0 0 20 1 0 1 1
0 1 1 1 0 0 20 2 0 1 1
1 0 1 1 0 0 20 2 0 1 1
0 1 1 1 0 0 20 3 0 1 1
1 0 1 1 0 0 20 3 0 1 1
0 1 1 1 0 0 20 4 1 1 1
1 0 1 1 0 0 20 4 1 0 1
0 1 1 1 0 0 21 1 0 0 1
1 0 1 1 0 0 21 1 0 1 1
0 1 1 1 0 0 21 2 0 1 1
1 0 1 1 0 0 21 2 0 1 1
0 1 1 1 0 0 21 3 0 1 1
1 0 1 1 0 0 21 3 0 1 1
0 1 1 1 0 0 21 4 1 1 1
1 0 1 1 0 0 21 4 1 0 1
0 1 1 1 1 0 22 1 1 0 1
1 0 1 1 1 0 22 1 1 0 1
0 1 1 1 1 0 23 1 1 0 1
1 0 1 1 1 0 23 1 1 0 1
0 1 1 1 0 0 24 1 0 0 1
1 0 1 1 0 0 24 1 0 1 1
0 1 1 1 0 0 24 2 0 1 1
1 0 1 1 0 0 24 2 0 1 1
0 1 1 1 0 0 24 3 0 1 1
1 0 1 1 0 0 24 3 0 1 1
0 1 1 1 0 0 24 4 1 1 1
1 0 1 1 0 0 24 4 1 0 1
0 1 1 1 0 0 25 1 0 0 1
1 0 1 1 0 0 25 1 0 1 1
0 1 1 1 0 0 25 2 0 1 1
1 0 1 1 0 0 25 2 0 1 1
0 1 1 1 0 0 25 3 0 1 1
1 0 1 1 0 0 25 3 0 1 1
0 1 1 1 0 0 25 4 1 1 1
1 0 1 1 0 0 25 4 1 0 1
0 1 1 1 0 0 26 1 0 0 1
1 0 1 1 0 0 26 1 0 1 1
0 1 1 1 0 0 26 2 0 1 1
1 0 1 1 0 0 26 2 0 1 1
0 1 1 1 0 0 26 3 0 1 1
1 0 1 1 0 0 26 3 0 1 1
0 1 1 1 0 0 26 4 1 1 1
1 0 1 1 0 0 26 4 1 0 1
0 1 1 1 0 0 27 1 0 0 1
1 0 1 1 0 0 27 1 0 1 1
0 1 1 1 0 0 27 2 0 1 1
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*/
