// Digital circuit DebugShift32.dig as structural Verilog
module DebugShift32 (
  input  CLK,
  input  D,
  input  nEN,
  output [31:0] Val
);

  wire debugshift8_1_q, debugshift8_2_q, debugshift8_3_q;

  DebugShift8 debugshift8_1 (.CLK(CLK), .D(D), .nEN(nEN), .Q(debugshift8_1_q), .Val(Val[31:24]));
  DebugShift8 debugshift8_2 (.CLK(CLK), .D(debugshift8_1_q), .nEN(nEN), .Q(debugshift8_2_q), .Val(Val[23:16]));
  DebugShift8 debugshift8_3 (.CLK(CLK), .D(debugshift8_2_q), .nEN(nEN), .Q(debugshift8_3_q), .Val(Val[15:8]));
  DebugShift8 debugshift8_4 (.CLK(CLK), .D(debugshift8_3_q), .nEN(nEN), .Val(Val[7:0]));  // open: Q
endmodule
