// Digital circuit DebugShift8.dig as structural Verilog
module DebugShift8 (
  input  CLK,
  input  D,
  input  nEN,
  output Q,
  output [7:0] Val
);

  FF_D_En ff_d_en_1 (.CLK(CLK), .D(D), .nEN(nEN), .Q(Val[7]));
  FF_D_En ff_d_en_2 (.CLK(CLK), .D(Val[7]), .nEN(nEN), .Q(Val[6]));
  FF_D_En ff_d_en_3 (.CLK(CLK), .D(Val[6]), .nEN(nEN), .Q(Val[5]));
  FF_D_En ff_d_en_4 (.CLK(CLK), .D(Val[5]), .nEN(nEN), .Q(Val[4]));
  FF_D_En ff_d_en_5 (.CLK(CLK), .D(Val[4]), .nEN(nEN), .Q(Val[3]));
  FF_D_En ff_d_en_6 (.CLK(CLK), .D(Val[3]), .nEN(nEN), .Q(Val[2]));
  FF_D_En ff_d_en_7 (.CLK(CLK), .D(Val[2]), .nEN(nEN), .Q(Val[1]));
  FF_D_En ff_d_en_8 (.CLK(CLK), .D(Val[1]), .nEN(nEN), .Q(Q));

  assign Val[0] = Q;
endmodule
