// Digital circuit FF-D-En.dig as structural Verilog
module FF_D_En (
  input  CLK,
  input  D,
  input  nEN,
  output Q
);

  wire and_1_out, nor_1_out;

  and and_1 (and_1_out, D, ~nEN);  // And
  nor nor_1 (nor_1_out, D, nEN);
  JK_FF jk_ff_1 (.J(and_1_out), .C(CLK), .K(nor_1_out), .Q(Q));  // open: nQ
endmodule
