// Digital circuit FF1.dig as structural Verilog
module FF1 (
  input  D,
  input  C,
  input  Clr,
  output Q,
  output nQ
);

  D_FF_AS d_ff_as_1 (.Set(1'b0), .D(D), .C(C), .Clr(Clr), .Q(Q), .nQ(nQ));
endmodule
