// Digital circuit FF16.dig as structural Verilog
module FF16 (
  input  D,
  input  C,
  input  Clr,
  output Q,
  output nQ
);

  wire d_ff_as_1_q, d_ff_as_2_q, d_ff_as_3_q, d_ff_as_4_q, d_ff_as_5_q, d_ff_as_6_q, d_ff_as_7_q,
       d_ff_as_8_q, d_ff_as_9_q, d_ff_as_10_q, d_ff_as_11_q, d_ff_as_12_q, d_ff_as_13_q, d_ff_as_14_q,
       d_ff_as_15_q;

  D_FF_AS d_ff_as_1 (.Set(1'b0), .D(D), .C(C), .Clr(Clr), .Q(d_ff_as_1_q));  // open: nQ
  D_FF_AS d_ff_as_2 (.Set(1'b0), .D(d_ff_as_15_q), .C(C), .Clr(Clr), .Q(d_ff_as_2_q));  // open: nQ
  D_FF_AS d_ff_as_3 (.Set(1'b0), .D(d_ff_as_1_q), .C(C), .Clr(Clr), .Q(d_ff_as_3_q));  // open: nQ
  D_FF_AS d_ff_as_4 (.Set(1'b0), .D(d_ff_as_2_q), .C(C), .Clr(Clr), .Q(d_ff_as_4_q));  // open: nQ
  D_FF_AS d_ff_as_5 (.Set(1'b0), .D(d_ff_as_3_q), .C(C), .Clr(Clr), .Q(d_ff_as_5_q));  // open: nQ
  D_FF_AS d_ff_as_6 (.Set(1'b0), .D(d_ff_as_4_q), .C(C), .Clr(Clr), .Q(d_ff_as_6_q));  // open: nQ
  D_FF_AS d_ff_as_7 (.Set(1'b0), .D(d_ff_as_5_q), .C(C), .Clr(Clr), .Q(d_ff_as_7_q));  // open: nQ
  D_FF_AS d_ff_as_8 (.Set(1'b0), .D(d_ff_as_6_q), .C(C), .Clr(Clr), .Q(d_ff_as_8_q));  // open: nQ
  D_FF_AS d_ff_as_9 (.Set(1'b0), .D(d_ff_as_7_q), .C(C), .Clr(Clr), .Q(d_ff_as_9_q));  // open: nQ
  D_FF_AS d_ff_as_10 (.Set(1'b0), .D(d_ff_as_8_q), .C(C), .Clr(Clr), .Q(d_ff_as_10_q));  // open: nQ
  D_FF_AS d_ff_as_11 (.Set(1'b0), .D(d_ff_as_9_q), .C(C), .Clr(Clr), .Q(d_ff_as_11_q));  // open: nQ
  D_FF_AS d_ff_as_12 (.Set(1'b0), .D(d_ff_as_10_q), .C(C), .Clr(Clr), .Q(d_ff_as_12_q));  // open: nQ
  D_FF_AS d_ff_as_13 (.Set(1'b0), .D(d_ff_as_11_q), .C(C), .Clr(Clr), .Q(d_ff_as_13_q));  // open: nQ
  D_FF_AS d_ff_as_14 (.Set(1'b0), .D(d_ff_as_12_q), .C(C), .Clr(Clr), .Q(d_ff_as_14_q));  // open: nQ
  D_FF_AS d_ff_as_15 (.Set(1'b0), .D(d_ff_as_13_q), .C(C), .Clr(Clr), .Q(d_ff_as_15_q));  // open: nQ
  D_FF_AS d_ff_as_16 (.Set(1'b0), .D(d_ff_as_14_q), .C(C), .Clr(Clr), .Q(Q), .nQ(nQ));
endmodule
