// Digital circuit FF4.dig as structural Verilog
module FF4 (
  input  D,
  input  C,
  input  Clr,
  output Q,
  output nQ
);

  wire d_ff_as_1_q, d_ff_as_2_q, d_ff_as_3_q;

  D_FF_AS d_ff_as_1 (.Set(1'b0), .D(D), .C(C), .Clr(Clr), .Q(d_ff_as_1_q));  // open: nQ
  D_FF_AS d_ff_as_2 (.Set(1'b0), .D(d_ff_as_1_q), .C(C), .Clr(Clr), .Q(d_ff_as_2_q));  // open: nQ
  D_FF_AS d_ff_as_3 (.Set(1'b0), .D(d_ff_as_2_q), .C(C), .Clr(Clr), .Q(d_ff_as_3_q));  // open: nQ
  D_FF_AS d_ff_as_4 (.Set(1'b0), .D(d_ff_as_3_q), .C(C), .Clr(Clr), .Q(Q), .nQ(nQ));
endmodule
