// Digital circuit HEF4557B.dig as structural Verilog
module HEF4557B (
  input  DA,
  input  DB,
  input  A_nB,
  input  nCP1,
  input  CP0,
  input  MR,
  input  L32,
  input  L16,
  input  L8,
  input  L4,
  input  L2,
  input  L1,
  input  VCC,
  input  GND,
  output Q,
  output nQ
);

  wire and_1_out, and_2_out, and_3_out, and_4_out, and_5_out, and_6_out, and_7_out, and_8_out, and_9_out,
       and_10_out, and_11_out, and_12_out, and_13_out, and_14_out, ff1_1_q, ff2_1_q, ff4_1_q, ff8_1_q,
       ff16_1_q, ff32_1_q, nor_1_out, nor_2_out, not_1_out, not_2_out, not_3_out, not_4_out, not_5_out,
       not_6_out, not_7_out, not_8_out, not_9_out, not_10_out, not_11_out, not_12_out, not_13_out,
       not_14_out, not_15_out, not_16_out, or_1_out, or_2_out, or_3_out, or_4_out, or_5_out, or_6_out;

  not not_1 (not_1_out, A_nB);
  not not_2 (not_2_out, DA);
  not not_3 (not_3_out, not_1_out);
  not not_4 (not_4_out, DB);
  nor nor_1 (nor_1_out, nCP1, ~CP0);  // NOr
  and and_1 (and_1_out, not_2_out, not_3_out);
  and and_2 (and_2_out, not_1_out, not_4_out);
  PowerSupply powersupply_1 (.VDD(VCC), .GND(GND));
  nor nor_2 (nor_2_out, and_1_out, and_2_out);
  not not_5 (not_5_out, L32);
  not not_6 (not_6_out, not_5_out);
  FF32 ff32_1 (.D(nor_2_out), .C(nor_1_out), .Clr(MR), .Q(ff32_1_q));  // open: nQ
  and and_3 (and_3_out, not_5_out, nor_2_out);
  and and_4 (and_4_out, not_6_out, ff32_1_q);
  or or_1 (or_1_out, and_3_out, and_4_out);
  FF16 ff16_1 (.D(or_1_out), .C(nor_1_out), .Clr(MR), .Q(ff16_1_q));  // open: nQ
  not not_7 (not_7_out, L16);
  not not_8 (not_8_out, not_7_out);
  and and_5 (and_5_out, not_7_out, or_1_out);
  and and_6 (and_6_out, not_8_out, ff16_1_q);
  or or_2 (or_2_out, and_5_out, and_6_out);
  not not_9 (not_9_out, L8);
  not not_10 (not_10_out, not_9_out);
  FF8 ff8_1 (.D(or_2_out), .C(nor_1_out), .Clr(MR), .Q(ff8_1_q));  // open: nQ
  and and_7 (and_7_out, not_9_out, or_2_out);
  and and_8 (and_8_out, not_10_out, ff8_1_q);
  or or_3 (or_3_out, and_7_out, and_8_out);
  not not_11 (not_11_out, L4);
  not not_12 (not_12_out, not_11_out);
  FF4 ff4_1 (.D(or_3_out), .C(nor_1_out), .Clr(MR), .Q(ff4_1_q));  // open: nQ
  and and_9 (and_9_out, not_11_out, or_3_out);
  and and_10 (and_10_out, not_12_out, ff4_1_q);
  or or_4 (or_4_out, and_9_out, and_10_out);
  not not_13 (not_13_out, L2);
  not not_14 (not_14_out, not_13_out);
  FF2 ff2_1 (.D(or_4_out), .C(nor_1_out), .Clr(MR), .Q(ff2_1_q));  // open: nQ
  and and_11 (and_11_out, not_13_out, or_4_out);
  and and_12 (and_12_out, not_14_out, ff2_1_q);
  or or_5 (or_5_out, and_11_out, and_12_out);
  FF1 ff1_1 (.D(or_5_out), .C(nor_1_out), .Clr(MR), .Q(ff1_1_q));  // open: nQ
  not not_15 (not_15_out, L1);
  not not_16 (not_16_out, not_15_out);
  and and_13 (and_13_out, not_15_out, or_5_out);
  and and_14 (and_14_out, not_16_out, ff1_1_q);
  or or_6 (or_6_out, and_13_out, and_14_out);
  FF1 ff1_2 (.D(or_6_out), .C(nor_1_out), .Clr(MR), .Q(Q), .nQ(nQ));

  // Notes on the sheet:
  //   DA: pin 7, default 1
  //   DB: pin 6
  //   A_nB: pin 9
  //   nCP1: pin 5
  //   CP0: pin 4
  //   MR: pin 3, default 1
  //   L32: pin 12
  //   L16: pin 13, default 1
  //   L8: pin 14, default 1
  //   L4: pin 15, default 1
  //   L2: pin 1, default 1
  //   L1: pin 2, default 1
  //   Q: pin 10
  //   nQ: pin 11
  //   VCC: pin 16, default 1
  //   GND: pin 8
endmodule
