// Digital circuit Imm16.dig as structural Verilog
module Imm16 (
  input  CLK,
  input  nRESET,
  input  LATCH,
  input  SnP,
  input  [15:0] Val,
  output OUT,
  output [15:0] DVal
);

  wire _74hc597_1_q7;

  _74HC597 _74hc597_1 (
    .nMR(nRESET), .SHCP(CLK), .DS(Val[15]), .STCP(LATCH), .nPL(SnP), .D7(Val[8]), .D6(Val[9]), .D5(Val[10]),
    .D4(Val[11]), .D3(Val[12]), .D2(Val[13]), .D1(Val[14]), .D0(Val[15]), .Q7(_74hc597_1_q7), .Val(DVal[15:8]));
  _74HC597 _74hc597_2 (
    .nMR(nRESET), .SHCP(CLK), .DS(_74hc597_1_q7), .STCP(LATCH), .nPL(SnP), .D7(Val[0]), .D6(Val[1]),
    .D5(Val[2]), .D4(Val[3]), .D3(Val[4]), .D2(Val[5]), .D1(Val[6]), .D0(Val[7]), .Q7(OUT), .Val(DVal[7:0]));
endmodule
