// Digital circuit Imm32.dig as structural Verilog
module Imm32 (
  input  CLK,
  input  nRESET,
  input  LATCH,
  input  SnP,
  input  [31:0] Val,
  output OUT
);

  wire _74hc597_1_q7, _74hc597_2_q7, _74hc597_3_q7;

  _74HC597 _74hc597_1 (
    .nMR(nRESET), .SHCP(CLK), .DS(Val[31]), .STCP(LATCH), .nPL(SnP), .D7(Val[24]), .D6(Val[25]),
    .D5(Val[26]), .D4(Val[27]), .D3(Val[28]), .D2(Val[29]), .D1(Val[30]), .D0(Val[31]), .Q7(_74hc597_1_q7));  // open: Val
  _74HC597 _74hc597_2 (
    .nMR(nRESET), .SHCP(CLK), .DS(_74hc597_1_q7), .STCP(LATCH), .nPL(SnP), .D7(Val[16]), .D6(Val[17]),
    .D5(Val[18]), .D4(Val[19]), .D3(Val[20]), .D2(Val[21]), .D1(Val[22]), .D0(Val[23]), .Q7(_74hc597_2_q7));  // open: Val
  _74HC597 _74hc597_3 (
    .nMR(nRESET), .SHCP(CLK), .DS(_74hc597_2_q7), .STCP(LATCH), .nPL(SnP), .D7(Val[8]), .D6(Val[9]),
    .D5(Val[10]), .D4(Val[11]), .D3(Val[12]), .D2(Val[13]), .D1(Val[14]), .D0(Val[15]), .Q7(_74hc597_3_q7));  // open: Val
  _74HC597 _74hc597_4 (
    .nMR(nRESET), .SHCP(CLK), .DS(_74hc597_3_q7), .STCP(LATCH), .nPL(SnP), .D7(Val[0]), .D6(Val[1]),
    .D5(Val[2]), .D4(Val[3]), .D3(Val[4]), .D2(Val[5]), .D1(Val[6]), .D0(Val[7]), .Q7(OUT));  // open: Val
endmodule
