// Digital circuit Imm8.dig as structural Verilog
module Imm8 (
  input  CLK,
  input  nRESET,
  input  LATCH,
  input  SnP,
  input  [7:0] Val,
  output OUT
);

  _74HC597 _74hc597_1 (
    .nMR(nRESET), .SHCP(CLK), .DS(Val[7]), .STCP(LATCH), .nPL(SnP), .D7(Val[0]), .D6(Val[1]), .D5(Val[2]),
    .D4(Val[3]), .D3(Val[4]), .D2(Val[5]), .D1(Val[6]), .D0(Val[7]), .Q7(OUT));  // open: Val
endmodule
