// Digital circuit Interrupt-Controller.dig as structural Verilog
module Interrupt_Controller (
  input  BUS_CLK,
  input  MEPC_IN,
  input  nMEPC_IN_EN,
  input  IRQ_OP_SnP,
  input  MTVEC_SnP,
  input  LASTSTEP,
  input  IRQ,
  input  OP_LATCH,
  input  RESET,
  input  nRESET,
  output MEPC_OUT,
  output IRQ_OP,
  output MTVEC_OUT,
  output IRQ_OP_FETCH,
  output [31:0] MEPC
);

  wire diodebackward_1_out, not_1_out, not_2_out;

  not not_1 (not_1_out, LASTSTEP);
  not not_2 (not_2_out, OP_LATCH);
  DiodeBackward diodebackward_1 (.in(nRESET), .out(diodebackward_1_out));
  DiodeBackward diodebackward_2 (.in(not_2_out), .out(diodebackward_1_out));
  PullUp pullup_1 (.out(diodebackward_1_out));
  D_FF_AS d_ff_as_1 (.Set(1'b0), .D(IRQ), .C(not_1_out), .Clr(~diodebackward_1_out), .Q(IRQ_OP_FETCH));  // open: nQ
  Imm32 mtvec (.CLK(BUS_CLK), .nRESET(nRESET), .LATCH(BUS_CLK), .SnP(MTVEC_SnP), .Val(32'h1000), .OUT(MTVEC_OUT));
  Imm32 u_irq_op (.CLK(BUS_CLK), .nRESET(nRESET), .LATCH(BUS_CLK), .SnP(IRQ_OP_SnP), .Val(32'h200073), .OUT(IRQ_OP));
  HEF4557B u_mepc (
    .DA(MEPC_OUT), .DB(MEPC_IN), .A_nB(nMEPC_IN_EN), .nCP1(1'b0), .CP0(BUS_CLK), .MR(RESET), .L32(1'b0),
    .L16(1'b1), .L8(1'b1), .L4(1'b1), .L2(1'b1), .L1(1'b1), .VCC(1'b1), .GND(1'b0), .Q(MEPC_OUT));  // open: nQ
  DebugShift32 debugshift32_1 (.CLK(BUS_CLK), .D(BUS_CLK), .nEN(nMEPC_IN_EN), .Val(MEPC));

  // Other names for the same wires on the sheet: PC_IN = MEPC_IN
endmodule
