// Digital circuit MEPC.dig as structural Verilog
module MEPC (
  input  BUS_CLK,
  input  PC_IN,
  input  IN_EN,
  input  CSR_IN,
  input  CSR_IN_LATCH,
  input  [11:0] CSR_ADDR,
  input  RESET,
  output OUT,
  output CSR_OUT,
  output [31:0] mepc
);

  wire and_1_out, comparator_1_eq, multiplexer_1_out, not_1_out, not_2_out, or_1_out;

  not not_1 (not_1_out, CSR_IN_LATCH);
  Comparator #(.Bits(12)) comparator_1 (.a(CSR_ADDR), .b(12'h341), .eq(comparator_1_eq));  // open: gt, lt
  Multiplexer multiplexer_1 (.sel(IN_EN), .in_0(CSR_IN), .in_1(PC_IN), .out(multiplexer_1_out));
  and and_1 (and_1_out, not_1_out, comparator_1_eq);
  or or_1 (or_1_out, IN_EN, and_1_out);
  not not_2 (not_2_out, or_1_out);
  HEF4557B u_mepc (
    .DA(multiplexer_1_out), .DB(OUT), .A_nB(or_1_out), .nCP1(1'b0), .CP0(BUS_CLK), .MR(RESET), .L32(1'b0),
    .L16(1'b1), .L8(1'b1), .L4(1'b1), .L2(1'b1), .L1(1'b1), .VCC(1'b1), .GND(1'b0), .Q(OUT));  // open: nQ
  DebugShift32 debugshift32_1 (.CLK(BUS_CLK), .D(multiplexer_1_out), .nEN(not_2_out), .Val(mepc));
  assign CSR_OUT = comparator_1_eq ? OUT : 1'bz;  // Driver driver_1

  // Other names for the same wires on the sheet: MEPC_IN_EN = IN_EN
endmodule
