// Digital circuit MIE.dig as structural Verilog
module MIE (
  input  CLK,
  input  BUS_CLK,
  input  CSR_IN,
  input  CSR_IN_LATCH,
  input  CSR_OUT_LATCH,
  input  [11:0] CSR_ADDR,
  input  nRESET,
  output CSR_OUT,
  output [31:0] mie,
  output MEI1E,
  output MEI2E,
  output MEI3E
);

  wire _74hc595_1_qh_2, _74hc595_2_qh_2, _74hc595_3_qh_2, _74hc597_1_q7, _74hc597_2_q7, _74hc597_3_q7,
       BIT_LATCH, comparator_1_eq, IN_LATCH, not_1_out, nPL;

  Comparator #(.Bits(12)) comparator_1 (.a(CSR_ADDR), .b(12'h304), .eq(comparator_1_eq));  // open: gt, lt
  not not_1 (not_1_out, comparator_1_eq);
  D_FF_AS d_ff_as_1 (.Set(~nRESET), .D(IN_LATCH), .C(CLK), .Clr(~1'b1), .Q(BIT_LATCH));  // open: nQ
  or or_1 (IN_LATCH, not_1_out, CSR_IN_LATCH);
  not not_2 (nPL, IN_LATCH);
  _74HC595 _74hc595_1 (
    .SER(CSR_IN), .SRCLK(BUS_CLK), .nSRCLR(nRESET), .RCLK(IN_LATCH), .nOE(1'b0), .VCC(1'b1), .GND(1'b0),
    .QH_2(_74hc595_1_qh_2));  // open: QH, QG, QF, QE, QD, QC, QB, QA
  _74HC595 _74hc595_2 (
    .SER(_74hc595_1_qh_2), .SRCLK(BUS_CLK), .nSRCLR(nRESET), .RCLK(IN_LATCH), .nOE(1'b0), .VCC(1'b1),
    .GND(1'b0), .QG(MEI1E), .QF(MEI2E), .QE(MEI3E), .QH_2(_74hc595_2_qh_2));  // open: QH, QD, QC, QB, QA
  _74HC595 _74hc595_3 (
    .SER(_74hc595_2_qh_2), .SRCLK(BUS_CLK), .nSRCLR(nRESET), .RCLK(IN_LATCH), .nOE(1'b0), .VCC(1'b1),
    .GND(1'b0), .QH_2(_74hc595_3_qh_2));  // open: QH, QG, QF, QE, QD, QC, QB, QA
  // _74HC595 _74hc595_4: pin names not known; wires that end beside it: _74hc595_3_qh_2, BUS_CLK, nRESET, IN_LATCH, 1'b0, 1'b1, 1'b0
  _74HC597 _74hc597_1 (
    .nMR(nRESET), .SHCP(BUS_CLK), .DS(1'b0), .STCP(CSR_OUT_LATCH), .nPL(nPL), .D7(1'b0), .D6(MEI1E),
    .D5(MEI2E), .D4(MEI3E), .D3(1'b0), .D2(1'b0), .D1(1'b0), .D0(1'b0), .Q7(_74hc597_1_q7));
  _74HC597 _74hc597_2 (
    .nMR(nRESET), .SHCP(BUS_CLK), .DS(_74hc597_1_q7), .STCP(CSR_OUT_LATCH), .nPL(nPL), .D7(1'b0), .D6(1'b0),
    .D5(1'b0), .D4(1'b0), .D3(1'b0), .D2(1'b0), .D1(1'b0), .D0(1'b0), .Q7(_74hc597_2_q7));
  _74HC597 _74hc597_3 (
    .nMR(nRESET), .SHCP(BUS_CLK), .DS(_74hc597_2_q7), .STCP(CSR_OUT_LATCH), .nPL(nPL), .D7(1'b0), .D6(1'b0),
    .D5(1'b0), .D4(1'b0), .D3(1'b0), .D2(1'b0), .D1(1'b0), .D0(1'b0), .Q7(_74hc597_3_q7));
  assign CSR_OUT = ~IN_LATCH ? _74hc597_3_q7 : 1'bz;  // DriverInvSel driverinvsel_1

  assign mie = {{12{1'b0}}, MEI3E, MEI2E, MEI1E, {17{1'b0}}};
endmodule
