// Digital circuit MIP.dig as structural Verilog
module MIP (
  input  CLK,
  input  BUS_CLK,
  input  CSR_IN,
  input  CSR_IN_LATCH,
  input  CSR_OUT_LATCH,
  input  [11:0] CSR_ADDR,
  input  nINT1,
  input  nINT2,
  input  nINT3,
  input  nRESET,
  output CSR_OUT,
  output [31:0] mip,
  output MEI1P,
  output MEI2P,
  output MEI3P
);

  wire _74hc595_1_qh_2, _74hc595_2_qh_2, _74hc595_3_qh_2, _74hc597_1_q7, _74hc597_2_q7, _74hc597_3_q7,
       BIT_LATCH, comparator_1_eq, IN_LATCH, MEI1P_IN, MEI2P_IN, MEI3P_IN, MEIP_IN, MSIP_IN, MTIP_IN,
       not_1_out, nPL;

  Comparator #(.Bits(12)) comparator_1 (.a(CSR_ADDR), .b(12'h344), .eq(comparator_1_eq));  // open: gt, lt
  not not_1 (not_1_out, comparator_1_eq);
  D_FF_AS d_ff_as_1 (.Set(~nRESET), .D(IN_LATCH), .C(CLK), .Clr(~1'b1), .Q(BIT_LATCH));  // open: nQ
  or or_1 (IN_LATCH, not_1_out, CSR_IN_LATCH);
  not not_2 (nPL, IN_LATCH);
  _74HC595 _74hc595_1 (
    .SER(CSR_IN), .SRCLK(BUS_CLK), .nSRCLR(nRESET), .RCLK(IN_LATCH), .nOE(1'b0), .VCC(1'b1), .GND(1'b0),
    .QH_2(_74hc595_1_qh_2));  // open: QH, QG, QF, QE, QD, QC, QB, QA
  _74HC595 _74hc595_2 (
    .SER(_74hc595_1_qh_2), .SRCLK(BUS_CLK), .nSRCLR(nRESET), .RCLK(IN_LATCH), .nOE(1'b0), .VCC(1'b1),
    .GND(1'b0), .QG(MEI1P_IN), .QF(MEI2P_IN), .QE(MEI3P_IN), .QH_2(_74hc595_2_qh_2));  // open: QH, QD, QC, QB, QA
  _74HC595 _74hc595_3 (
    .SER(_74hc595_2_qh_2), .SRCLK(BUS_CLK), .nSRCLR(nRESET), .RCLK(IN_LATCH), .nOE(1'b0), .VCC(1'b1),
    .GND(1'b0), .QE(MEIP_IN), .QH_2(_74hc595_3_qh_2));  // open: QH, QG, QF, QD, QC, QB, QA
  _74HC595 _74hc595_4 (
    .SER(_74hc595_3_qh_2), .SRCLK(BUS_CLK), .nSRCLR(nRESET), .RCLK(IN_LATCH), .nOE(1'b0), .VCC(1'b1),
    .GND(1'b0), .QE(MSIP_IN), .QA(MTIP_IN));  // open: QH, QG, QF, QD, QC, QB, QH_2
  D_FF_AS d_ff_as_2 (.Set(~nINT2), .D(MEI2P_IN), .C(BIT_LATCH), .Clr(~nRESET), .Q(MEI2P));  // open: nQ
  D_FF_AS d_ff_as_3 (.Set(~nINT1), .D(MEI1P_IN), .C(BIT_LATCH), .Clr(~nRESET), .Q(MEI1P));  // open: nQ
  D_FF_AS d_ff_as_4 (.Set(~nINT3), .D(MEI3P_IN), .C(BIT_LATCH), .Clr(~nRESET), .Q(MEI3P));  // open: nQ
  _74HC597 _74hc597_1 (
    .nMR(nRESET), .SHCP(BUS_CLK), .DS(1'b0), .STCP(CSR_OUT_LATCH), .nPL(nPL), .D7(1'b0), .D6(MEI1P),
    .D5(MEI2P), .D4(MEI3P), .D3(1'b0), .D2(1'b0), .D1(1'b0), .D0(1'b0), .Q7(_74hc597_1_q7));  // open: Val
  _74HC597 _74hc597_2 (
    .nMR(nRESET), .SHCP(BUS_CLK), .DS(_74hc597_1_q7), .STCP(CSR_OUT_LATCH), .nPL(nPL), .D7(1'b0), .D6(1'b0),
    .D5(1'b0), .D4(1'b0), .D3(1'b0), .D2(1'b0), .D1(1'b0), .D0(1'b0), .Q7(_74hc597_2_q7));  // open: Val
  _74HC597 _74hc597_3 (
    .nMR(nRESET), .SHCP(BUS_CLK), .DS(_74hc597_2_q7), .STCP(CSR_OUT_LATCH), .nPL(nPL), .D7(1'b0), .D6(1'b0),
    .D5(1'b0), .D4(1'b0), .D3(1'b0), .D2(1'b0), .D1(1'b0), .D0(1'b0), .Q7(_74hc597_3_q7));  // open: Val
  assign CSR_OUT = ~IN_LATCH ? _74hc597_3_q7 : 1'bz;  // DriverInvSel driverinvsel_1

  assign mip = {{12{1'b0}}, MEI3P, MEI2P, MEI1P, {17{1'b0}}};
endmodule
