// Digital circuit MSCRATCH.dig as structural Verilog
module MSCRATCH (
  input  BUS_CLK,
  input  CSR_IN,
  input  CSR_IN_LATCH,
  input  [11:0] CSR_ADDR,
  input  RESET,
  output CSR_OUT,
  output [31:0] mscratch
);

  wire and_1_out, comparator_1_eq, hef4557b_1_q, not_1_out, not_2_out;

  Comparator #(.Bits(12)) comparator_1 (.a(CSR_ADDR), .b(12'h340), .eq(comparator_1_eq));  // open: gt, lt
  not not_1 (not_1_out, CSR_IN_LATCH);
  and and_1 (and_1_out, comparator_1_eq, not_1_out);
  not not_2 (not_2_out, and_1_out);
  DebugShift32 debugshift32_1 (.CLK(BUS_CLK), .D(CSR_IN), .nEN(not_2_out), .Val(mscratch));
  HEF4557B hef4557b_1 (
    .DA(CSR_IN), .DB(hef4557b_1_q), .A_nB(and_1_out), .nCP1(1'b0), .CP0(BUS_CLK), .MR(RESET), .L32(1'b0),
    .L16(1'b1), .L8(1'b1), .L4(1'b1), .L2(1'b1), .L1(1'b1), .VCC(1'b1), .GND(1'b0), .Q(hef4557b_1_q));  // open: nQ
  assign CSR_OUT = and_1_out ? hef4557b_1_q : 1'bz;  // Driver driver_1
endmodule
