// Digital circuit MSTATUS.dig as structural Verilog
module MSTATUS (
  input  CLK,
  input  BUS_CLK,
  input  CSR_IN,
  input  CSR_IN_LATCH,
  input  CSR_OUT_LATCH,
  input  [11:0] CSR_ADDR,
  input  IRQ,
  input  MRET,
  input  IRQ_LATCH,
  input  RESET,
  input  nRESET,
  output CSR_OUT,
  output [31:0] mstatus,
  output MIE,
  output MPIE
);

  wire _74hc597_1_q7, _74hc597_2_q7, BIT_LATCH, comparator_1_eq, d_ff_as_1_q, hef4557b_1_q, IN_LATCH, MIE_IN,
       MIE_SET, MPIE_IN, MPIE_SET, multiplexer_1_out, multiplexer_2_out, not_1_out, nPL;

  Comparator #(.Bits(12)) comparator_1 (.a(CSR_ADDR), .b(12'h300), .eq(comparator_1_eq));  // open: gt, lt
  not not_1 (not_1_out, comparator_1_eq);
  or or_1 (IN_LATCH, not_1_out, CSR_IN_LATCH);
  not not_2 (nPL, IN_LATCH);
  D_FF_AS d_ff_as_1 (.Set(~nRESET), .D(IN_LATCH), .C(CLK), .Clr(~1'b1), .Q(d_ff_as_1_q));  // open: nQ
  and and_1 (BIT_LATCH, IRQ_LATCH, d_ff_as_1_q);
  HEF4557B hef4557b_1 (
    .DA(CSR_IN), .DB(1'b0), .A_nB(1'b1), .nCP1(IN_LATCH), .CP0(BUS_CLK), .MR(RESET), .L32(1'b0), .L16(1'b1),
    .L8(1'b0), .L4(1'b1), .L2(1'b1), .L1(1'b1), .VCC(1'b1), .GND(1'b0), .Q(hef4557b_1_q));  // open: nQ
  _74HC595 _74hc595_1 (
    .SER(hef4557b_1_q), .SRCLK(BUS_CLK), .nSRCLR(nRESET), .RCLK(IN_LATCH), .nOE(1'b0), .VCC(1'b1),
    .GND(1'b0), .QE(MIE_SET), .QA(MPIE_SET));  // open: QH, QG, QF, QD, QC, QB, QH_2
  Multiplexer multiplexer_1 (.sel(MRET), .in_0(1'b0), .in_1(MPIE), .out(multiplexer_1_out));
  Multiplexer multiplexer_2 (.sel(MRET), .in_0(MIE), .in_1(MPIE), .out(multiplexer_2_out));
  D_FF_AS u_MIE (.Set(~nRESET), .D(MIE_IN), .C(BIT_LATCH), .Clr(~1'b1), .Q(MIE));  // open: nQ
  D_FF_AS u_MPIE (.Set(~1'b1), .D(MPIE_IN), .C(BIT_LATCH), .Clr(~nRESET), .Q(MPIE));  // open: nQ
  Multiplexer multiplexer_3 (.sel(IRQ), .in_0(MIE_SET), .in_1(multiplexer_1_out), .out(MIE_IN));
  Multiplexer multiplexer_4 (.sel(IRQ), .in_0(MPIE_SET), .in_1(multiplexer_2_out), .out(MPIE_IN));
  _74HC597 _74hc597_1 (
    .nMR(nRESET), .SHCP(BUS_CLK), .DS(1'b0), .STCP(CSR_OUT_LATCH), .nPL(nPL), .D7(1'b0), .D6(1'b0),
    .D5(1'b0), .D4(1'b1), .D3(1'b1), .D2(1'b0), .D1(1'b0), .D0(1'b0), .Q7(_74hc597_1_q7));  // open: Val
  _74HC597 _74hc597_2 (
    .nMR(nRESET), .SHCP(BUS_CLK), .DS(_74hc597_1_q7), .STCP(CSR_OUT_LATCH), .nPL(nPL), .D7(1'b0), .D6(1'b0),
    .D5(1'b0), .D4(MIE), .D3(1'b0), .D2(1'b0), .D1(1'b0), .D0(MPIE), .Q7(_74hc597_2_q7));  // open: Val
  assign CSR_OUT = ~IN_LATCH ? _74hc597_2_q7 : 1'bz;  // DriverInvSel driverinvsel_1

  assign mstatus = {24'h18, MPIE, 3'b000, MIE, 3'b000};
endmodule
