// Digital circuit MTVEC.dig as structural Verilog
module MTVEC (
  input  BUS_CLK,
  input  MTVEC_SnP,
  input  CSR_IN,
  input  CSR_IN_LATCH,
  input  [11:0] CSR_ADDR,
  input  RESET,
  output MTVEC_OUT,
  output CSR_OUT,
  output [31:0] mtvec
);

  wire and_1_out, comparator_1_eq, nor_1_out, not_1_out, not_2_out;

  Comparator #(.Bits(12)) comparator_1 (.a(CSR_ADDR), .b(12'h305), .eq(comparator_1_eq));  // open: gt, lt
  not not_1 (not_1_out, CSR_IN_LATCH);
  and and_1 (and_1_out, comparator_1_eq, not_1_out);
  nor nor_1 (nor_1_out, not_1_out, MTVEC_SnP);
  not not_2 (not_2_out, and_1_out);
  DebugShift32 debugshift32_1 (.CLK(BUS_CLK), .D(CSR_IN), .nEN(not_2_out), .Val(mtvec));
  HEF4557B hef4557b_1 (
    .DA(CSR_IN), .DB(MTVEC_OUT), .A_nB(and_1_out), .nCP1(nor_1_out), .CP0(BUS_CLK), .MR(RESET), .L32(1'b0),
    .L16(1'b1), .L8(1'b1), .L4(1'b1), .L2(1'b1), .L1(1'b1), .VCC(1'b1), .GND(1'b0), .Q(MTVEC_OUT));  // open: nQ
  assign CSR_OUT = and_1_out ? MTVEC_OUT : 1'bz;  // Driver driver_1

  // Other names for the same wires on the sheet: SnP = MTVEC_SnP

  // Notes on the sheet:
  //   Why not tie ~CP1 to ground?
endmodule
