// Digital circuit Mem-Counter.dig as structural Verilog
module Mem_Counter (
  input  [31:0] A,
  input  nOE,
  input  nWE,
  input  [7:0] Din,
  input  CLK,
  input  nRESET,
  output [7:0] DATA,
  output [31:0] Time,
  output [31:0] Comp,
  output IRQ
);

  wire _74hc85_1_eq, _74hc85_1_gt, _74hc85_1_lt, _74hc85_2_eq, _74hc85_2_gt, _74hc85_2_lt, _74hc85_3_eq,
       _74hc85_3_gt, _74hc85_3_lt, _74hc85_4_eq, _74hc85_4_gt, _74hc85_4_lt, _74hc85_5_eq, _74hc85_5_gt,
       _74hc85_5_lt, _74hc85_6_eq, _74hc85_6_gt, _74hc85_6_lt, _74hc85_7_eq, _74hc85_7_gt, _74hc85_7_lt,
       _74161_1_p12, _74161_2_p12, _74161_3_p12, _74161_4_p12, _74161_5_p12, _74161_6_p12, _74161_7_p12,
       _74161_8_p1, and_1_out, and_2_out, and_5_out, COMP_EQ, COMP_GT, COMP_LT, comparator_1_eq,
       comparator_2_eq, d_ff_1_nq, d_ff_1_q, d_ff_as_1_q, nCLK, nLD, nOE_C0, nOE_C1, nOE_C2, nOE_C3, nOE_C4,
       nOE_C5, nOE_C6, nOE_C7, nOE_N0, nOE_N1, nOE_N2, nOE_N3, nOE_N4, nOE_N5, nOE_N6, nOE_N7, nRESET_t,
       nWE_C0, nWE_C1, nWE_C2, nWE_C3, nWE_C4, nWE_C5, nWE_C6, nWE_C7, nWE_N0, nWE_N1, nWE_N2, nWE_N3,
       nWE_N4, nWE_N5, nWE_N6, nWE_N7, OE_C0, SEL_C, SEL_N;
  wire [7:0] D_0_7, D_8_15, D_16_23, D_24_31;

  nor nor_1 (IRQ, COMP_GT, COMP_EQ);
  Reset reset_1 (.out(nRESET_t));
  not not_1 (nCLK, CLK);
  Comparator #(.Bits(8)) comparator_1 (.a(A[23:16]), .b({8{1'b0}}), .eq(comparator_1_eq));  // open: gt, lt
  Comparator #(.Bits(8)) comparator_2 (.a(A[23:16]), .b({8{1'b0}}), .eq(comparator_2_eq));  // open: gt, lt
  _74HC574 _74hc574_1 (
    .D0(Din[0]), .D1(Din[1]), .D2(Din[2]), .D3(Din[3]), .D4(Din[4]), .D5(Din[5]), .D6(Din[6]), .D7(Din[7]),
    .CP(nWE_C0), .nOE(1'b0), .Q0(D_0_7[0]), .Q1(D_0_7[1]), .Q2(D_0_7[2]), .Q3(D_0_7[3]), .Q4(D_0_7[4]),
    .Q5(D_0_7[5]), .Q6(D_0_7[6]), .Q7(D_0_7[7]));
  _74HC574 _74hc574_2 (
    .D0(Din[0]), .D1(Din[1]), .D2(Din[2]), .D3(Din[3]), .D4(Din[4]), .D5(Din[5]), .D6(Din[6]), .D7(Din[7]),
    .CP(nWE_C1), .nOE(1'b0), .Q0(D_8_15[0]), .Q1(D_8_15[1]), .Q2(D_8_15[2]), .Q3(D_8_15[3]), .Q4(D_8_15[4]),
    .Q5(D_8_15[5]), .Q6(D_8_15[6]), .Q7(D_8_15[7]));
  _74HC574 _74hc574_3 (
    .D0(Din[0]), .D1(Din[1]), .D2(Din[2]), .D3(Din[3]), .D4(Din[4]), .D5(Din[5]), .D6(Din[6]), .D7(Din[7]),
    .CP(nWE_C2), .nOE(1'b0), .Q0(D_16_23[0]), .Q1(D_16_23[1]), .Q2(D_16_23[2]), .Q3(D_16_23[3]),
    .Q4(D_16_23[4]), .Q5(D_16_23[5]), .Q6(D_16_23[6]), .Q7(D_16_23[7]));
  _74HC574 _74hc574_4 (
    .D0(Din[0]), .D1(Din[1]), .D2(Din[2]), .D3(Din[3]), .D4(Din[4]), .D5(Din[5]), .D6(Din[6]), .D7(Din[7]),
    .CP(nWE_C3), .nOE(1'b0), .Q0(D_24_31[0]), .Q1(D_24_31[1]), .Q2(D_24_31[2]), .Q3(D_24_31[3]),
    .Q4(D_24_31[4]), .Q5(D_24_31[5]), .Q6(D_24_31[6]), .Q7(D_24_31[7]));
  and and_1 (and_1_out, comparator_1_eq, A[30], ~A[31]);  // And
  and and_2 (and_2_out, comparator_2_eq, A[30], ~A[31]);  // And
  and and_3 (SEL_N, A[3], and_1_out);
  and and_4 (SEL_C, ~A[3], and_2_out);  // And
  not not_2 (OE_C0, nOE_C0);
  // _74161 _74161_1: pin names not known; wires that end beside it: nLD, nRESET_t, CLK, 1'b1, 1'b1, D_0_7[0], D_0_7[1], D_0_7[2], D_0_7[3], 1'b1, 1'b0, _74161_1_p12, Time[0], Time[1], Time[2], Time[3]
  // _74161 _74161_2: pin names not known; wires that end beside it: nLD, nRESET_t, CLK, _74161_1_p12, 1'b1, D_0_7[4], D_0_7[5], D_0_7[6], D_0_7[7], 1'b1, 1'b0, _74161_2_p12, Time[4], Time[5], Time[6], Time[7]
  // _74161 _74161_3: pin names not known; wires that end beside it: nLD, nRESET_t, CLK, _74161_2_p12, 1'b1, D_8_15[0], D_8_15[1], D_8_15[2], D_8_15[3], 1'b1, 1'b0, _74161_3_p12, Time[8], Time[9], Time[10], Time[11]
  // _74161 _74161_4: pin names not known; wires that end beside it: nLD, nRESET_t, CLK, _74161_3_p12, 1'b1, D_8_15[4], D_8_15[5], D_8_15[6], D_8_15[7], 1'b1, 1'b0, _74161_4_p12, Time[12], Time[13], Time[14], Time[15]
  // _74161 _74161_5: pin names not known; wires that end beside it: nLD, nRESET_t, CLK, _74161_4_p12, 1'b1, D_16_23[0], D_16_23[1], D_16_23[2], D_16_23[3], 1'b1, 1'b0, _74161_5_p12, Time[16], Time[17], Time[18], Time[19]
  // _74161 _74161_6: pin names not known; wires that end beside it: nLD, nRESET_t, CLK, _74161_5_p12, 1'b1, D_16_23[4], D_16_23[5], D_16_23[6], D_16_23[7], 1'b1, 1'b0, _74161_6_p12, Time[20], Time[21], Time[22], Time[23]
  // _74161 _74161_7: pin names not known; wires that end beside it: nLD, nRESET_t, CLK, _74161_6_p12, 1'b1, D_24_31[0], D_24_31[1], D_24_31[2], D_24_31[3], 1'b1, 1'b0, _74161_7_p12, Time[24], Time[25], Time[26], Time[27]
  // _74161 _74161_8: pin names not known; wires that end beside it: _74161_8_p1, nLD, nRESET_t, CLK, _74161_7_p12, 1'b1, D_24_31[4], D_24_31[5], D_24_31[6], D_24_31[7], 1'b1, 1'b0, _74161_8_p1, Time[28], Time[29], Time[30], Time[31]
  _74HC138 _74hc138_1 (
    .A0(A[0]), .A1(A[1]), .A2(A[2]), .nE1(nOE), .nE2(1'b0), .E3(SEL_C), .nY0(nOE_C0), .nY1(nOE_C1),
    .nY2(nOE_C2), .nY3(nOE_C3), .nY4(nOE_C4), .nY5(nOE_C5), .nY6(nOE_C6), .nY7(nOE_C7));
  and and_5 (and_5_out, nRESET_t, d_ff_1_nq);
  _74HC138 _74hc138_2 (
    .A0(A[0]), .A1(A[1]), .A2(A[2]), .nE1(nWE), .nE2(1'b0), .E3(SEL_C), .nY0(nWE_C0), .nY1(nWE_C1),
    .nY2(nWE_C2), .nY3(nWE_C3), .nY4(nWE_C4), .nY5(nWE_C5), .nY6(nWE_C6), .nY7(nWE_C7));
  D_FF_AS d_ff_as_1 (.Set(~1'b1), .D(1'b1), .C(nWE_C3), .Clr(~and_5_out), .Q(d_ff_as_1_q));  // open: nQ
  D_FF d_ff_1 (.D(d_ff_as_1_q), .C(CLK), .Q(d_ff_1_q), .nQ(d_ff_1_nq));
  _74HC574 _74hc574_5 (
    .D0(Time[0]), .D1(Time[1]), .D2(Time[2]), .D3(Time[3]), .D4(Time[4]), .D5(Time[5]), .D6(Time[6]),
    .D7(Time[7]), .CP(OE_C0), .nOE(nOE_C0), .Q0(Din[0]), .Q1(Din[1]), .Q2(Din[2]), .Q3(Din[3]), .Q4(Din[4]),
    .Q5(Din[5]), .Q6(Din[6]), .Q7(Din[7]));
  _74HC574 _74hc574_6 (
    .D0(Time[8]), .D1(Time[9]), .D2(Time[10]), .D3(Time[11]), .D4(Time[12]), .D5(Time[13]), .D6(Time[14]),
    .D7(Time[15]), .CP(OE_C0), .nOE(nOE_C1), .Q0(Din[0]), .Q1(Din[1]), .Q2(Din[2]), .Q3(Din[3]), .Q4(Din[4]),
    .Q5(Din[5]), .Q6(Din[6]), .Q7(Din[7]));
  _74HC574 _74hc574_7 (
    .D0(Time[16]), .D1(Time[17]), .D2(Time[18]), .D3(Time[19]), .D4(Time[20]), .D5(Time[21]), .D6(Time[22]),
    .D7(Time[23]), .CP(OE_C0), .nOE(nOE_C2), .Q0(Din[0]), .Q1(Din[1]), .Q2(Din[2]), .Q3(Din[3]), .Q4(Din[4]),
    .Q5(Din[5]), .Q6(Din[6]), .Q7(Din[7]));
  _74HC574 _74hc574_8 (
    .D0(Time[24]), .D1(Time[25]), .D2(Time[26]), .D3(Time[27]), .D4(Time[28]), .D5(Time[29]), .D6(Time[30]),
    .D7(Time[31]), .CP(OE_C0), .nOE(nOE_C3), .Q0(Din[0]), .Q1(Din[1]), .Q2(Din[2]), .Q3(Din[3]), .Q4(Din[4]),
    .Q5(Din[5]), .Q6(Din[6]), .Q7(Din[7]));
  _74HC138 _74hc138_3 (
    .A0(A[0]), .A1(A[1]), .A2(A[2]), .nE1(nOE), .nE2(1'b0), .E3(SEL_N), .nY0(nOE_N0), .nY1(nOE_N1),
    .nY2(nOE_N2), .nY3(nOE_N3), .nY4(nOE_N4), .nY5(nOE_N5), .nY6(nOE_N6), .nY7(nOE_N7));
  D_FF d_ff_2 (.D(d_ff_1_q), .C(nCLK), .nQ(nLD));  // open: Q
  _74HC138 _74hc138_4 (
    .A0(A[0]), .A1(A[1]), .A2(A[2]), .nE1(nWE), .nE2(1'b0), .E3(SEL_N), .nY0(nWE_N0), .nY1(nWE_N1),
    .nY2(nWE_N2), .nY3(nWE_N3), .nY4(nWE_N4), .nY5(nWE_N5), .nY6(nWE_N6), .nY7(nWE_N7));
  _74HC574 _74hc574_9 (
    .D0(Din[0]), .D1(Din[1]), .D2(Din[2]), .D3(Din[3]), .D4(Din[4]), .D5(Din[5]), .D6(Din[6]), .D7(Din[7]),
    .CP(nWE_N0), .nOE(1'b0), .Q0(Comp[0]), .Q1(Comp[1]), .Q2(Comp[2]), .Q3(Comp[3]), .Q4(Comp[4]),
    .Q5(Comp[5]), .Q6(Comp[6]), .Q7(Comp[7]));
  _74HC574 _74hc574_10 (
    .D0(Din[0]), .D1(Din[1]), .D2(Din[2]), .D3(Din[3]), .D4(Din[4]), .D5(Din[5]), .D6(Din[6]), .D7(Din[7]),
    .CP(nWE_N1), .nOE(1'b0), .Q0(Comp[8]), .Q1(Comp[9]), .Q2(Comp[10]), .Q3(Comp[11]), .Q4(Comp[12]),
    .Q5(Comp[13]), .Q6(Comp[14]), .Q7(Comp[15]));
  _74HC574 _74hc574_11 (
    .D0(Din[0]), .D1(Din[1]), .D2(Din[2]), .D3(Din[3]), .D4(Din[4]), .D5(Din[5]), .D6(Din[6]), .D7(Din[7]),
    .CP(nWE_N2), .nOE(1'b0), .Q0(Comp[16]), .Q1(Comp[17]), .Q2(Comp[18]), .Q3(Comp[19]), .Q4(Comp[20]),
    .Q5(Comp[21]), .Q6(Comp[22]), .Q7(Comp[23]));
  _74HC574 _74hc574_12 (
    .D0(Din[0]), .D1(Din[1]), .D2(Din[2]), .D3(Din[3]), .D4(Din[4]), .D5(Din[5]), .D6(Din[6]), .D7(Din[7]),
    .CP(nWE_N3), .nOE(1'b0), .Q0(Comp[24]), .Q1(Comp[25]), .Q2(Comp[26]), .Q3(Comp[27]), .Q4(Comp[28]),
    .Q5(Comp[29]), .Q6(Comp[30]), .Q7(Comp[31]));
  _74HC85 _74hc85_1 (
    .A0(Time[0]), .A1(Time[1]), .A2(Time[2]), .A3(Time[3]), .B0(Comp[0]), .B1(Comp[1]), .B2(Comp[2]),
    .B3(Comp[3]), .I__gt(1'b0), .I__eq(1'b1), .I__lt(1'b0), .gt(_74hc85_1_gt), .eq(_74hc85_1_eq),
    .lt(_74hc85_1_lt));
  _74HC85 _74hc85_2 (
    .A0(Time[4]), .A1(Time[5]), .A2(Time[6]), .A3(Time[7]), .B0(Comp[4]), .B1(Comp[5]), .B2(Comp[6]),
    .B3(Comp[7]), .I__gt(_74hc85_1_gt), .I__eq(_74hc85_1_eq), .I__lt(_74hc85_1_lt), .gt(_74hc85_2_gt),
    .eq(_74hc85_2_eq), .lt(_74hc85_2_lt));
  _74HC85 _74hc85_3 (
    .A0(Time[8]), .A1(Time[9]), .A2(Time[10]), .A3(Time[11]), .B0(Comp[8]), .B1(Comp[9]), .B2(Comp[10]),
    .B3(Comp[11]), .I__gt(_74hc85_2_gt), .I__eq(_74hc85_2_eq), .I__lt(_74hc85_2_lt), .gt(_74hc85_3_gt),
    .eq(_74hc85_3_eq), .lt(_74hc85_3_lt));
  _74HC85 _74hc85_4 (
    .A0(Time[12]), .A1(Time[13]), .A2(Time[14]), .A3(Time[15]), .B0(Comp[12]), .B1(Comp[13]), .B2(Comp[14]),
    .B3(Comp[15]), .I__gt(_74hc85_3_gt), .I__eq(_74hc85_3_eq), .I__lt(_74hc85_3_lt), .gt(_74hc85_4_gt),
    .eq(_74hc85_4_eq), .lt(_74hc85_4_lt));
  _74HC85 _74hc85_5 (
    .A0(Time[16]), .A1(Time[17]), .A2(Time[18]), .A3(Time[19]), .B0(Comp[16]), .B1(Comp[17]), .B2(Comp[18]),
    .B3(Comp[19]), .I__gt(_74hc85_4_gt), .I__eq(_74hc85_4_eq), .I__lt(_74hc85_4_lt), .gt(_74hc85_5_gt),
    .eq(_74hc85_5_eq), .lt(_74hc85_5_lt));
  _74HC85 _74hc85_6 (
    .A0(Time[20]), .A1(Time[21]), .A2(Time[22]), .A3(Time[23]), .B0(Comp[20]), .B1(Comp[21]), .B2(Comp[22]),
    .B3(Comp[23]), .I__gt(_74hc85_5_gt), .I__eq(_74hc85_5_eq), .I__lt(_74hc85_5_lt), .gt(_74hc85_6_gt),
    .eq(_74hc85_6_eq), .lt(_74hc85_6_lt));
  _74HC85 _74hc85_7 (
    .A0(Time[24]), .A1(Time[25]), .A2(Time[26]), .A3(Time[27]), .B0(Comp[24]), .B1(Comp[25]), .B2(Comp[26]),
    .B3(Comp[27]), .I__gt(_74hc85_6_gt), .I__eq(_74hc85_6_eq), .I__lt(_74hc85_6_lt), .gt(_74hc85_7_gt),
    .eq(_74hc85_7_eq), .lt(_74hc85_7_lt));
  _74HC85 _74hc85_8 (
    .A0(Time[28]), .A1(Time[29]), .A2(Time[30]), .A3(Time[31]), .B0(Comp[28]), .B1(Comp[29]), .B2(Comp[30]),
    .B3(Comp[31]), .I__gt(_74hc85_7_gt), .I__eq(_74hc85_7_eq), .I__lt(_74hc85_7_lt), .gt(COMP_GT),
    .eq(COMP_EQ), .lt(COMP_LT));
  assign Din = ~nOE_N0 ? Comp[7:0] : 8'bz;  // DriverInvSel driverinvsel_1
  assign Din = ~nOE_N1 ? Comp[15:8] : 8'bz;  // DriverInvSel driverinvsel_2
  assign Din = ~nOE_N2 ? Comp[23:16] : 8'bz;  // DriverInvSel driverinvsel_3
  assign Din = ~nOE_N3 ? Comp[31:24] : 8'bz;  // DriverInvSel driverinvsel_4

  assign DATA = Din;

  // Other names for the same wires on the sheet: Q_0_7[7:0] = Time[7:0]; Q_8_15[7:0] = Time[15:8];
  //   Q_16_23[7:0] = Time[23:16]; Q_24_31[7:0] = Time[31:24]; ND_0_7[7:0] = Comp[7:0]; ND_8_15[7:0] = Comp[15:8];
  //   ND_16_23[7:0] = Comp[23:16]; ND_24_31[7:0] = Comp[31:24]

  // Notes on the sheet:
  //   A: default 1073741824
  //   nOE: default 1
  //   nWE: default 1
  //   CLK: Hz: 4
  //   nRESET: default 1
endmodule
