// Digital circuit Mem-addr.dig as structural Verilog
module Mem_addr (
  input  CLK,
  input  IN,
  input  LATCH,
  input  ADDR_CLK,
  input  nPE,
  input  nRESET,
  output [31:0] ADDR
);

  wire _74hc595_1_qa, _74hc595_1_qb, _74hc595_1_qc, _74hc595_1_qd, _74hc595_1_qe, _74hc595_1_qf,
       _74hc595_1_qg, _74hc595_1_qh, _74hc595_1_qh_2, _74hc595_2_qa, _74hc595_2_qb, _74hc595_2_qc,
       _74hc595_2_qd, _74hc595_2_qe, _74hc595_2_qf, _74hc595_2_qg, _74hc595_2_qh, _74hc595_2_qh_2,
       _74hc595_3_qa, _74hc595_3_qb, _74hc595_3_qc, _74hc595_3_qd, _74hc595_3_qe, _74hc595_3_qf,
       _74hc595_3_qg, _74hc595_3_qh, _74hc595_3_qh_2, _74hc595_4_qa, _74hc595_4_qb, _74hc595_4_qc,
       _74hc595_4_qd, _74hc595_4_qe, _74hc595_4_qf, _74hc595_4_qg, _74hc595_4_qh, _74hc595_4_qh_2,
       _74161_1_p12, _74161_2_p13, _74161_3_p12, _74161_4_p12, _74161_5_p12, _74161_6_p12, _74161_7_p12;

  _74HC595 _74hc595_1 (
    .SER(_74hc595_2_qh_2), .SRCLK(CLK), .nSRCLR(nRESET), .RCLK(LATCH), .nOE(1'b0), .VCC(1'b1), .GND(1'b0),
    .QH(_74hc595_1_qh), .QG(_74hc595_1_qg), .QF(_74hc595_1_qf), .QE(_74hc595_1_qe), .QD(_74hc595_1_qd),
    .QC(_74hc595_1_qc), .QB(_74hc595_1_qb), .QA(_74hc595_1_qa), .QH_2(_74hc595_1_qh_2));
  _74HC595 _74hc595_2 (
    .SER(_74hc595_3_qh_2), .SRCLK(CLK), .nSRCLR(nRESET), .RCLK(LATCH), .nOE(1'b0), .VCC(1'b1), .GND(1'b0),
    .QH(_74hc595_2_qh), .QG(_74hc595_2_qg), .QF(_74hc595_2_qf), .QE(_74hc595_2_qe), .QD(_74hc595_2_qd),
    .QC(_74hc595_2_qc), .QB(_74hc595_2_qb), .QA(_74hc595_2_qa), .QH_2(_74hc595_2_qh_2));
  _74HC595 _74hc595_3 (
    .SER(_74hc595_4_qh_2), .SRCLK(CLK), .nSRCLR(nRESET), .RCLK(LATCH), .nOE(1'b0), .VCC(1'b1), .GND(1'b0),
    .QH(_74hc595_3_qh), .QG(_74hc595_3_qg), .QF(_74hc595_3_qf), .QE(_74hc595_3_qe), .QD(_74hc595_3_qd),
    .QC(_74hc595_3_qc), .QB(_74hc595_3_qb), .QA(_74hc595_3_qa), .QH_2(_74hc595_3_qh_2));
  _74HC595 _74hc595_4 (
    .SER(IN), .SRCLK(CLK), .nSRCLR(nRESET), .RCLK(LATCH), .nOE(1'b0), .VCC(1'b1), .GND(1'b0),
    .QH(_74hc595_4_qh), .QG(_74hc595_4_qg), .QF(_74hc595_4_qf), .QE(_74hc595_4_qe), .QD(_74hc595_4_qd),
    .QC(_74hc595_4_qc), .QB(_74hc595_4_qb), .QA(_74hc595_4_qa), .QH_2(_74hc595_4_qh_2));
  // _74161 _74161_1: pin names not known; wires that end beside it: nPE, nRESET, ADDR_CLK, 1'b1, 1'b1, _74hc595_1_qh, _74hc595_1_qg, _74hc595_1_qf, _74hc595_1_qe, 1'b1, 1'b0, _74161_1_p12, ADDR[0], ADDR[1], ADDR[2], ADDR[3]
  // _74161 _74161_2: pin names not known; wires that end beside it: _74hc595_1_qh_2, nPE, nRESET, ADDR_CLK, _74161_1_p12, 1'b1, _74hc595_1_qd, _74hc595_1_qc, _74hc595_1_qb, _74hc595_1_qa, 1'b1, 1'b0, _74161_2_p13, ADDR[4], ADDR[5], ADDR[6], ADDR[7]
  // _74161 _74161_3: pin names not known; wires that end beside it: nPE, nRESET, ADDR_CLK, _74161_2_p13, 1'b1, _74hc595_2_qh, _74hc595_2_qg, _74hc595_2_qf, _74hc595_2_qe, 1'b1, 1'b0, _74161_3_p12, ADDR[8], ADDR[9], ADDR[10], ADDR[11]
  // _74161 _74161_4: pin names not known; wires that end beside it: nPE, nRESET, ADDR_CLK, _74161_3_p12, 1'b1, _74hc595_2_qd, _74hc595_2_qc, _74hc595_2_qb, _74hc595_2_qa, 1'b1, 1'b0, _74161_4_p12, ADDR[12], ADDR[13], ADDR[14], ADDR[15]
  // _74161 _74161_5: pin names not known; wires that end beside it: nPE, nRESET, ADDR_CLK, _74161_4_p12, 1'b1, _74hc595_3_qh, _74hc595_3_qg, _74hc595_3_qf, _74hc595_3_qe, 1'b1, 1'b0, _74161_5_p12, ADDR[16], ADDR[17], ADDR[18], ADDR[19]
  // _74161 _74161_6: pin names not known; wires that end beside it: nPE, nRESET, ADDR_CLK, _74161_5_p12, 1'b1, _74hc595_3_qd, _74hc595_3_qc, _74hc595_3_qb, _74hc595_3_qa, 1'b1, 1'b0, _74161_6_p12, ADDR[20], ADDR[21], ADDR[22], ADDR[23]
  // _74161 _74161_7: pin names not known; wires that end beside it: nPE, nRESET, ADDR_CLK, _74161_6_p12, 1'b1, _74hc595_4_qh, _74hc595_4_qg, _74hc595_4_qf, _74hc595_4_qe, 1'b1, 1'b0, _74161_7_p12, ADDR[24], ADDR[25], ADDR[26], ADDR[27]
  // _74161 _74161_8: pin names not known; wires that end beside it: nPE, nRESET, ADDR_CLK, _74161_7_p12, 1'b1, _74hc595_4_qd, _74hc595_4_qc, _74hc595_4_qb, _74hc595_4_qa, 1'b1, 1'b0, ADDR[28], ADDR[29], ADDR[30], ADDR[31]
endmodule

/* Test case:
CLK IN          LATCH ADDR-CLK ~PE ~RESET   ADDR

loop (rep,32)

let addr = random(1<<32);

0   0           0     0        1   0        0

loop (i,32)
0   (addr>>i&1) 0     0        0   1        X
1   (addr>>i&1) 0     0        0   1        X
end loop
0   0           1     0        0   1        0
0   0           1     1        0   1        (addr)
0   0           0     0        1   1        X
0   0           0     1        1   1        (addr+1)
0   0           0     0        1   1        X
0   0           0     1        1   1        (addr+2)
0   0           0     0        1   1        X
0   0           0     1        1   1        (addr+3)

end loop
*/
