// Digital circuit Mem-decode.dig as structural Verilog
module Mem_decode (
  input  [31:0] ADDR,
  input  [7:0] IN,
  input  nOE,
  input  nWE,
  output [7:0] OUT
);

  wire demultiplexer_1_out_0, demultiplexer_1_out_2, not_1_out, or_1_out;
  wire [7:0] rom_1_d;

  assign OUT = ~nWE ? IN : 8'bz;  // DriverInvSel driverinvsel_1
  Demultiplexer #(.Selector_Bits(2), .Default(1)) demultiplexer_1 (
    .sel(ADDR[31:30]), .in(1'b0), .out_0(demultiplexer_1_out_0), .out_2(demultiplexer_1_out_2));  // open: out_1, out_3
  RAMSinglePortSel #(.AddrBits(8), .Bits(8)) ramsingleportsel_1 (
    .A(ADDR[7:0]), .CS(~demultiplexer_1_out_2), .WE(~nWE), .OE(~nOE), .D(OUT));
  not not_1 (not_1_out, demultiplexer_1_out_0);
  ROM #(.AddrBits(8), .Bits(8)) rom_1 (.A(ADDR[7:0]), .sel(not_1_out), .D(rom_1_d));
  or or_1 (or_1_out, demultiplexer_1_out_0, nOE);
  assign OUT = ~or_1_out ? rom_1_d : 8'bz;  // DriverInvSel driverinvsel_2

  // Notes on the sheet:
  //   contents of rom_1 (hex, n*v repeats v):
  //   0,1,2,3,4,5,6,7,8,9,a,b,c,d,e,f,10,11,12,13,14,15,16,17,18,19,1a,1b,1c,1d,1e,1f,20,
  //   21,22,23,24,25,26,27,28,29,2a,2b,2c,2d,2e,2f,30,31,32,33,34,35,36,37,38,39,3a,3b,
  //   3c,3d,3e,3f,40,41,42,43,44,45,46,47,48,49,4a,4b,4c,4d,4e,4f,50,51,52,53,54,55,56,
  //   57,58,59,5a,5b,5c,5d,5e,5f,60,61,62,63,64,65,66,67,68,69,6a,6b,6c,6d,6e,6f,70,71,
  //   72,73,74,75,76,77,78,79,7a,7b,7c,7d,7e,7f,80,81,82,83,84,85,86,87,88,89,8a,8b,8c,
  //   8d,8e,8f,90,91,92,93,94,95,96,97,98,99,9a,9b,9c,9d,9e,9f,a0,a1,a2,a3,a4,a5,a6,a7,
  //   a8,a9,aa,ab,ac,ad,ae,af,b0,b1,b2,b3,b4,b5,b6,b7,b8,b9,ba,bb,bc,bd,be,bf,c0,c1,c2,
  //   c3,c4,c5,c6,c7,c8,c9,ca,cb,cc,cd,ce,cf,d0,d1,d2,d3,d4,d5,d6,d7,d8,d9,da,db,dc,dd,
  //   de,df,e0,e1,e2,e3,e4,e5,e6,e7,e8,e9,ea,eb,ec,ed,ee,ef,f0,f1,f2,f3,f4,f5,f6,f7,f8,
  //   f9,fa,fb,fc,fd,fe,ff
endmodule

/* Test case:
ADDR       ~OE ~WE IN          OUT

0x00000000 1   1   Z           Z
0x00000000 0   1   Z           0x00
0x00000010 0   1   Z           0x10
0x000000AA 0   1   Z           0xAA
0x0000001F 0   1   Z           0x1F

0x80000000 1   0   0xDE        X
0x80000010 1   0   0xAD        X
0x80000000 0   1   Z           0xDE
0x80000010 0   1   Z           0xAD
0x4000001F 0   1   Z           Z
*/
