// Digital circuit Mem.dig as structural Verilog
module Mem (
  input  CLK,
  input  nCLK,
  input  BUS_CLK,
  input  IN,
  input  ADDR_IN,
  input  ADDR_LATCH,
  input  ADDR_CLK,
  input  nOE,
  input  nWE,
  input  nS_EXT,
  input  nRESET,
  input  [7:0] DIn,
  output OUT,
  output [7:0] DATA,
  output [15:0] DATA_ADDR,
  output CS_ROM,
  output CS_RAM,
  output CS_IO,
  output [31:0] DAddr,
  output [7:0] DVal
);

  wire d_ff_1_nq, d_ff_2_nq, d_ff_3_nq, d_ff_as_1_nq, d_ff_as_1_q, SIGN;

  D_FF_AS d_ff_as_1 (.Set(~nRESET), .D(nWE), .C(CLK), .Clr(~nWE), .Q(d_ff_as_1_q), .nQ(d_ff_as_1_nq));
  D_FF #(.Default(1)) d_ff_1 (.D(ADDR_LATCH), .C(CLK), .nQ(d_ff_1_nq));  // open: Q
  _74HC595 _74hc595_1 (
    .SER(IN), .SRCLK(BUS_CLK), .nSRCLR(nRESET), .RCLK(d_ff_as_1_nq), .nOE(d_ff_as_1_q), .VCC(1'b1),
    .GND(1'b0), .QH(DIn[0]), .QG(DIn[1]), .QF(DIn[2]), .QE(DIn[3]), .QD(DIn[4]), .QC(DIn[5]), .QB(DIn[6]),
    .QA(DIn[7]));  // open: QH_2
  Mem_addr mem_addr_1 (
    .CLK(BUS_CLK), .IN(ADDR_IN), .LATCH(ADDR_LATCH), .CLK_MEM(ADDR_CLK), .nPE(d_ff_1_nq), .nRESET(nRESET),
    .ADDR(DAddr));
  PullDown #(.Bits(8)) pulldown_1 (.out(DIn));
  Demultiplexer #(.Selector_Bits(2), .Default(1)) demultiplexer_1 (
    .sel(DAddr[31:30]), .in(1'b0), .out_0(CS_ROM), .out_2(CS_RAM), .out_3(CS_IO));  // open: out_1
  D_FF #(.Default(1)) d_ff_2 (.D(nOE), .C(CLK), .nQ(d_ff_2_nq));  // open: Q
  D_FF #(.Default(1)) d_ff_3 (.D(DIn[7]), .C(d_ff_2_nq), .nQ(d_ff_3_nq));  // open: Q
  nor nor_1 (SIGN, nS_EXT, d_ff_3_nq);
  _74HC597 _74hc597_1 (
    .nMR(nRESET), .SHCP(BUS_CLK), .DS(SIGN), .STCP(d_ff_2_nq), .nPL(nOE), .D7(DIn[0]), .D6(DIn[1]),
    .D5(DIn[2]), .D4(DIn[3]), .D3(DIn[4]), .D2(DIn[5]), .D1(DIn[6]), .D0(DIn[7]), .Q7(OUT), .Val(DVal));

  assign DATA = DIn;
  assign DATA_ADDR = DAddr[15:0];

  // Notes on the sheet:
  //   nOE: default 1
  //   nWE: default 1
  //   Can also set RCLK to 
  //   ~{WE} through an inverter
  //   if FF has no ~{Q} output
endmodule

/* Test case Address:
CLK ~CLK BUS-CLK ADDR-IN      ADDR-LATCH ADDR-CLK IN       ~OE ~WE ~{S-EXT} ~RESET DIn      DAddr    CS-ROM CS-RAM CS-IO

0   1    0       0            0          0        0        1   1   1        0      Z        X        X      X      X
0   1    0       0            0          0        0        1   1   1        0      Z        X        X      X      X

# ROM

loop (rep,32)

let rom = 0;
let ram = 1;
let io = 1;
let hi2 = 0x0;

let addr = (hi2 << 30) | random(1<<29);

# Output address
loop (i,32)
0   1    0       (addr>>i&1)  0          0        0         1  1   1        1      Z        X        X      X      X
1   0    1       (addr>>i&1)  0          0        0         1  1   1        1      Z        X        X      X      X
end loop

# Latch address
0   1    0       0            1          0        0         1  1   1        1      Z        X        X      X      X
1   0    0       0            1          0        0         1  1   1        1      Z        X        X      X      X

# Output address
0   1    0       0            0          1        0         1  1   1        1      Z        X        X      X      X
1   0    0       0            0          1        0         1  1   1        1      Z        X        X      X      X

# Check address
0   1    0       0            0          0        0         1  1   1        1      Z        (addr)   (rom)  (ram)  (io)
1   0    0       0            0          0        0         1  1   1        1      Z        (addr)   (rom)  (ram)  (io)

# Increment address
0   1    0       0            0          1        0         1  1   1        1      Z        X        X      X      X
1   0    0       0            0          1        0         1  1   1        1      Z        X        X      X      X

# Check address
0   1    0       0            0          0        0         1  1   1        1      Z        (addr+1) (rom)  (ram)  (io)
1   0    0       0            0          0        0         1  1   1        1      Z        (addr+1) (rom)  (ram)  (io)

# Increment address
0   1    0       0            0          1        0         1  1   1        1      Z        X        X      X      X
1   0    0       0            0          1        0         1  1   1        1      Z        X        X      X      X

# Check address
0   1    0       0            0          0        0         1  1   1        1      Z        (addr+2) (rom)  (ram)  (io)
1   0    0       0            0          0        0         1  1   1        1      Z        (addr+2) (rom)  (ram)  (io)

# RAM

let rom = 1;
let ram = 0;
let io = 1;
let hi2 = 0x2;

let addr = (hi2 << 30) | random(1<<29);

# Output address
loop (i,32)
0   1    0       (addr>>i&1)  0          0        0         1  1   1        1      Z        X        X      X      X
1   0    1       (addr>>i&1)  0          0        0         1  1   1        1      Z        X        X      X      X
end loop

# Latch address
0   1    0       0            1          0        0         1  1   1        1      Z        X        X      X      X
1   0    0       0            1          0        0         1  1   1        1      Z        X        X      X      X

# Output address
0   1    0       0            0          1        0         1  1   1        1      Z        X        X      X      X
1   0    0       0            0          1        0         1  1   1        1      Z        X        X      X      X

# Check address
0   1    0       0            0          0        0         1  1   1        1      Z        (addr)   (rom)  (ram)  (io)
1   0    0       0            0          0        0         1  1   1        1      Z        (addr)   (rom)  (ram)  (io)

# Increment address
0   1    0       0            0          1        0         1  1   1        1      Z        X        X      X      X
1   0    0       0            0          1        0         1  1   1        1      Z        X        X      X      X

# Check address
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*/

/* Test case Data Out:
CLK ~CLK BUS-CLK ADDR-IN      ADDR-LATCH ADDR-CLK IN       ~OE ~WE ~{S-EXT} ~RESET DIn      OUT        DVal

0   1    0       0            0          0        0        1   1   1        0      Z        X          X

loop (rep,32)

# Not sign extended

let d = random(1<<8);

# Output address
0   1    0       0            0          0        0         1  1   1        1      Z        X          X
1   0    1       0            0          0        0         1  1   1        1      Z        X          X

# Latch address
0   1    0       0            1          0        0         1  1   1        1      Z        X          X
1   0    0       0            1          0        0         1  1   1        1      Z        X          X

# Output address
0   1    0       0            0          1        0         1  1   1        1      Z        X          X
1   0    0       0            0          1        0         1  1   1        1      Z        X          X

# Output data
0   1    0       0            0          1        0         0  1   1        1      (d)      X          X
1   0    0       0            0          1        0         0  1   1        1      (d)      X          X

# Shift out data
loop (i,8)
0   1    0       0            0          1        0         1  1   1        1      Z        ((d>>i)&1) X
1   0    1       0            0          1        0         1  1   1        1      Z        X          X
end loop

# Check sign bit

0   1    0       0            0          1        0         1  1   1        1      Z        0          X
1   0    0       0            0          1        0         1  1   1        1      Z        X          X

# Sign extended positive

let s = 0;
let d = (s << 7) | random(1<<7);

# Output address
0   1    0       0            0          0        0         1  1   0        1      Z        X          X
1   0    1       0            0          0        0         1  1   0        1      Z        X          X

# Latch address
0   1    0       0            1          0        0         1  1   0        1      Z        X          X
1   0    0       0            1          0        0         1  1   0        1      Z        X          X

# Output address
0   1    0       0            0          1        0         1  1   0        1      Z        X          X
1   0    0       0            0          1        0         1  1   0        1      Z        X          X

# Output data
0   1    0       0            0          1        0         0  1   0        1      (d)      X          X
1   0    0       0            0          1        0         0  1   0        1      (d)      X          X

# Shift out data
loop (i,8)
0   1    0       0            0          1        0         1  1   0        1      Z        ((d>>i)&1) X
1   0    1       0            0          1        0         1  1   0        1      Z        X          X
end loop

# Check sign bit

0   1    0       0            0          1        0         1  1   0        1      Z        (s)        X
1   0    0       0            0          1        0         1  1   0        1      Z        X          X


# Sign extended negative

let s = 1;
let d = (s << 7) | random(1<<7);

# Output address
0   1    0       0            0          0        0         1  1   0        1      Z        X          X
1   0    1       0            0          0        0         1  1   0        1      Z        X          X

# Latch address
0   1    0       0            1          0        0         1  1   0        1      Z        X          X
1   0    0       0            1          0        0         1  1   0        1      Z        X          X

# Output address
0   1    0       0            0          1        0         1  1   0        1      Z        X          X
1   0    0       0            0          1        0         1  1   0        1      Z        X          X

# Output data
0   1    0       0            0          1        0         0  1   0        1      (d)      X          X
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*/

/* Test case Data In:
CLK ~CLK BUS-CLK ADDR-IN      ADDR-LATCH ADDR-CLK IN         ~OE ~WE ~{S-EXT} ~RESET DIn      DATA

0   1    0       0            0          0        0          1   1   1        0      Z        X

loop (rep,32)

let d = random(1<<8);

# Clock in data

loop (i,8)
0   1    0       0            0          0        ((d>>i)&1) 1   1   1        1      Z        X
1   0    1       0            0          0        ((d>>i)&1) 1   1   1        1      Z        X
end loop

# Output data
0   1    0       0            0          0        0          1   0   1        1      Z        X
1   0    0       0            0          0        0          1   0   1        1      Z        (d)

# Check data

0   1    0       0            0          0        0          1   1   1        1      Z        (d)
1   0    0       0            0          0        0          1   1   1        1      Z        X

end loop
*/
