// Digital circuit OpCode.dig as structural Verilog
module OpCode (
  input  BUS_CLK,
  input  IN,
  input  OP_LATCH,
  input  OP_LATCH_LSB,
  input  IMM_LATCH,
  input  IMM_SnP,
  input  [2:0] IMM_MUX,
  input  nRESET,
  input  OP_FETCH,
  input  OP_IN_MUX,
  output IMM,
  output [4:0] RSA,
  output [4:0] RSB,
  output [4:0] RD,
  output [4:0] OPCODE,
  output [2:0] FUNC3,
  output ALU_SA,
  output nS_EXT,
  output SYS,
  output [1:0] TRAP2,
  output CNT_2,
  output [31:0] Instr,
  output [15:0] Instr16,
  output Compr,
  output MRET
);

  wire _74595_1_p1, _74595_2_p1, _74595_3_p1, and_3_out, BUS_CLK_GATED, C0, C1, d_ff_as_1_nq, d_ff_as_1_q,
       d_ff_as_2_nq, ImmB, ImmCSR, ImmI, ImmJ, ImmS, ImmU, nCOMPRESSED, not_1_out, or_1_out, or_2_out,
       or_3_out;

  assign {Instr[31:16], Instr16} = 1'b0 ? 32'h300073 : 32'bz;  // Driver driver_1
  PullUp pullup_1 ();  // open: out
  PullUp pullup_2 ();  // open: out
  PullUp pullup_3 ();  // open: out
  PullDown pulldown_1 ();  // open: out
  PullDown pulldown_2 ();  // open: out
  PullUp pullup_4 ();  // open: out
  PullUp pullup_5 ();  // open: out
  PullDown pulldown_3 ();  // open: out
  PullDown pulldown_4 ();  // open: out
  PullDown pulldown_5 ();  // open: out
  PullDown pulldown_6 ();  // open: out
  PullDown pulldown_7 ();  // open: out
  PullDown pulldown_8 ();  // open: out
  PullDown pulldown_9 ();  // open: out
  PullDown pulldown_10 ();  // open: out
  PullDown pulldown_11 ();  // open: out
  PullDown pulldown_12 ();  // open: out
  PullDown pulldown_13 ();  // open: out
  PullDown pulldown_14 ();  // open: out
  PullDown pulldown_15 ();  // open: out
  PullDown pulldown_16 ();  // open: out
  PullDown pulldown_17 ();  // open: out
  PullDown pulldown_18 ();  // open: out
  PullDown pulldown_19 ();  // open: out
  PullDown pulldown_20 ();  // open: out
  PullDown pulldown_21 ();  // open: out
  PullDown pulldown_22 ();  // open: out
  PullDown pulldown_23 ();  // open: out
  PullDown pulldown_24 ();  // open: out
  PullDown pulldown_25 ();  // open: out
  PullDown pulldown_26 ();  // open: out
  PullDown pulldown_27 ();  // open: out
  PullUp pullup_6 (.out(Instr16[0]));
  PullUp pullup_7 (.out(Instr16[1]));
  PullDown pulldown_28 (.out(Instr16[2]));
  PullDown pulldown_29 (.out(Instr16[3]));
  PullUp pullup_8 (.out(Instr16[4]));
  PullUp pullup_9 (.out(Instr16[5]));
  PullUp pullup_10 (.out(Instr16[6]));
  PullDown pulldown_30 (.out(Instr16[7]));
  PullDown pulldown_31 (.out(Instr16[8]));
  PullDown pulldown_32 (.out(Instr16[9]));
  PullDown pulldown_33 (.out(Instr16[10]));
  PullDown pulldown_34 (.out(Instr16[11]));
  PullDown pulldown_35 (.out(Instr16[12]));
  PullDown pulldown_36 (.out(Instr16[13]));
  PullDown pulldown_37 (.out(Instr16[14]));
  PullDown pulldown_38 (.out(Instr16[15]));
  PullDown pulldown_39 (.out(Instr[16]));
  PullDown pulldown_40 (.out(Instr[17]));
  PullDown pulldown_41 (.out(Instr[18]));
  PullDown pulldown_42 (.out(Instr[19]));
  PullUp pullup_11 (.out(Instr[20]));
  PullUp pullup_12 (.out(Instr[21]));
  PullDown pulldown_43 (.out(Instr[22]));
  PullDown pulldown_44 (.out(Instr[23]));
  PullDown pulldown_45 (.out(Instr[24]));
  PullDown pulldown_46 (.out(Instr[25]));
  PullDown pulldown_47 (.out(Instr[26]));
  PullDown pulldown_48 (.out(Instr[27]));
  PullDown pulldown_49 (.out(Instr[28]));
  PullDown pulldown_50 (.out(Instr[29]));
  PullDown pulldown_51 (.out(Instr[30]));
  PullDown pulldown_52 (.out(Instr[31]));
  or or_1 (or_1_out, Compr, OP_IN_MUX);
  and and_1 (BUS_CLK_GATED, BUS_CLK, OP_FETCH);
  D_FF_AS d_ff_as_1 (.Set(~1'b1), .D(1'b1), .C(OP_LATCH), .Clr(~nRESET), .Q(d_ff_as_1_q), .nQ(d_ff_as_1_nq));
  // _74595 _74595_1: pin names not known; wires that end beside it: _74595_1_p1, BUS_CLK_GATED, 1'b1, OP_LATCH, OP_IN_MUX, 1'b1, 1'b0, d_ff_as_1_nq, Instr16[0], Instr16[1], Instr16[2], Instr16[3], Instr16[4], Instr16[5], Instr16[6], Instr16[7]
  // _74595 _74595_2: pin names not known; wires that end beside it: _74595_2_p1, BUS_CLK_GATED, 1'b1, OP_LATCH, OP_IN_MUX, 1'b1, 1'b0, Instr16[8], Instr16[9], Instr16[10], Instr16[11], Instr16[12], Instr16[13], Instr16[14], Instr16[15], _74595_1_p1
  // _74595 _74595_3: pin names not known; wires that end beside it: _74595_3_p1, BUS_CLK_GATED, 1'b1, OP_LATCH, or_1_out, 1'b1, 1'b0, Instr[16], Instr[17], Instr[18], Instr[19], Instr[20], Instr[21], Instr[22], Instr[23], _74595_2_p1
  // _74595 _74595_4: pin names not known; wires that end beside it: IN, BUS_CLK_GATED, 1'b1, OP_LATCH, or_1_out, 1'b1, 1'b0, Instr[24], Instr[25], Instr[26], Instr[27], Instr[28], Instr[29], Instr[30], Instr[31], _74595_3_p1
  D_FF_AS d_ff_as_2 (.Set(~1'b1), .D(d_ff_as_1_q), .C(OP_LATCH), .Clr(~nRESET), .nQ(d_ff_as_2_nq));  // open: Q
  and and_2 (nCOMPRESSED, Instr16[0], Instr16[1]);
  nand nand_1 (Compr, Instr16[0], Instr16[1]);
  // _74595 _74595_5: pin names not known; wires that end beside it: _74595_3_p1, BUS_CLK_GATED, 1'b1, OP_LATCH_LSB, 1'b0, 1'b1, 1'b0, C0, C1
  EEPROM #(.AddrBits(16), .Bits(16)) eeprom_1 (
    .A(Instr16), .CS(~1'b0), .WE(~1'b1), .OE(~nCOMPRESSED), .D(Instr[31:16]));
  EEPROM #(.AddrBits(16), .Bits(16)) eeprom_2 (
    .A(Instr16), .CS(~1'b0), .WE(~1'b1), .OE(~1'b0), .D({Instr[15], FUNC3, Instr[11:0]}));
  Imm24 u_ImmJ (
    .CLK(BUS_CLK), .nRESET(1'b1), .LATCH(IMM_LATCH), .SnP(IMM_SnP),
    .Val({{4{Instr[31]}}, Instr[19:15], FUNC3, Instr[20], Instr[30:21], 1'b0}), .OUT(ImmJ));
  Imm8 u_ImmCSR (
    .CLK(BUS_CLK), .nRESET(1'b1), .LATCH(IMM_LATCH), .SnP(IMM_SnP), .Val({3'b000, Instr[19:15]}), .OUT(ImmCSR));
  Imm16 u_ImmI (
    .CLK(BUS_CLK), .nRESET(1'b1), .LATCH(IMM_LATCH), .SnP(IMM_SnP), .Val({{5{Instr[31]}}, Instr[30:20]}),
    .OUT(ImmI));  // open: DVal
  Imm16 u_ImmS (
    .CLK(BUS_CLK), .nRESET(1'b1), .LATCH(IMM_LATCH), .SnP(IMM_SnP),
    .Val({{5{Instr[31]}}, Instr[30:25], Instr[11:7]}), .OUT(ImmS));  // open: DVal
  Imm16 u_ImmB (
    .CLK(BUS_CLK), .nRESET(1'b1), .LATCH(IMM_LATCH), .SnP(IMM_SnP),
    .Val({{4{Instr[31]}}, Instr[7], Instr[30:25], Instr[11:8], 1'b0}), .OUT(ImmB));  // open: DVal
  Imm32 u_ImmU (
    .CLK(BUS_CLK), .nRESET(1'b1), .LATCH(IMM_LATCH), .SnP(IMM_SnP), .Val({Instr[31:15], FUNC3, {12{1'b0}}}),
    .OUT(ImmU));
  nand nand_2 (CNT_2, C1, C0);
  Multiplexer #(.Selector_Bits(3)) multiplexer_1 (
    .sel(IMM_MUX), .in_0(ImmCSR), .in_1(ImmI), .in_2(ImmS), .in_3(ImmB), .in_4(ImmU), .in_5(ImmJ),
    .in_6(1'b0), .in_7(1'b1), .out(IMM));
  not not_1 (not_1_out, Instr[20]);
  and and_3 (and_3_out, Instr[28], Instr[20]);
  and and_4 (MRET, Instr[21], not_1_out);
  or or_2 (or_2_out, Instr[30], Instr[25], and_3_out);
  or or_3 (or_3_out, Instr[25], MRET);
  Multiplexer multiplexer_2 (.sel(Instr[2]), .in_0(or_2_out), .in_1(Instr[28]), .out(ALU_SA));
  Multiplexer multiplexer_3 (.sel(Instr[2]), .in_0(or_3_out), .in_1(Instr[27]), .out(SYS));

  assign Instr[14:12] = FUNC3;
  assign nS_EXT = FUNC3[2];
  assign OPCODE = Instr[6:2];
  assign RD = Instr[11:7];
  assign RSA = Instr[19:15];
  assign RSB = Instr[24:20];
  assign TRAP2 = Instr[21:20];

  // Other names for the same wires on the sheet: B16 = Instr[16]; B17 = Instr[17]; B18 = Instr[18]; B19 = Instr[19];
  //   B20 = Instr[20]; B21 = Instr[21]; B22 = Instr[22]; B23 = Instr[23]; B24 = Instr[24]; B25 = Instr[25];
  //   B26 = Instr[26]; B27 = Instr[27]; B28 = Instr[28]; B29 = Instr[29]; B30 = Instr[30]; B31 = Instr[31];
  //   B0 = Instr[0]; B1 = Instr[1]; B2 = Instr[2]; B3 = Instr[3]; B4 = Instr[4]; B5 = Instr[5]; B6 = Instr[6];
  //   B7 = Instr[7]; B8 = Instr[8]; B9 = Instr[9]; B10 = Instr[10]; B11 = Instr[11]; B12 = FUNC3[0]; B13 = FUNC3[1];
  //   B14 = FUNC3[2]; B15 = Instr[15]; A0 = Instr16[0]; A1 = Instr16[1]; A2 = Instr16[2]; A3 = Instr16[3];
  //   A4 = Instr16[4]; A5 = Instr16[5]; A6 = Instr16[6]; A7 = Instr16[7]; A8 = Instr16[8]; A9 = Instr16[9];
  //   A10 = Instr16[10]; A11 = Instr16[11]; A12 = Instr16[12]; A13 = Instr16[13]; A14 = Instr16[14];
  //   A15 = Instr16[15]; COMPRESSED = Compr; IMM_SP = IMM_SnP; nOE = OP_IN_MUX

  // Notes on the sheet:
  //   First instruction:
  //   00000067     jalr x0, 0(x0)
  //   contents of eeprom_1 (hex, n*v repeats v):
  //   ffff,0,0,ffff,1,10,10,ffff,1,20,20,ffff,1,30,30,ffff,1,40,40,ffff
  //   ,1,50,50,ffff,1,60,60,ffff,1,70,70,ffff,81,80,80,ffff,81,90,90
  //   ,ffff,81,a0,a0,ffff,81,b0,b0,ffff,81,c0,c0,ffff,81,d0,d0,ffff
  //   ,81,e0,e0,ffff,81,f0,f0,ffff,41,100,100,ffff,41,110,110,ffff,41
  //   ,120,120,ffff,41,130,130,ffff,41,140,140,ffff,41,150,150,ffff
  //   ,41,160,160,ffff,41,170,170,ffff,c1,180,180,ffff,c1,190,190,ffff
  //   ,c1,1a0,1a0,ffff,c1,1b0,1b0,ffff,c1,1c0,1c0,ffff,c1,1d0,1d0,ffff
  //   ,c1,1e0,1e0,ffff,c1,1f0,1f0,ffff,401,0,0,ffff,401,10,10,ffff,401
  //   ,20,20,ffff,401,30,30,ffff,401,40,40,ffff,401,50,50,ffff,401,60,60
  //   ,ffff,401,70,70,ffff,481,80,80,ffff,481,90,90,ffff,481,a0,a0,ffff
  //   ,481,b0,b0,ffff,481,c0,c0,ffff,481,d0,d0,ffff,481,e0,e0,ffff,481
  //   ,f0,f0,ffff,441,100,100,ffff,441,110,110,ffff,441,120,120,ffff
  //   ,441,130,130,ffff,441,140,140,ffff,441,150,150,ffff,441,160,160
  //   ,ffff,441,170,170,ffff,4c1,180,180,ffff,4c1,190,190,ffff,4c1,1a0,1a0
  //   ,ffff,4c1,1b0,1b0,ffff,4c1,1c0,1c0,ffff,4c1,1d0,1d0,ffff,4c1,1e0,1e0
  //   ,ffff,4c1,1f0,1f0,ffff,801,1,1,ffff,801,11,11,ffff,801,21,21,ffff
  //   ,801,31,31,ffff,801,41,41,ffff,801,51,51,ffff,801,61,61,ffff,801
  //   ,71,71,ffff,881,81,81,ffff,881,91,91,ffff,881,a1,a1,ffff,881,b1,b1
  //   ,ffff,881,c1,c1,ffff,881,d1,d1,ffff,881,e1,e1,ffff,881,f1,f1,ffff
  //   ,841,101,101,ffff,841,111,111,ffff,841,121,121,ffff,841,131,131
  //   ,ffff,841,141,141,ffff,841,151,151,ffff,841,161,161,ffff,841,171,171
  //   ,ffff,8c1,181,181,ffff,8c1,191,191,ffff,8c1,1a1,1a1,ffff,8c1,1b1,1b1
  //   ,ffff,8c1,1c1,1c1,ffff,8c1,1d1,1d1,ffff,8c1,1e1,1e1,ffff,8c1,1f1,1f1
  //   ,ffff,c01,1,1,ffff,c01,11,11,ffff,c01,21,21,ffff,c01,31,31,ffff
  //   ,c01,41,41,ffff,c01,51,51,ffff,c01,61,61,ffff,c01,71,71,ffff,c81
  //   ,81,81,ffff,c81,91,91,ffff,c81,a1,a1,ffff,c81,b1,b1,ffff,c81,c1,c1
  //   ,ffff,c81,d1,d1,ffff,c81,e1,e1,ffff,c81,f1,f1,ffff,c41,101,101
  //   ,ffff,c41,111,111,ffff,c41,121,121,ffff,c41,131,131,ffff,c41,141,141
  //   ,ffff,c41,151,151,ffff,c41,161,161,ffff,c41,171,171,ffff,cc1,181,181
  //   ,ffff,cc1,191,191,ffff,cc1,1a1,1a1,ffff,cc1,1b1,1b1,ffff,cc1,1c1,1c1
  //   ,ffff,cc1,1d1,1d1,ffff,cc1,1e1,1e1,ffff,cc1,1f1,1f1,ffff,1001
  //   ,2,2,ffff,1001,12,12,ffff,1001,22,22,ffff,1001,32,32,ffff,1001
  //   ,42,42,ffff,1001,52,52,ffff,1001,62,62,ffff,1001,72,72,ffff,1081
  //   ,82,82,ffff,1081,92,92,ffff,1081,a2,a2,ffff,1081,b2,b2,ffff,1081
  //   ,c2,c2,ffff,1081,d2,d2,ffff,1081,e2,e2,ffff,1081,f2,f2,ffff,1041
  //   ,102,102,ffff,1041,112,112,ffff,1041,122,122,ffff,1041,132,132
  //   ,ffff,1041,142,142,ffff,1041,152,152,ffff,1041,162,162,ffff,1041
  //   ,172,172,ffff,10c1,182,182,ffff,10c1,192,192,ffff,10c1,1a2,1a2
  //   ,ffff,10c1,1b2,1b2,ffff,10c1,1c2,1c2,ffff,10c1,1d2,1d2,ffff,10c1
  //   ,1e2,1e2,ffff,10c1,1f2,1f2,ffff,1401,2,2,ffff,1401,12,12,ffff
  //   ,1401,22,22,ffff,1401,32,32,ffff,1401,42,42,ffff,1401,52,52,ffff
  //   ,1401,62,62,ffff,1401,72,72,ffff,1481,82,82,ffff,1481,92,92,ffff
  //   ,1481,a2,a2,ffff,1481,b2,b2,ffff,1481,c2,c2,ffff,1481,d2,d2,ffff
  //   ,1481,e2,e2,ffff,1481,f2,f2,ffff,1441,102,102,ffff,1441,112,112
  //   ,ffff,1441,122,122,ffff,1441,132,132,ffff,1441,142,142,ffff,1441
  //   ,152,152,ffff,1441,162,162,ffff,1441,172,172,ffff,14c1,182,182
  //   ,ffff,14c1,192,192,ffff,14c1,1a2,1a2,ffff,14c1,1b2,1b2,ffff,14c1
  //   ,1c2,1c2,ffff,14c1,1d2,1d2,ffff,14c1,1e2,1e2,ffff,14c1,1f2,1f2
  //   ,ffff,1801,3,3,ffff,1801,13,13,ffff,1801,23,23,ffff,1801,33,33
  //   ,ffff,1801,43,43,ffff,1801,53,53,ffff,1801,63,63,ffff,1801,73,73
  //   ,ffff,1881,83,83,ffff,1881,93,93,ffff,1881,a3,a3,ffff,1881,b3,b3
  //   ,ffff,1881,c3,c3,ffff,1881,d3,d3,ffff,1881,e3,e3,ffff,1881,f3,f3
  //   ,ffff,1841,103,103,ffff,1841,113,113,ffff,1841,123,123,ffff,1841
  //   ,133,133,ffff,1841,143,143,ffff,1841,153,153,ffff,1841,163,163
  //   ,ffff,1841,173,173,ffff,18c1,183,183,ffff,18c1,193,193,ffff,18c1
  //   ,1a3,1a3,ffff,18c1,1b3,1b3,ffff,18c1,1c3,1c3,ffff,18c1,1d3,1d3
  //   ,ffff,18c1,1e3,1e3,ffff,18c1,1f3,1f3,ffff,1c01,3,3,ffff,1c01,13,13
  //   ,ffff,1c01,23,23,ffff,1c01,33,33,ffff,1c01,43,43,ffff,1c01,53,53
  //   ,ffff,1c01,63,63,ffff,1c01,73,73,ffff,1c81,83,83,ffff,1c81,93,93
  //   ,ffff,1c81,a3,a3,ffff,1c81,b3,b3,ffff,1c81,c3,c3,ffff,1c81,d3,d3
  //   ,ffff,1c81,e3,e3,ffff,1c81,f3,f3,ffff,1c41,103,103,ffff,1c41,113,113
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  //   contents of eeprom_2 (hex, n*v repeats v):
  //   ffff,13,1013,3,493,13,1013,7,513,13,1013,b,593,13,1013,f,613,13
  //   ,1013,13,693,13,1013,17,713,13,1013,1b,793,13,1013,1f,413,13,1013
  //   ,23,493,13,1013,27,513,13,1013,2b,593,13,1013,2f,613,13,1013,33
  //   ,693,13,1013,37,713,13,1013,3b,793,13,1013,3f,413,13,1013,43,493
  //   ,13,1013,47,513,13,1013,4b,593,13,1013,4f,613,13,1013,53,693,13
  //   ,1013,57,713,13,1013,5b,793,13,1013,5f,413,13,1013,63,493,13,1013
  //   ,67,513,13,1013,6b,593,13,1013,6f,613,13,1013,73,693,13,1013,77
  //   ,713,13,1013,7b,793,13,1013,7f,413,8093,9093,83,493,8093,9093
  //   ,87,513,8093,9093,8b,593,8093,9093,8f,613,8093,9093,93,693,8093
  //   ,9093,97,713,8093,9093,9b,793,8093,9093,9f,413,8093,9093,a3,493
  //   ,8093,9093,a7,513,8093,9093,ab,593,8093,9093,af,613,8093,9093
  //   ,b3,693,8093,9093,b7,713,8093,9093,bb,793,8093,9093,bf,413,8093
  //   ,9093,c3,493,8093,9093,c7,513,8093,9093,cb,593,8093,9093,cf,613
  //   ,8093,9093,d3,693,8093,9093,d7,713,8093,9093,db,793,8093,9093
  //   ,df,413,8093,9093,e3,493,8093,9093,e7,513,8093,9093,eb,593,8093
  //   ,9093,ef,613,8093,9093,f3,693,8093,9093,f7,713,8093,9093,fb,793
  //   ,8093,9093,ff,413,113,1113,103,493,113,1113,107,513,113,1113,10b
  //   ,593,113,1113,10f,613,113,1113,113,693,113,1113,117,713,113,1113
  //   ,11b,793,113,1113,11f,413,113,1113,123,493,113,1113,127,513,113
  //   ,1113,12b,593,113,1113,12f,613,113,1113,133,693,113,1113,137,713
  //   ,113,1113,13b,793,113,1113,13f,413,113,1113,143,493,113,1113,147
  //   ,513,113,1113,14b,593,113,1113,14f,613,113,1113,153,693,113,1113
  //   ,157,713,113,1113,15b,793,113,1113,15f,413,113,1113,163,493,113
  //   ,1113,167,513,113,1113,16b,593,113,1113,16f,613,113,1113,173,693
  //   ,113,1113,177,713,113,1113,17b,793,113,1113,17f,413,8193,9193
  //   ,183,493,8193,9193,187,513,8193,9193,18b,593,8193,9193,18f,613
  //   ,8193,9193,193,693,8193,9193,197,713,8193,9193,19b,793,8193,9193
  //   ,19f,413,8193,9193,1a3,493,8193,9193,1a7,513,8193,9193,1ab,593
  //   ,8193,9193,1af,613,8193,9193,1b3,693,8193,9193,1b7,713,8193,9193
  //   ,1bb,793,8193,9193,1bf,413,8193,9193,1c3,493,8193,9193,1c7,513
  //   ,8193,9193,1cb,593,8193,9193,1cf,613,8193,9193,1d3,693,8193,9193
  //   ,1d7,713,8193,9193,1db,793,8193,9193,1df,413,8193,9193,1e3,493
  //   ,8193,9193,1e7,513,8193,9193,1eb,593,8193,9193,1ef,613,8193,9193
  //   ,1f3,693,8193,9193,1f7,713,8193,9193,1fb,793,8193,9193,1ff,413
  //   ,213,1213,203,493,213,1213,207,513,213,1213,20b,593,213,1213,20f
  //   ,613,213,1213,213,693,213,1213,217,713,213,1213,21b,793,213,1213
  //   ,21f,413,213,1213,223,493,213,1213,227,513,213,1213,22b,593,213
  //   ,1213,22f,613,213,1213,233,693,213,1213,237,713,213,1213,23b,793
  //   ,213,1213,23f,413,213,1213,243,493,213,1213,247,513,213,1213,24b
  //   ,593,213,1213,24f,613,213,1213,253,693,213,1213,257,713,213,1213
  //   ,25b,793,213,1213,25f,413,213,1213,263,493,213,1213,267,513,213
  //   ,1213,26b,593,213,1213,26f,613,213,1213,273,693,213,1213,277,713
  //   ,213,1213,27b,793,213,1213,27f,413,8293,9293,283,493,8293,9293
  //   ,287,513,8293,9293,28b,593,8293,9293,28f,613,8293,9293,293,693
  //   ,8293,9293,297,713,8293,9293,29b,793,8293,9293,29f,413,8293,9293
  //   ,2a3,493,8293,9293,2a7,513,8293,9293,2ab,593,8293,9293,2af,613
  //   ,8293,9293,2b3,693,8293,9293,2b7,713,8293,9293,2bb,793,8293,9293
  //   ,2bf,413,8293,9293,2c3,493,8293,9293,2c7,513,8293,9293,2cb,593
  //   ,8293,9293,2cf,613,8293,9293,2d3,693,8293,9293,2d7,713,8293,9293
  //   ,2db,793,8293,9293,2df,413,8293,9293,2e3,493,8293,9293,2e7,513
  //   ,8293,9293,2eb,593,8293,9293,2ef,613,8293,9293,2f3,693,8293,9293
  //   ,2f7,713,8293,9293,2fb,793,8293,9293,2ff,413,313,1313,303,493
  //   ,313,1313,307,513,313,1313,30b,593,313,1313,30f,613,313,1313,313
  //   ,693,313,1313,317,713,313,1313,31b,793,313,1313,31f,413,313,1313
  //   ,323,493,313,1313,327,513,313,1313,32b,593,313,1313,32f,613,313
  //   ,1313,333,693,313,1313,337,713,313,1313,33b,793,313,1313,33f,413
  //   ,313,1313,343,493,313,1313,347,513,313,1313,34b,593,313,1313,34f
  //   ,613,313,1313,353,693,313,1313,357,713,313,1313,35b,793,313,1313
  //   ,35f,413,313,1313,363,493,313,1313,367,513,313,1313,36b,593,313
  //   ,1313,36f,613,313,1313,373,693,313,1313,377,713,313,1313,37b,793
  //   ,313,1313,37f,413,8393,9393,383,493,8393,9393,387,513,8393,9393
  //   ,38b,593,8393,9393,38f,613,8393,9393,393,693,8393,9393,397,713
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endmodule

/* Test case ADD/ADDI/BEQ:
BUS-CLK IN       ~RESET OP-LATCH IMM-LATCH IMM-S~P     ImmI        ImmB        RSA   RSB   RD   FUNC3   OPCODE  ALU-SA

loop (rep, 32)

# Bin immediate

let imm = random(1<<12);
let s = (imm >> 11) & 1;
let op = 0b00100;
let func3 = random(8);
let rd = random(16);
let rs1 = random(16);

let instr = ((imm << 20) | (rs1 << 15) | (func3 << 12) | (rd << 7) | (op << 2) | 0b11) & 0xFFFFFFFF;

0   0            0      0        0         1           X           X           X     X     X     X       X       X
0   0            0      1        0         1           X           X           X     X     X     X       X       X
0   0            0      0        0         1           X           X           X     X     X     X       X       X

loop (i,32)
0   (instr>>i&1) 1      0        0         0           X           X           X     X     X     X       X       X
1   (instr>>i&1) 1      0        0         0           X           X           X     X     X     X       X       X
end loop

0   0            1      1        0         0           X           X           X     X     X     X       X       X
1   0            1      1        0         0           X           X           X     X     X     X       X       X

0   0            1      0        1         0           X           X           X     X     X     X       X       X
1   0            1      0        1         0           X           X           (rs1) X     (rd)  (func3) (op)    X

loop (i,12)
0   0            1      0        0         1           (imm>>i&1)  X           X     X     X     X       X       X
1   0            1      0        0         1           X           X           X     X     X     X       X       X
end loop

loop (i,20)
0   0            1      0        0         1           (s)         X           X     X     X     X       X       X
1   0            1      0        0         1           X           X           X     X     X     X       X       X
end loop


# SUB

let s = (imm >> 11) & 1;
let op = 0b01100;
let func3 = 000;
let rd = random(16);
let rs1 = random(16);
let rs2 = random(16);

let instr = ((0b0100000 << 25) | (rs2 << 20) | (rs1 << 15) | (func3 << 12) | (rd << 7) | (op << 2) | 0b11) & 0xFFFFFFFF;

0   0            0      0        0         1           X           X           X     X     X     X       X       X

loop (i,32)
0   (instr>>i&1) 1      0        0         0           X           X           X     X     X     X       X       X
1   (instr>>i&1) 1      0        0         0           X           X           X     X     X     X       X       X
end loop

0   0            1      1        0         0           X           X           X     X     X     X       X       X
1   0            1      1        0         0           X           X           X     X     X     X       X       X

0   0            1      0        1         0           X           X           X     X     X     X       X       X
1   0            1      0        1         0           X           X           (rs1) (rs2) (rd)  (func3) (op)    1

# BEQ

let imm12 = random(1<<1);
let imm10to5 = random(1<<6);
let imm4to1 = random(1<<4);
let imm11 = random(1<<1);
let rs1 = random(1<<4);
let rs2 = random(1<<4);
let funct3 = 0;
let op = 0b11000;

let imm = (imm12 << 12) | (imm11 << 11) | (imm10to5 << 5) | (imm4to1 << 1);
let s = (imm >> 12) & 1;

let instr = (imm12 << 31) | (imm10to5 << 25) | (rs2 << 20) | (rs1 << 15) | (funct3 << 12) | (imm4to1 << 8) | (imm11 << 7) | (op << 2) | (0b11);

0   0            0      0        0         1           X           X           X     X     X     X       X       X

loop (i,32)
0   (instr>>i&1) 1      0        0         0           X           X           X     X     X     X       X       X
1   (instr>>i&1) 1      0        0         0           X           X           X     X     X     X       X       X
end loop

0   0            1      1        0         0           X           X           X     X     X     X       X       X
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*/
