// Digital circuit Register-bank-8.dig as structural Verilog
module Register_bank_8 (
  input  BUS_CLK,
  input  IN,
  input  [2:0] SA,
  input  [2:0] SB,
  input  [2:0] SD,
  input  nIN_EN,
  input  nA_EN,
  input  nB_EN,
  input  RESET,
  output A,
  output B
);

  wire demultiplexer_1_out_0, demultiplexer_1_out_1, demultiplexer_1_out_2, demultiplexer_1_out_3,
       demultiplexer_1_out_4, demultiplexer_1_out_5, demultiplexer_1_out_6, demultiplexer_1_out_7,
       multiplexer_1_out, multiplexer_2_out, register_1_out, register_2_out, register_3_out, register_4_out,
       register_5_out, register_6_out, register_7_out, register_8_out;

  Demultiplexer #(.Selector_Bits(3), .Default(1)) demultiplexer_1 (
    .sel(SD), .in(nIN_EN), .out_0(demultiplexer_1_out_0), .out_1(demultiplexer_1_out_1),
    .out_2(demultiplexer_1_out_2), .out_3(demultiplexer_1_out_3), .out_4(demultiplexer_1_out_4),
    .out_5(demultiplexer_1_out_5), .out_6(demultiplexer_1_out_6), .out_7(demultiplexer_1_out_7));
  Register register_1 (
    .CLK(BUS_CLK), .IN(IN), .nEN_IN(demultiplexer_1_out_0), .nEN(1'b0), .RESET(RESET), .OUT(register_1_out));
  Register register_2 (
    .CLK(BUS_CLK), .IN(IN), .nEN_IN(demultiplexer_1_out_1), .nEN(1'b0), .RESET(RESET), .OUT(register_2_out));
  Register register_3 (
    .CLK(BUS_CLK), .IN(IN), .nEN_IN(demultiplexer_1_out_2), .nEN(1'b0), .RESET(RESET), .OUT(register_3_out));
  Register register_4 (
    .CLK(BUS_CLK), .IN(IN), .nEN_IN(demultiplexer_1_out_3), .nEN(1'b0), .RESET(RESET), .OUT(register_4_out));
  Register register_5 (
    .CLK(BUS_CLK), .IN(IN), .nEN_IN(demultiplexer_1_out_4), .nEN(1'b0), .RESET(RESET), .OUT(register_5_out));
  Register register_6 (
    .CLK(BUS_CLK), .IN(IN), .nEN_IN(demultiplexer_1_out_5), .nEN(1'b0), .RESET(RESET), .OUT(register_6_out));
  Register register_7 (
    .CLK(BUS_CLK), .IN(IN), .nEN_IN(demultiplexer_1_out_6), .nEN(1'b0), .RESET(RESET), .OUT(register_7_out));
  Register register_8 (
    .CLK(BUS_CLK), .IN(IN), .nEN_IN(demultiplexer_1_out_7), .nEN(1'b0), .RESET(RESET), .OUT(register_8_out));
  Multiplexer #(.Selector_Bits(3)) multiplexer_1 (
    .sel(SA), .in_0(register_1_out), .in_1(register_2_out), .in_2(register_3_out), .in_3(register_4_out),
    .in_4(register_5_out), .in_5(register_6_out), .in_6(register_7_out), .in_7(register_8_out),
    .out(multiplexer_1_out));
  Multiplexer #(.Selector_Bits(3)) multiplexer_2 (
    .sel(SB), .in_0(register_1_out), .in_1(register_2_out), .in_2(register_3_out), .in_3(register_4_out),
    .in_4(register_5_out), .in_5(register_6_out), .in_6(register_7_out), .in_7(register_8_out),
    .out(multiplexer_2_out));
  assign A = ~nA_EN ? multiplexer_1_out : 1'bz;  // DriverInvSel driverinvsel_1
  assign B = ~nB_EN ? multiplexer_2_out : 1'bz;  // DriverInvSel driverinvsel_2
endmodule

/* Test case:
BUS-CLK RESET IN       ~{IN-EN} ~{A-EN} ~{B-EN} SA   SB   SD   A B

loop (rep,32)

let RA = 1 + random(6);
let RB = 1 + RA + random(7-RA);

let A = random(1<<32);
let B = random(1<<32);

0       1     0        1        1       1       0    0    0    X        X
0       0     0        1        1       1       0    0    0    X        X

loop (i,32)
0       0     (A>>i&1) 0        1       1       0    0    (RA) X        X
1       0     (A>>i&1) 0        1       1       0    0    (RA) X        X
end loop

loop (i,32)
0       0     (B>>i&1) 0        0       1       (RA) 0    (RB)  (A>>i&1) X
1       0     (B>>i&1) 0        0       1       (RA) 0    (RB)  X        X
end loop


loop (i,32)
0       0     0        1        0       0       (RA) (RB) 0     (A>>i&1) (B>>i&1)
1       0     0        1        0       0       (RA) (RB) 0     X        X
end loop

end loop
*/
