// Digital circuit Register-bank.dig as structural Verilog
module Register_bank (
  input  BUS_CLK,
  input  IN,
  input  nIN_EN,
  input  [4:0] SA,
  input  [4:0] SB,
  input  [4:0] SD,
  input  RESET,
  output A,
  output B
);

  wire demultiplexer_1_out_0, demultiplexer_1_out_1, demultiplexer_1_out_2, demultiplexer_1_out_3,
       demultiplexer_2_out_0, demultiplexer_2_out_1, demultiplexer_2_out_2, demultiplexer_2_out_3,
       demultiplexer_3_out_0, demultiplexer_3_out_1, demultiplexer_3_out_2, demultiplexer_3_out_3;

  Demultiplexer #(.Selector_Bits(2), .Default(1)) demultiplexer_1 (
    .sel(SD[4:3]), .in(nIN_EN), .out_0(demultiplexer_1_out_0), .out_1(demultiplexer_1_out_1),
    .out_2(demultiplexer_1_out_2), .out_3(demultiplexer_1_out_3));
  Demultiplexer #(.Selector_Bits(2), .Default(1)) demultiplexer_2 (
    .sel(SA[4:3]), .in(1'b0), .out_0(demultiplexer_2_out_0), .out_1(demultiplexer_2_out_1),
    .out_2(demultiplexer_2_out_2), .out_3(demultiplexer_2_out_3));
  Demultiplexer #(.Selector_Bits(2), .Default(1)) demultiplexer_3 (
    .sel(SB[4:3]), .in(1'b0), .out_0(demultiplexer_3_out_0), .out_1(demultiplexer_3_out_1),
    .out_2(demultiplexer_3_out_2), .out_3(demultiplexer_3_out_3));
  Register_bank_0 register_bank_0_1 (
    .BUS_CLK(BUS_CLK), .IN(IN), .SA(SA[2:0]), .SB(SB[2:0]), .SD(SD[2:0]), .nIN_EN(demultiplexer_1_out_0),
    .nA_EN(demultiplexer_2_out_0), .nB_EN(demultiplexer_3_out_0), .RESET(RESET), .A(A), .B(B));
  Register_bank_8 register_bank_8_1 (
    .BUS_CLK(BUS_CLK), .IN(IN), .SA(SA[2:0]), .SB(SB[2:0]), .SD(SD[2:0]), .nIN_EN(demultiplexer_1_out_1),
    .nA_EN(demultiplexer_2_out_1), .nB_EN(demultiplexer_3_out_1), .RESET(RESET), .A(A), .B(B));
  Register_bank_8 register_bank_8_2 (
    .BUS_CLK(BUS_CLK), .IN(IN), .SA(SA[2:0]), .SB(SB[2:0]), .SD(SD[2:0]), .nIN_EN(demultiplexer_1_out_2),
    .nA_EN(demultiplexer_2_out_2), .nB_EN(demultiplexer_3_out_2), .RESET(RESET), .A(A), .B(B));
  Register_bank_8 register_bank_8_3 (
    .BUS_CLK(BUS_CLK), .IN(IN), .SA(SA[2:0]), .SB(SB[2:0]), .SD(SD[2:0]), .nIN_EN(demultiplexer_1_out_3),
    .nA_EN(demultiplexer_2_out_3), .nB_EN(demultiplexer_3_out_3), .RESET(RESET), .A(A), .B(B));

  // Other names for the same wires on the sheet: SA012[2:0] = SA[2:0]; SA34[1:0] = SA[4:3]; SB012[2:0] = SB[2:0];
  //   SB34[1:0] = SB[4:3]; SD012[2:0] = SD[2:0]; SD34[1:0] = SD[4:3]
endmodule

/* Test case:
BUS-CLK IN        ~{IN-EN} RESET SA   SB   SD     A        B

loop (rep,32)

let R1 = 1 + random(14);
let R2 = R1 + 1 + random(15 - R1);

let A = random(1<<32);
let B = random(1<<32);


0   0         1        1     0    0    0      0        0

loop (i,32)
0   (A>>i&1)  0        0     0    0    (R1)   0        0
1   (A>>i&1)  0        0     0    0    (R1)   X        X
end loop

loop (i,32)
0   (B>>i&1)  0        0     (R1) 0    (R2)   (A>>i&1) 0
1   (B>>i&1)  0        0     (R1) 0    (R2)   X        X
end loop

loop (i,32)
0   0         1        0     (R1) (R2) 0      (A>>i&1) (B>>i&1)
1   0         1        0     (R1) (R2) 0      X        X
end loop

end loop
*/
