// Digital circuit Register-view.dig as structural Verilog
module Register_view (
  input  BUS_CLK,
  input  nREG_IN_EN,
  input  REG_IN,
  input  [4:0] RSD,
  output [31:0] x1_ra,
  output [31:0] x2_sp,
  output [31:0] x3_gp,
  output [31:0] x4_tp,
  output [31:0] x5_t0,
  output [31:0] x6_t1,
  output [31:0] x7_t2,
  output [31:0] x8_s0_fp,
  output [31:0] x9_s1,
  output [31:0] x10_a0,
  output [31:0] x11_a1,
  output [31:0] x12_a2,
  output [31:0] x13_a3,
  output [31:0] x14_a4,
  output [31:0] x15_a5
);

  wire demultiplexer_1_out_1, demultiplexer_1_out_2, demultiplexer_1_out_3, demultiplexer_1_out_4,
       demultiplexer_1_out_5, demultiplexer_1_out_6, demultiplexer_1_out_7, demultiplexer_1_out_8,
       demultiplexer_1_out_9, demultiplexer_1_out_10, demultiplexer_1_out_11, demultiplexer_1_out_12,
       demultiplexer_1_out_13, demultiplexer_1_out_14, demultiplexer_1_out_15;

  Demultiplexer #(.Selector_Bits(4), .Default(1)) demultiplexer_1 (
    .sel(RSD[3:0]), .in(nREG_IN_EN), .out_1(demultiplexer_1_out_1), .out_2(demultiplexer_1_out_2),
    .out_3(demultiplexer_1_out_3), .out_4(demultiplexer_1_out_4), .out_5(demultiplexer_1_out_5),
    .out_6(demultiplexer_1_out_6), .out_7(demultiplexer_1_out_7), .out_8(demultiplexer_1_out_8),
    .out_9(demultiplexer_1_out_9), .out_10(demultiplexer_1_out_10), .out_11(demultiplexer_1_out_11),
    .out_12(demultiplexer_1_out_12), .out_13(demultiplexer_1_out_13), .out_14(demultiplexer_1_out_14),
    .out_15(demultiplexer_1_out_15));  // open: out_0
  DebugShift32 debugshift32_1 (.CLK(BUS_CLK), .D(REG_IN), .nEN(demultiplexer_1_out_1), .Val(x1_ra));
  DebugShift32 debugshift32_2 (.CLK(BUS_CLK), .D(REG_IN), .nEN(demultiplexer_1_out_2), .Val(x2_sp));
  DebugShift32 debugshift32_3 (.CLK(BUS_CLK), .D(REG_IN), .nEN(demultiplexer_1_out_3), .Val(x3_gp));
  DebugShift32 debugshift32_4 (.CLK(BUS_CLK), .D(REG_IN), .nEN(demultiplexer_1_out_4), .Val(x4_tp));
  DebugShift32 debugshift32_5 (.CLK(BUS_CLK), .D(REG_IN), .nEN(demultiplexer_1_out_5), .Val(x5_t0));
  DebugShift32 debugshift32_6 (.CLK(BUS_CLK), .D(REG_IN), .nEN(demultiplexer_1_out_6), .Val(x6_t1));
  DebugShift32 debugshift32_7 (.CLK(BUS_CLK), .D(REG_IN), .nEN(demultiplexer_1_out_7), .Val(x7_t2));
  DebugShift32 debugshift32_8 (.CLK(BUS_CLK), .D(REG_IN), .nEN(demultiplexer_1_out_8), .Val(x8_s0_fp));
  DebugShift32 debugshift32_9 (.CLK(BUS_CLK), .D(REG_IN), .nEN(demultiplexer_1_out_9), .Val(x9_s1));
  DebugShift32 debugshift32_10 (.CLK(BUS_CLK), .D(REG_IN), .nEN(demultiplexer_1_out_10), .Val(x10_a0));
  DebugShift32 debugshift32_11 (.CLK(BUS_CLK), .D(REG_IN), .nEN(demultiplexer_1_out_11), .Val(x11_a1));
  DebugShift32 debugshift32_12 (.CLK(BUS_CLK), .D(REG_IN), .nEN(demultiplexer_1_out_12), .Val(x12_a2));
  DebugShift32 debugshift32_13 (.CLK(BUS_CLK), .D(REG_IN), .nEN(demultiplexer_1_out_13), .Val(x13_a3));
  DebugShift32 debugshift32_14 (.CLK(BUS_CLK), .D(REG_IN), .nEN(demultiplexer_1_out_14), .Val(x14_a4));
  DebugShift32 debugshift32_15 (.CLK(BUS_CLK), .D(REG_IN), .nEN(demultiplexer_1_out_15), .Val(x15_a5));
endmodule
