// Digital circuit Register.dig as structural Verilog
module Register (
  input  CLK,
  input  IN,
  input  nEN_IN,
  input  nEN,
  input  RESET,
  output OUT
);

  HEF4557B hef4557b_1 (
    .DA(OUT), .DB(IN), .A_nB(nEN_IN), .nCP1(nEN), .CP0(CLK), .MR(RESET), .L32(1'b0), .L16(1'b1), .L8(1'b1),
    .L4(1'b1), .L2(1'b1), .L1(1'b1), .VCC(1'b1), .GND(1'b0), .Q(OUT));  // open: nQ

  // Notes on the sheet:
  //   CLK: Hz: 4
endmodule
