// Digital circuit SD-SPI.dig as structural Verilog
module SD_SPI (
  input  [15:0] A,
  input  nCS,
  input  nWE,
  input  nOE,
  input  SPI_CLK_RAW,
  input  MISO,
  output [7:0] D,
  output nWAIT,
  output SCLK,
  output MOSI,
  output CS
);

  wire _74597_1_p15, _74597_2_p14, and_2_out, comparator_1_eq, d_ff_as_3_q, demultiplexer_1_out_2,
       demultiplexer_1_out_3, demultiplexer_2_out_2, demultiplexer_2_out_3, DUMMY_READ, nDATA_OE,
       nDATA_OE_IN, nDATA_WE, nDATA_WE_IN, nDUMMY_READ, nor_1_out, nor_2_out, not_1_out, not_2_out, nSD_E,
       nSPI_CLK, nSPI_EN, nSTATUS_OE, nSTATUS_WE, nTRIG, or_4_out, reset_1_out, reset_2_out, reset_3_out,
       reset_4_out, reset_5_out, reset_6_out, reset_7_out, SPI_EN, switchdt_1_p3;
  wire [3:0] counter_1_out, counter_2_out;

  Comparator #(.Bits(8)) comparator_1 (.a(A[15:8]), .b(8'h4), .eq(comparator_1_eq));  // open: gt, lt
  Demultiplexer #(.Selector_Bits(2), .Default(1)) demultiplexer_1 (
    .sel({nSD_E, A[2]}), .in(nOE), .out_0(nDATA_OE_IN), .out_1(nSTATUS_OE), .out_2(demultiplexer_1_out_2),
    .out_3(demultiplexer_1_out_3));
  Demultiplexer #(.Selector_Bits(2), .Default(1)) demultiplexer_2 (
    .sel({nSD_E, A[2]}), .in(nWE), .out_0(nDATA_WE_IN), .out_1(nSTATUS_WE), .out_2(demultiplexer_2_out_2),
    .out_3(demultiplexer_2_out_3));
  D_FF_AS d_ff_as_1 (.Set(1'b0), .D(D[1]), .C(nSTATUS_WE), .Clr(reset_1_out), .Q(DUMMY_READ), .nQ(nDUMMY_READ));
  Reset #(.invertOutput("false")) reset_1 (.out(reset_1_out));
  assign D = ~nSTATUS_OE ? {3'b000, SPI_EN, 2'b00, DUMMY_READ, CS} : 8'bz;  // DriverInvSel driverinvsel_1
  not not_1 (not_1_out, comparator_1_eq);
  or or_1 (nSD_E, not_1_out, nCS);
  Reset #(.invertOutput("false")) reset_2 (.out(reset_2_out));
  D_FF_AS d_ff_as_2 (.Set(reset_2_out), .D(D[0]), .C(nSTATUS_WE), .Clr(1'b0), .Q(CS));  // open: nQ
  nor nor_1 (nor_1_out, nDATA_OE_IN, nSPI_EN);
  assign nWAIT = nor_1_out ? 1'b0 : 1'bz;  // Driver driver_1
  nor nor_2 (nor_2_out, nDATA_WE_IN, nSPI_EN);
  assign nWAIT = nor_2_out ? 1'b0 : 1'bz;  // Driver driver_2
  or or_2 (nDATA_WE, nDATA_WE_IN, SPI_EN);
  or or_3 (nDATA_OE, nDATA_OE_IN, SPI_EN);
  D_FF_AS d_ff_as_3 (.Set(1'b0), .D(1'b1), .C(SPI_EN), .Clr(~nDATA_WE), .Q(d_ff_as_3_q));  // open: nQ
  // SwitchDT switchdt_1: pin names not known; wires that end beside it: MOSI, MISO, switchdt_1_p3
  Reset reset_3 (.out(reset_3_out));
  or or_4 (or_4_out, nDUMMY_READ, nDATA_OE);
  Reset reset_4 (.out(reset_4_out));
  not not_2 (not_2_out, nDATA_OE);
  // _74597 _74597_1: pin names not known; wires that end beside it: reset_4_out, nSPI_CLK, 1'b1, nDATA_WE, d_ff_as_3_q, D[7], D[6], D[5], D[4], D[3], D[2], D[1], D[0], MOSI, _74597_1_p15
  // _74595 _74595_1: pin names not known; wires that end beside it: switchdt_1_p3, SCLK, reset_3_out, not_2_out, nDATA_OE, 1'b1, 1'b0, D[7], D[6], D[5], D[4], D[3], D[2], D[1], D[0]
  and and_1 (nTRIG, nDATA_WE, or_4_out);
  // Probe on _74597_1_p15
  and and_2 (and_2_out, nTRIG, _74597_2_p14);
  Reset reset_5 (.out(reset_5_out));
  D_FF_AS d_ff_as_4 (.Set(~1'b1), .D(and_2_out), .C(SPI_CLK_RAW), .Clr(~reset_5_out), .Q(SPI_EN), .nQ(nSPI_EN));
  or or_5 (nSPI_CLK, SPI_CLK_RAW, nSPI_EN);
  // Probe on counter_1_out
  Counter #(.Bits(4)) counter_1 (.en(1'b1), .C(nSPI_CLK), .clr(reset_6_out), .out(counter_1_out));  // open: ovf
  Reset #(.invertOutput("false")) reset_6 (.out(reset_6_out));
  not not_3 (SCLK, nSPI_CLK);
  // Probe on counter_2_out
  Counter #(.Bits(4)) counter_2 (.en(1'b1), .C(SCLK), .clr(reset_6_out), .out(counter_2_out));  // open: ovf
  Reset reset_7 (.out(reset_7_out));
  // _74597 _74597_2: pin names not known; wires that end beside it: reset_7_out, SCLK, 1'b0, reset_7_out, nTRIG, 1'b1, 1'b1, 1'b1, 1'b1, 1'b1, 1'b1, 1'b1, 1'b1, _74597_2_p14

  // Other names for the same wires on the sheet: DATA[7:0] = D; SPI_CLK = SCLK

  // Notes on the sheet:
  //   A: default 1
  //   nCS: default 1
  //   nWE: default 1
  //   nOE: default 1
  //   MISO: default 170
endmodule
