// Digital circuit Step-Counter.dig as structural Verilog
module Step_Counter (
  input  nCLK,
  input  nRESET,
  input  EN,
  input  nOPDONE,
  output [5:0] COUNT
);

  wire _74161_1_pin15;

  _74161 _74161_1 (
    .pin1(nRESET), .pin2(nCLK), .pin3(1'b0), .pin4(1'b0), .pin5(1'b0), .pin6(1'b0), .pin7(EN), .pin8(1'b0),
    .pin9(nOPDONE), .pin10(1'b1), .pin11(COUNT[3]), .pin12(COUNT[2]), .pin13(COUNT[1]), .pin14(COUNT[0]),
    .pin15(_74161_1_pin15), .pin16(1'b1));
  _74161 _74161_2 (
    .pin1(nRESET), .pin2(nCLK), .pin3(1'b0), .pin4(1'b0), .pin5(1'b0), .pin6(1'b0), .pin7(EN), .pin8(1'b0),
    .pin9(nOPDONE), .pin10(_74161_1_pin15), .pin13(COUNT[5]), .pin14(COUNT[4]), .pin16(1'b1));  // open: pin11, pin12, pin15
endmodule
