// Digital circuit Terminal.dig as structural Verilog
module Terminal (
  input  [15:0] A,
  input  nCS,
  input  nWE,
  input  nOE,
  output [7:0] D,
  output nINT
);

  wire and_1_out, and_2_out, comparator_1_eq, comparator_2_eq, keyboard_1_av, or_1_out;
  wire [15:8] keyboard_1_d;

  Comparator #(.Bits(16)) comparator_1 (.a(A), .b({16{1'b0}}), .eq(comparator_1_eq));  // open: gt, lt
  Comparator #(.Bits(16)) comparator_2 (.a(A), .b(16'h1), .eq(comparator_2_eq));  // open: gt, lt
  and and_1 (and_1_out, ~nCS, comparator_1_eq);  // And
  and and_2 (and_2_out, ~nCS, comparator_2_eq);  // And
  or or_1 (or_1_out, ~and_2_out, nOE);  // Or
  Terminal terminal_1 (.D(D), .C(nWE), .en(and_1_out));
  DriverInvSel #(.Bits(16)) driverinvsel_1 (.in({16{1'b0}}), .en(or_1_out));  // open: out
  Keyboard keyboard_1 (.C(nOE), .en(and_2_out), .D({keyboard_1_d, D}), .av(keyboard_1_av));
  not not_1 (nINT, keyboard_1_av);

  // Other names for the same wires on the sheet: DATA[7:0] = D; ADDRESS[15:0] = A
endmodule
