// Digital circuit test.dig as structural Verilog
module test (
  input  A,
  input  B,
  output Out
);

  or or_1 (Out, A, B);
endmodule

/* Test case Testcase 00:
A B Out
0 0 0
*/

/* Test case Testcase 11:
A B Out
1 1 1
*/
